// Logisim project MANIAC.circ as structural Verilog: 21 circuits, main circuit Full Adder
module REG (
  input  I15,
  input  I14,
  input  I13,
  input  I12,
  input  I11,
  input  I10,
  input  I9,
  input  I8,
  input  I7,
  input  I6,
  input  I5,
  input  I4,
  input  I3,
  input  I2,
  input  I1,
  input  I0,
  input  LM,
  input  CLR,
  input  CLK,
  input  nRegEn,
  output O15,
  output O14,
  output O13,
  output O12,
  output O11,
  output O10,
  output O9,
  output O8,
  output O7,
  output O6,
  output O5,
  output O4,
  output O3,
  output O2,
  output O1,
  output O0
);

  wire and_1_out, and_2_out, and_3_out, and_4_out, and_5_out, and_6_out, and_7_out, and_8_out, and_9_out,
       and_10_out, and_11_out, and_12_out, and_13_out, and_14_out, and_15_out, and_16_out, and_17_out,
       and_18_out, and_19_out, and_20_out, and_21_out, and_22_out, and_23_out, and_24_out, and_25_out,
       and_26_out, and_27_out, and_28_out, and_29_out, and_30_out, and_31_out, and_32_out, d_ff_1_q,
       d_ff_2_q, d_ff_3_q, d_ff_4_q, d_ff_5_q, d_ff_6_q, d_ff_7_q, d_ff_8_q, d_ff_9_q, d_ff_10_q, d_ff_11_q,
       d_ff_12_q, d_ff_13_q, d_ff_14_q, d_ff_15_q, d_ff_16_q, not_1_out, or_1_out, or_2_out, or_3_out,
       or_4_out, or_5_out, or_6_out, or_7_out, or_8_out, or_9_out, or_10_out, or_11_out, or_12_out,
       or_13_out, or_14_out, or_15_out, or_16_out;

  and and_1 (and_1_out, I15, LM);
  or or_1 (or_1_out, and_1_out, and_2_out);
  and and_2 (and_2_out, not_1_out, d_ff_1_q);
  D_Flip_Flop #(.trigger("falling")) d_ff_1 (
    .clk(CLK), .D(or_1_out), .Q(d_ff_1_q), .reset(CLR));  // open: Qn, preset, en
  Transistor transistor_1 (.in(d_ff_1_q), .out(O15), .gate(nRegEn));
  and and_3 (and_3_out, I14, LM);
  or or_2 (or_2_out, and_3_out, and_4_out);
  and and_4 (and_4_out, not_1_out, d_ff_2_q);
  D_Flip_Flop #(.trigger("falling")) d_ff_2 (
    .clk(CLK), .D(or_2_out), .Q(d_ff_2_q), .reset(CLR));  // open: Qn, preset, en
  Transistor transistor_2 (.in(d_ff_2_q), .out(O14), .gate(nRegEn));
  and and_5 (and_5_out, I13, LM);
  or or_3 (or_3_out, and_5_out, and_6_out);
  and and_6 (and_6_out, not_1_out, d_ff_3_q);
  D_Flip_Flop #(.trigger("falling")) d_ff_3 (
    .clk(CLK), .D(or_3_out), .Q(d_ff_3_q), .reset(CLR));  // open: Qn, preset, en
  Transistor transistor_3 (.in(d_ff_3_q), .out(O13), .gate(nRegEn));
  and and_7 (and_7_out, I12, LM);
  or or_4 (or_4_out, and_7_out, and_8_out);
  and and_8 (and_8_out, not_1_out, d_ff_4_q);
  D_Flip_Flop #(.trigger("falling")) d_ff_4 (
    .clk(CLK), .D(or_4_out), .Q(d_ff_4_q), .reset(CLR));  // open: Qn, preset, en
  Transistor transistor_4 (.in(d_ff_4_q), .out(O12), .gate(nRegEn));
  and and_9 (and_9_out, I11, LM);
  or or_5 (or_5_out, and_9_out, and_10_out);
  and and_10 (and_10_out, not_1_out, d_ff_5_q);
  D_Flip_Flop #(.trigger("falling")) d_ff_5 (
    .clk(CLK), .D(or_5_out), .Q(d_ff_5_q), .reset(CLR));  // open: Qn, preset, en
  and and_11 (and_11_out, I10, LM);
  Transistor transistor_5 (.in(d_ff_5_q), .out(O11), .gate(nRegEn));
  or or_6 (or_6_out, and_11_out, and_12_out);
  and and_12 (and_12_out, not_1_out, d_ff_6_q);
  D_Flip_Flop #(.trigger("falling")) d_ff_6 (
    .clk(CLK), .D(or_6_out), .Q(d_ff_6_q), .reset(CLR));  // open: Qn, preset, en
  Transistor transistor_6 (.in(d_ff_6_q), .out(O10), .gate(nRegEn));
  and and_13 (and_13_out, I9, LM);
  or or_7 (or_7_out, and_13_out, and_14_out);
  and and_14 (and_14_out, not_1_out, d_ff_7_q);
  D_Flip_Flop #(.trigger("falling")) d_ff_7 (
    .clk(CLK), .D(or_7_out), .Q(d_ff_7_q), .reset(CLR));  // open: Qn, preset, en
  and and_15 (and_15_out, I8, LM);
  Transistor transistor_7 (.in(d_ff_7_q), .out(O9), .gate(nRegEn));
  or or_8 (or_8_out, and_15_out, and_16_out);
  and and_16 (and_16_out, not_1_out, d_ff_8_q);
  D_Flip_Flop #(.trigger("falling")) d_ff_8 (
    .clk(CLK), .D(or_8_out), .Q(d_ff_8_q), .reset(CLR));  // open: Qn, preset, en
  and and_17 (and_17_out, I7, LM);
  Transistor transistor_8 (.in(d_ff_8_q), .out(O8), .gate(nRegEn));
  or or_9 (or_9_out, and_17_out, and_18_out);
  and and_18 (and_18_out, not_1_out, d_ff_9_q);
  D_Flip_Flop #(.trigger("falling")) d_ff_9 (
    .clk(CLK), .D(or_9_out), .Q(d_ff_9_q), .reset(CLR));  // open: Qn, preset, en
  Transistor transistor_9 (.in(d_ff_9_q), .out(O7), .gate(nRegEn));
  and and_19 (and_19_out, I6, LM);
  and and_20 (and_20_out, not_1_out, d_ff_10_q);
  or or_10 (or_10_out, and_19_out, and_20_out);
  D_Flip_Flop #(.trigger("falling")) d_ff_10 (
    .clk(CLK), .D(or_10_out), .Q(d_ff_10_q), .reset(CLR));  // open: Qn, preset, en
  Transistor transistor_10 (.in(d_ff_10_q), .out(O6), .gate(nRegEn));
  and and_21 (and_21_out, I5, LM);
  or or_11 (or_11_out, and_21_out, and_22_out);
  and and_22 (and_22_out, not_1_out, d_ff_11_q);
  D_Flip_Flop #(.trigger("falling")) d_ff_11 (
    .clk(CLK), .D(or_11_out), .Q(d_ff_11_q), .reset(CLR));  // open: Qn, preset, en
  Transistor transistor_11 (.in(d_ff_11_q), .out(O5), .gate(nRegEn));
  and and_23 (and_23_out, I4, LM);
  and and_24 (and_24_out, not_1_out, d_ff_12_q);
  or or_12 (or_12_out, and_23_out, and_24_out);
  D_Flip_Flop #(.trigger("falling")) d_ff_12 (
    .clk(CLK), .D(or_12_out), .Q(d_ff_12_q), .reset(CLR));  // open: Qn, preset, en
  Transistor transistor_12 (.in(d_ff_12_q), .out(O4), .gate(nRegEn));
  and and_25 (and_25_out, I3, LM);
  and and_26 (and_26_out, not_1_out, d_ff_13_q);
  or or_13 (or_13_out, and_25_out, and_26_out);
  D_Flip_Flop #(.trigger("falling")) d_ff_13 (
    .clk(CLK), .D(or_13_out), .Q(d_ff_13_q), .reset(CLR));  // open: Qn, preset, en
  Transistor transistor_13 (.in(d_ff_13_q), .out(O3), .gate(nRegEn));
  and and_27 (and_27_out, I2, LM);
  and and_28 (and_28_out, not_1_out, d_ff_14_q);
  or or_14 (or_14_out, and_27_out, and_28_out);
  D_Flip_Flop #(.trigger("falling")) d_ff_14 (
    .clk(CLK), .D(or_14_out), .Q(d_ff_14_q), .reset(CLR));  // open: Qn, preset, en
  Transistor transistor_14 (.in(d_ff_14_q), .out(O2), .gate(nRegEn));
  and and_29 (and_29_out, I1, LM);
  and and_30 (and_30_out, not_1_out, d_ff_15_q);
  or or_15 (or_15_out, and_29_out, and_30_out);
  D_Flip_Flop #(.trigger("falling")) d_ff_15 (
    .clk(CLK), .D(or_15_out), .Q(d_ff_15_q), .reset(CLR));  // open: Qn, preset, en
  Transistor transistor_15 (.in(d_ff_15_q), .out(O1), .gate(nRegEn));
  and and_31 (and_31_out, I0, LM);
  not not_1 (not_1_out, LM);
  and and_32 (and_32_out, not_1_out, d_ff_16_q);
  or or_16 (or_16_out, and_31_out, and_32_out);
  D_Flip_Flop #(.trigger("falling")) d_ff_16 (
    .clk(CLK), .D(or_16_out), .Q(d_ff_16_q), .reset(CLR));  // open: Qn, preset, en
  Transistor transistor_16 (.in(d_ff_16_q), .out(O0), .gate(nRegEn));
endmodule

module Full_Adder (
  input  A,
  input  B,
  input  C,
  output O,
  output C_2
);

  wire and_1_out, and_2_out, xor_1_out;

  xor xor_1 (xor_1_out, A, B);
  and and_1 (and_1_out, C, xor_1_out);
  and and_2 (and_2_out, B, A);
  xor xor_2 (O, xor_1_out, C);
  or or_1 (C_2, and_1_out, and_2_out);
endmodule

module _74161 (
  input  nLOAD,
  input  A,
  input  B,
  input  C,
  input  CLK,
  input  nCLR,
  input  D,
  input  ENP,
  input  ENT,
  output QA,
  output QB,
  output QC,
  output QD,
  output RCO
);

  wire and_1_out, and_2_out, and_3_out, and_4_out, and_5_out, and_6_out, and_7_out, and_8_out, and_9_out,
       and_10_out, and_11_out, and_12_out, nand_1_out, nand_2_out, nand_3_out, nand_4_out, nand_5_out,
       nand_6_out, nand_7_out, nand_8_out, not_1_out, not_2_out, not_3_out, or_1_out, or_2_out, or_3_out,
       or_4_out;

  not not_1 (not_1_out, nLOAD);
  not not_2 (not_2_out, CLK);
  not not_3 (not_3_out, nCLR);
  and and_1 (and_1_out, ENP, ENT);
  and and_2 (and_2_out, QA, and_1_out);
  and and_3 (and_3_out, QB, QA, and_1_out);
  and and_4 (and_4_out, QC, QB, QA, and_1_out);
  nand nand_1 (nand_1_out, nand_2_out, not_1_out);
  or or_1 (or_1_out, and_1_out, not_1_out);
  nand nand_2 (nand_2_out, A, not_1_out);
  nand nand_3 (nand_3_out, nand_4_out, not_1_out);
  or or_2 (or_2_out, and_2_out, not_1_out);
  nand nand_4 (nand_4_out, B, not_1_out);
  nand nand_5 (nand_5_out, nand_6_out, not_1_out);
  or or_3 (or_3_out, and_3_out, not_1_out);
  nand nand_6 (nand_6_out, C, not_1_out);
  nand nand_7 (nand_7_out, nand_8_out, not_1_out);
  or or_4 (or_4_out, and_4_out, not_1_out);
  nand nand_8 (nand_8_out, D, not_1_out);
  and and_5 (and_5_out, nand_1_out, or_1_out);
  and and_6 (and_6_out, or_1_out, nand_2_out);
  and and_7 (and_7_out, nand_3_out, or_2_out);
  and and_8 (and_8_out, or_2_out, nand_4_out);
  and and_9 (and_9_out, nand_5_out, or_3_out);
  and and_10 (and_10_out, or_3_out, nand_6_out);
  and and_11 (and_11_out, nand_7_out, or_4_out);
  and and_12 (and_12_out, or_4_out, nand_8_out);
  J_K_Flip_Flop j_k_ff_1 (
    .J(and_5_out), .clk(not_2_out), .K(and_6_out), .Q(QA), .reset(not_3_out));  // open: Qn, preset, en
  J_K_Flip_Flop j_k_ff_2 (
    .J(and_7_out), .clk(not_2_out), .K(and_8_out), .Q(QB), .reset(not_3_out));  // open: Qn, preset, en
  J_K_Flip_Flop j_k_ff_3 (
    .J(and_9_out), .clk(not_2_out), .K(and_10_out), .Q(QC), .reset(not_3_out));  // open: Qn, preset, en
  J_K_Flip_Flop j_k_ff_4 (
    .J(and_11_out), .clk(not_2_out), .K(and_12_out), .Q(QD), .reset(not_3_out));  // open: Qn, preset, en
  and and_13 (RCO, QD, QC, QB, QA, ENT);
endmodule

module MANIAC (
  input  Examine,
  input  Examine_Next,
  input  Deposit,
  input  Deposit_Next,
  input  Edit,
  input  Single_Step,
  input  Run___Stop,
  input  CLR_HLT,
  input  A0,
  input  A1,
  input  A2,
  input  A3,
  input  A4,
  input  A5,
  input  A6,
  input  A7,
  input  A8,
  input  A9,
  input  A10,
  input  A11,
  input  A12,
  input  A13,
  input  A14,
  input  A15,
  input  D0,
  input  D1,
  input  D2,
  input  D3,
  input  D4,
  input  D5,
  input  D6,
  input  D7,
  input  D8,
  input  D9,
  input  D10,
  input  D11,
  input  D12,
  input  D13,
  input  D14,
  input  D15,
  input  MANIAC_IN_0,
  input  MANIAC_IN_1,
  input  MANIAC_IN_2,
  input  MANIAC_IN_3,
  input  MANIAC_IN_4,
  input  MANIAC_IN_5,
  input  MANIAC_IN_6,
  input  MANIAC_IN_7,
  input  MANIAC_IN_8,
  input  MANIAC_IN_9,
  input  MANIAC_IN_10,
  input  MANIAC_IN_11,
  input  MANIAC_IN_12,
  input  MANIAC_IN_13,
  input  MANIAC_IN_14,
  input  MANIAC_IN_15,
  input  MANIAC_INPUT0___data_ready,
  input  MANIAC_OUTPUT0___data_recived,
  input  MANIAC_IN_0_2,
  input  MANIAC_IN_1_2,
  input  MANIAC_IN_2_2,
  input  MANIAC_IN_3_2,
  input  MANIAC_IN_4_2,
  input  MANIAC_IN_5_2,
  input  MANIAC_IN_6_2,
  input  MANIAC_IN_7_2,
  input  MANIAC_IN_8_2,
  input  MANIAC_IN_9_2,
  input  MANIAC_IN_10_2,
  input  MANIAC_IN_11_2,
  input  MANIAC_IN_12_2,
  input  MANIAC_IN_13_2,
  input  MANIAC_IN_14_2,
  input  MANIAC_IN_15_2,
  input  MANIAC_INPUT1___data_ready,
  input  MANIAC_OUTPUT1___data_recived,
  input  MANIAC_IN_0_3,
  input  MANIAC_IN_1_3,
  input  MANIAC_IN_2_3,
  input  MANIAC_IN_3_3,
  input  MANIAC_IN_4_3,
  input  MANIAC_IN_5_3,
  input  MANIAC_IN_6_3,
  input  MANIAC_IN_7_3,
  input  MANIAC_IN_8_3,
  input  MANIAC_IN_9_3,
  input  MANIAC_IN_10_3,
  input  MANIAC_IN_11_3,
  input  MANIAC_IN_12_3,
  input  MANIAC_IN_13_3,
  input  MANIAC_IN_14_3,
  input  MANIAC_IN_15_3,
  input  MANIAC_INPUT2___data_ready,
  input  MANIAC_OUTPUT2___data_recived,
  input  MANIAC_IN_0_4,
  input  MANIAC_IN_1_4,
  input  MANIAC_IN_2_4,
  input  MANIAC_IN_3_4,
  input  MANIAC_IN_4_4,
  input  MANIAC_IN_5_4,
  input  MANIAC_IN_6_4,
  input  MANIAC_IN_7_4,
  input  MANIAC_IN_8_4,
  input  MANIAC_IN_9_4,
  input  MANIAC_IN_10_4,
  input  MANIAC_IN_11_4,
  input  MANIAC_IN_12_4,
  input  MANIAC_IN_13_4,
  input  MANIAC_IN_14_4,
  input  MANIAC_IN_15_4,
  input  MANIAC_INPUT3___data_ready,
  input  MANIAC_OUTPUT3___data_recived,
  output HLT,
  output out_114,
  output out_115,
  output out_116,
  output out_117,
  output Bus_0,
  output Bus_1,
  output Bus_2,
  output Bus_3,
  output Bus_4,
  output Bus_5,
  output Bus_6,
  output Bus_7,
  output Bus_8,
  output Bus_9,
  output Bus_10,
  output Bus_11,
  output Bus_12,
  output Bus_13,
  output Bus_14,
  output Bus_15,
  output Adr_0,
  output Adr_1,
  output Adr_2,
  output Adr_3,
  output Adr_4,
  output Adr_5,
  output Adr_6,
  output Adr_7,
  output Adr_8,
  output Adr_9,
  output Adr_10,
  output Adr_11,
  output Adr_12,
  output Adr_13,
  output Adr_14,
  output Adr_15,
  output MANIAC_OUT_0,
  output MANIAC_OUT_1,
  output MANIAC_OUT_2,
  output MANIAC_OUT_3,
  output MANIAC_OUT_4,
  output MANIAC_OUT_5,
  output MANIAC_OUT_6,
  output MANIAC_OUT_7,
  output MANIAC_OUT_8,
  output MANIAC_OUT_9,
  output MANIAC_OUT_10,
  output MANIAC_OUT_11,
  output MANIAC_OUT_12,
  output MANIAC_OUT_13,
  output MANIAC_OUT_14,
  output MANIAC_OUT_15,
  output INPUT_0_ready_INDICATOR,
  output MANIAC_OUT_0_2,
  output MANIAC_OUT_1_2,
  output MANIAC_OUT_2_2,
  output MANIAC_OUT_3_2,
  output MANIAC_OUT_4_2,
  output MANIAC_OUT_5_2,
  output MANIAC_OUT_6_2,
  output MANIAC_OUT_7_2,
  output MANIAC_OUT_8_2,
  output MANIAC_OUT_9_2,
  output MANIAC_OUT_10_2,
  output MANIAC_OUT_11_2,
  output MANIAC_OUT_12_2,
  output MANIAC_OUT_13_2,
  output MANIAC_OUT_14_2,
  output MANIAC_OUT_15_2,
  output INPUT_1_ready_INDICATOR,
  output MANIAC_OUT_0_3,
  output MANIAC_OUT_1_3,
  output MANIAC_OUT_2_3,
  output MANIAC_OUT_3_3,
  output MANIAC_OUT_4_3,
  output MANIAC_OUT_5_3,
  output MANIAC_OUT_6_3,
  output MANIAC_OUT_7_3,
  output MANIAC_OUT_8_3,
  output MANIAC_OUT_9_3,
  output MANIAC_OUT_10_3,
  output MANIAC_OUT_11_3,
  output MANIAC_OUT_12_3,
  output MANIAC_OUT_13_3,
  output MANIAC_OUT_14_3,
  output MANIAC_OUT_15_3,
  output INPUT_2_ready_INDICATOR,
  output MANIAC_OUT_0_4,
  output MANIAC_OUT_1_4,
  output MANIAC_OUT_2_4,
  output MANIAC_OUT_3_4,
  output MANIAC_OUT_4_4,
  output MANIAC_OUT_5_4,
  output MANIAC_OUT_6_4,
  output MANIAC_OUT_7_4,
  output MANIAC_OUT_8_4,
  output MANIAC_OUT_9_4,
  output MANIAC_OUT_10_4,
  output MANIAC_OUT_11_4,
  output MANIAC_OUT_12_4,
  output MANIAC_OUT_13_4,
  output MANIAC_OUT_14_4,
  output MANIAC_OUT_15_4,
  output INPUT_3_ready_INDICATOR
);

  wire A0_ob0, A0_ob1, A0_ob2, A0_ob3, A0_ob4, A0_ob5, A0_ob6, A0_ob7, A0_ob8, A0_ob9, A0_ob10, A0_ob11,
       A0_ob12, A0_ob13, A0_ob14, A0_ob15, A0load, A1load, A2load, A3load, alu_1_crfo, alu_1_mfo, alu_1_ovf,
       alu_1_prfo, alu_1_zrf, ALUadr0, ALUadr1, ALUadr2, ALUadr3, and_1_out, and_2_out, and_3_out, and_5_out,
       and_6_out, and_7_out, and_10_out, and_11_out, and_13_out, and_14_out, and_15_out, and_16_out,
       and_17_out, and_18_out, and_19_out, and_20_out, B0_ob0, B0_ob1, B0_ob2, B0_ob3, B0_ob4, B0_ob5,
       B0_ob6, B0_ob7, B0_ob8, B0_ob9, B0_ob10, B0_ob11, B0_ob12, B0_ob13, B0_ob14, B0_ob15, B0load, B1load,
       B2load, B3load, BOOT, BOOTcounterUP, buff_short_one_protection_1_o, buff_short_one_protection_2_o,
       buff_short_one_protection_3_o, buff_short_one_protection_4_o, buff_short_one_protection_5_o,
       buff_short_one_protection_6_o, buff_short_one_protection_7_o, buff_short_one_protection_8_o,
       buff_short_one_protection_9_o, buff_short_one_protection_10_o, buff_short_one_protection_11_o,
       buff_short_one_protection_12_o, buff_short_one_protection_13_o, buff_short_one_protection_14_o,
       buff_short_zero_protection_1_out, buff_short_zero_protection_2_out, buff_short_zero_protection_3_out,
       buff_short_zero_protection_4_out, buff_short_zero_protection_5_out, buff_short_zero_protection_6_out,
       buff_short_zero_protection_7_out, buff_short_zero_protection_8_out, buff_short_zero_protection_9_out,
       buff_short_zero_protection_10_out, buff_short_zero_protection_11_out, buffer_1_out, buffer_2_out,
       buffer_3_out, buffer_4_out, buffer_5_out, buffer_6_out, buffer_7_out, buffer_8_out, buffer_9_out,
       buffer_10_out, buffer_11_out, buffer_12_out, buffer_13_out, buffer_14_out, buffer_15_out,
       buffer_16_out, buffer_17_out, buffer_18_out, buffer_19_out, buffer_20_out, buffer_21_out,
       buffer_22_out, buffer_23_out, buffer_24_out, buffer_25_out, buffer_26_out, CLF, CLK, CLK_out,
       d_ff_1_q, enALUout, enPC, enSPout, FLadr0, FLadr1, FLadr2, FLadr3, flag_reg_1_cr_2, flag_reg_1_crout,
       flag_reg_1_mout, flag_reg_1_nuout, flag_reg_1_nuout_2, flag_reg_1_nuout_3, flag_reg_1_ovfout,
       flag_reg_1_prout, flag_reg_1_zrout, Flag_state, G0load, G1load, huge_delay_1_out, huge_delay_2_out,
       incPC, INR0_CLF, INR1_CLF, INR2_CLF, INR3_CLF, IRload, jpr_1_o0, jpr_1_o1, jpr_1_o2, jpr_1_o3,
       jpr_1_o4, jpr_1_o5, jpr_1_o6, jpr_1_o7, jpr_1_o8, jpr_1_o9, jpr_1_o10, jpr_1_o11, jpr_1_o12,
       jpr_1_o13, jpr_1_o14, jpr_1_o15, JPRload, ldALUflagREG, MARload, n16bit_74193_3_oa0,
       n16bit_74193_3_oa1, n16bit_74193_3_oa2, n16bit_74193_3_oa3, n16bit_74193_3_oa4, n16bit_74193_3_oa5,
       n16bit_74193_3_oa6, n16bit_74193_3_oa7, n16bit_74193_3_oa8, n16bit_74193_3_oa9, n16bit_74193_3_oa10,
       n16bit_74193_3_oa11, n16bit_74193_3_oa12, n16bit_74193_3_oa13, n16bit_74193_3_oa14,
       n16bit_74193_3_oa15, nA_bus____Main_bus, nB_bus____Main_bus, nclrJPR, nenA0out, nenA1out, nenA2out,
       nenA3out, nenB0out, nenB1out, nenB2out, nenB3out, nenFlagREG, nenG0out, nenG1out, nenINPUT0,
       nenINPUT1, nenINPUT2, nenINPUT3, nenR0, nIDcounterLOAD, nLoadBOOTcounter, nloadSP, nmain_bus____MAR,
       nMAR____main_bus, nor_1_out, NOT, not_1_out, not_2_out, not_3_out, not_4_out, not_5_out, not_6_out,
       not_7_out, not_8_out, not_9_out, not_10_out, not_11_out, not_12_out, not_13_out, not_14_out,
       not_15_out, not_17_out, not_18_out, not_19_out, not_20_out, not_21_out, not_22_out, not_23_out,
       not_24_out, not_25_out, not_26_out, not_27_out, not_28_out, not_29_out, not_30_out, not_31_out,
       not_32_out, not_33_out, not_34_out, Not_Used, nPC____Main_bus, nPCload, nRAMen__nCE, nRAMread__nOE,
       nRAMwrite__nWE, or_1_out, or_2_out, or_3_out, or_4_out, or_5_out, or_6_out, or_7_out, or_8_out,
       OUTPUTregLoad0, OUTPUTregLoad1, OUTPUTregLoad2, OUTPUTregLoad3, OUTR0, OUTR0_STF, OUTR1, OUTR1_STF,
       OUTR2, OUTR2_STF, OUTR3, OUTR3_STF, pc_adder_1_o0, pc_adder_1_o1, pc_adder_1_o2, pc_adder_1_o3,
       pc_adder_1_o4, pc_adder_1_o5, pc_adder_1_o6, pc_adder_1_o7, pc_adder_1_o8, pc_adder_1_o9,
       pc_adder_1_o10, pc_adder_1_o11, pc_adder_1_o12, pc_adder_1_o13, pc_adder_1_o14, pc_adder_1_o15,
       RAM_read, RAM_write, Reset, SPdown, spOVF, SPup, STF, uprgraded_buffer_1_out, uprgraded_buffer_2_out,
       uprgraded_buffer_3_out, uprgraded_buffer_4_out, uprgraded_buffer_5_out, uprgraded_buffer_6_out,
       USEloopBOOTcounter;
  wire [0:0] n74193_experimental_1_qa;
  wire [15:0] multiplexer_1_out, multiplexer_2_out, multiplexer_3_out, n16bit_74193_1_oa0,
       n16bit_74193_2_oa0, reg_2_o0, rom_1_data;
  wire [15:4] reg_1_o11;

  Multiplexer #(.width(16)) multiplexer_1 (
    .in0(16'h5c00), .in1(16'h8fff), .out(multiplexer_1_out), .sel(reg_1_o11[8]));  // open: en
  Multiplexer #(.width(16)) multiplexer_2 (
    .in0({reg_1_o11[15:14], ALUadr3, ALUadr2, ALUadr1, ALUadr0, reg_1_o11[9:4], FLadr3, FLadr2, FLadr1, FLadr0}),
    .in1(multiplexer_1_out), .out(multiplexer_2_out), .sel(or_1_out));  // open: en
  not not_1 (not_1_out, reg_1_o11[15]);
  not not_2 (not_2_out, ALUadr3);
  not not_3 (not_3_out, ALUadr1);
  not not_4 (not_4_out, ALUadr0);
  and and_1 (and_1_out, not_3_out, reg_1_o11[9], not_4_out, not_12_out);
  and and_2 (and_2_out, not_1_out, reg_1_o11[14], not_2_out, ALUadr2);
  and and_3 (and_3_out, and_2_out, and_1_out);
  ROM #(.addrWidth(16), .dataWidth(16)) rom_1 (.addr(multiplexer_2_out), .data(rom_1_data), .sel(1'b1));
  and and_4 (HLT, reg_1_o11[15], not_8_out, not_5_out, not_7_out, not_6_out, not_9_out);
  not not_5 (not_5_out, ALUadr3);
  not not_6 (not_6_out, ALUadr1);
  not not_7 (not_7_out, ALUadr2);
  not not_8 (not_8_out, reg_1_o11[14]);
  or or_1 (or_1_out, and_3_out, and_7_out);
  not not_9 (not_9_out, ALUadr0);
  not not_10 (not_10_out, ALUadr3);
  not not_11 (not_11_out, reg_1_o11[15]);
  and and_5 (and_5_out, not_11_out, reg_1_o11[14], not_10_out, ALUadr2);
  not not_12 (not_12_out, Flag_state);
  not not_13 (not_13_out, ALUadr1);
  and and_6 (and_6_out, not_13_out, reg_1_o11[9], ALUadr0, not_12_out);
  and and_7 (and_7_out, and_5_out, and_6_out);
  buf buffer_1 (buffer_1_out, uprgraded_buffer_1_out);
  _74193_experimental u_74193_experimental_1 (
    .CLR(Reset), .UP(CLK), .DOWN(1'b1), .nLOAD(1'b1), .A(1'b0), .B(1'b0), .C(1'b0), .D(1'b0),
    .QA(n74193_experimental_1_qa[0]));  // open: QB, QC, QD, CO, BO
  uprgraded_buffer uprgraded_buffer_1 (.In(nIDcounterLOAD), .Out(uprgraded_buffer_1_out));
  uprgraded_buffer uprgraded_buffer_2 (.In(uprgraded_buffer_1_out), .Out(uprgraded_buffer_2_out));
  Transistor #(.\type ("n")) transistor_1 (.in(1'b1), .out(buffer_1_out), .gate(uprgraded_buffer_2_out));
  _16bit_74193 u_16bit_74193_1 (
    .I0(rom_1_data[0]), .I1(rom_1_data[1]), .I2(rom_1_data[2]), .I3(rom_1_data[3]), .I4(rom_1_data[4]),
    .I5(rom_1_data[5]), .I6(rom_1_data[6]), .I7(rom_1_data[7]), .I8(rom_1_data[8]), .I9(rom_1_data[9]),
    .I10(rom_1_data[10]), .I11(rom_1_data[11]), .I12(rom_1_data[12]), .I13(rom_1_data[13]),
    .I14(rom_1_data[14]), .I15(rom_1_data[15]), .CLR(Reset), .DOWN(1'b1), .UP(CLK), .nLOAD(buffer_1_out),
    .enAout(1'b1), .OA0(n16bit_74193_1_oa0[0]), .OA1(n16bit_74193_1_oa0[1]), .OA2(n16bit_74193_1_oa0[2]),
    .OA3(n16bit_74193_1_oa0[3]), .OA4(n16bit_74193_1_oa0[4]), .OA5(n16bit_74193_1_oa0[5]),
    .OA6(n16bit_74193_1_oa0[6]), .OA7(n16bit_74193_1_oa0[7]), .OA8(n16bit_74193_1_oa0[8]),
    .OA9(n16bit_74193_1_oa0[9]), .OA10(n16bit_74193_1_oa0[10]), .OA11(n16bit_74193_1_oa0[11]),
    .OA12(n16bit_74193_1_oa0[12]), .OA13(n16bit_74193_1_oa0[13]), .OA14(n16bit_74193_1_oa0[14]),
    .OA15(n16bit_74193_1_oa0[15]));  // open: spOVF
  D_Flip_Flop d_ff_1 (.Q(d_ff_1_q), .preset(Edit), .reset(n74193_experimental_1_qa[0]));  // open: clk, D, Qn, en
  Multiplexer #(.width(16)) multiplexer_3 (
    .in0(n16bit_74193_1_oa0), .in1({{15{1'b0}}, n74193_experimental_1_qa[0]}), .out(multiplexer_3_out),
    .sel(d_ff_1_q));  // open: en
  // Probe on multiplexer_3_out
  or or_2 (or_2_out, Examine, Examine_Next);
  or or_3 (or_3_out, Deposit, Deposit_Next);
  nor nor_1 (nor_1_out, Examine, Deposit);
  or or_4 (or_4_out, Examine_Next, Deposit_Next);
  not not_14 (not_14_out, HLT);
  ROM #(.addrWidth(16), .dataWidth(32)) rom_2 (
    .addr(multiplexer_3_out),
    .data({nenB3out, B3load, nenB2out, B2load, nenB1out, B1load, nenB0out, B0load, nenA3out, A3load, nenA2out, A2load, nenA1out, A1load, nenA0out, A0load, incPC, nPCload, JPRload, nclrJPR, nPC____Main_bus, nRAMread__nOE, nRAMwrite__nWE, nRAMen__nCE, nmain_bus____MAR, nIDcounterLOAD, IRload, MARload, BOOT, USEloopBOOTcounter, nLoadBOOTcounter, BOOTcounterUP}),
    .sel(1'b1));
  ROM #(.addrWidth(16), .dataWidth(32)) rom_3 (
    .addr(multiplexer_3_out),
    .data({enPC, nenFlagREG, nenINPUT3, nenINPUT2, nenINPUT1, nenINPUT0, {4{Not_Used}}, STF, CLF, ldALUflagREG, NOT, OUTPUTregLoad3, OUTPUTregLoad2, OUTPUTregLoad1, OUTPUTregLoad0, enALUout, Not_Used, nMAR____main_bus, nenR0, enSPout, nloadSP, SPup, SPdown, nB_bus____Main_bus, nA_bus____Main_bus, nenG1out, G1load, nenG0out, G0load}),
    .sel(1'b1));
  or or_5 (or_5_out, CLR_HLT, not_14_out);
  Clock u_CLK (.out(CLK_out));
  HUGE_Delay huge_delay_1 (.In(or_3_out), .Out(huge_delay_1_out));
  not not_15 (not_15_out, huge_delay_1_out);
  Row_of_transistors row_of_transistors_1 (
    .I(D0), .I_2(D1), .I_3(D2), .I_4(D3), .I_5(D4), .I_6(D5), .I_7(D6), .I_8(D7), .I_9(D8), .I_10(D9),
    .I_11(D10), .I_12(D11), .I_13(D12), .I_14(D13), .I_15(D14), .I_16(D15), .nEnOut(not_15_out), .O(Bus_0),
    .O_2(Bus_1), .O_3(Bus_2), .O_4(Bus_3), .O_5(Bus_4), .O_6(Bus_5), .O_7(Bus_6), .O_8(Bus_7), .O_9(Bus_8),
    .O_10(Bus_9), .O_11(Bus_10), .O_12(Bus_11), .O_13(Bus_12), .O_14(Bus_13), .O_15(Bus_14), .O_16(Bus_15));
  REG reg_1 (
    .I15(Bus_0), .I14(Bus_1), .I13(Bus_2), .I12(Bus_3), .I11(Bus_4), .I10(Bus_5), .I9(Bus_6), .I8(Bus_7),
    .I7(Bus_8), .I6(Bus_9), .I5(Bus_10), .I4(Bus_11), .I3(Bus_12), .I2(Bus_13), .I1(Bus_14), .I0(Bus_15),
    .O15(FLadr0), .O14(FLadr1), .O13(FLadr2), .O12(FLadr3), .O11(reg_1_o11[4]), .O10(reg_1_o11[5]),
    .O9(reg_1_o11[6]), .O8(reg_1_o11[7]), .O7(reg_1_o11[8]), .O6(reg_1_o11[9]), .O5(ALUadr0), .O4(ALUadr1),
    .O3(ALUadr2), .O2(ALUadr3), .O1(reg_1_o11[14]), .O0(reg_1_o11[15]), .LM(buff_short_one_protection_1_o),
    .CLR(Reset), .CLK(CLK), .nRegEn(1'b0));
  Buff_short_one_protection buff_short_one_protection_1 (.I(IRload), .O(buff_short_one_protection_1_o));
  and and_8 (RAM_read, Edit, or_2_out);
  and and_9 (RAM_write, Edit, or_3_out);
  not not_16 (Reset, Edit);
  or or_6 (or_6_out, Single_Step, and_10_out);
  and and_10 (and_10_out, Run___Stop, CLK_out);
  and and_11 (and_11_out, or_6_out, Reset);
  and and_12 (CLK, or_5_out, and_11_out);
  // Probe on {Adr_15, Adr_14, Adr_13, Adr_12, Adr_11, Adr_10, Adr_9, Adr_8, Adr_7, Adr_6, Adr_5, Adr_4, Adr_3, Adr_2, Adr_1, Adr_0}
  _16bit_74193 u_16bit_74193_2 (
    .I0(A0), .I1(A1), .I2(A2), .I3(A3), .I4(A4), .I5(A5), .I6(A6), .I7(A7), .I8(A8), .I9(A9), .I10(A10),
    .I11(A11), .I12(A12), .I13(A13), .I14(A14), .I15(A15), .CLR(Reset), .DOWN(1'b1), .UP(or_4_out),
    .nLOAD(nor_1_out), .enAout(1'b1), .OA0(n16bit_74193_2_oa0[0]), .OA1(n16bit_74193_2_oa0[1]),
    .OA2(n16bit_74193_2_oa0[2]), .OA3(n16bit_74193_2_oa0[3]), .OA4(n16bit_74193_2_oa0[4]),
    .OA5(n16bit_74193_2_oa0[5]), .OA6(n16bit_74193_2_oa0[6]), .OA7(n16bit_74193_2_oa0[7]),
    .OA8(n16bit_74193_2_oa0[8]), .OA9(n16bit_74193_2_oa0[9]), .OA10(n16bit_74193_2_oa0[10]),
    .OA11(n16bit_74193_2_oa0[11]), .OA12(n16bit_74193_2_oa0[12]), .OA13(n16bit_74193_2_oa0[13]),
    .OA14(n16bit_74193_2_oa0[14]), .OA15(n16bit_74193_2_oa0[15]));  // open: spOVF
  buf buffer_2 (buffer_2_out, buffer_3_out);
  buf buffer_3 (buffer_3_out, RAM_write);
  buf buffer_4 (buffer_4_out, buffer_5_out);
  buf buffer_5 (buffer_5_out, RAM_read);
  not not_17 (not_17_out, RAM_write);
  and and_13 (and_13_out, not_17_out, buffer_6_out);
  buf buffer_6 (buffer_6_out, nRAMwrite__nWE);
  buf buffer_7 (buffer_7_out, buffer_8_out);
  buf buffer_8 (buffer_8_out, RAM_read);
  not not_18 (not_18_out, RAM_read);
  and and_14 (and_14_out, not_18_out, buffer_9_out);
  buf buffer_9 (buffer_9_out, nRAMread__nOE);
  Multiplexer #(.width(16)) multiplexer_4 (
    .in0(reg_2_o0), .in1(n16bit_74193_2_oa0),
    .out({Adr_15, Adr_14, Adr_13, Adr_12, Adr_11, Adr_10, Adr_9, Adr_8, Adr_7, Adr_6, Adr_5, Adr_4, Adr_3, Adr_2, Adr_1, Adr_0}),
    .sel(Edit));  // open: en
  buf buffer_10 (buffer_10_out, buffer_2_out);
  buf buffer_11 (buffer_11_out, buffer_12_out);
  buf buffer_12 (buffer_12_out, buffer_10_out);
  buf buffer_13 (buffer_13_out, buffer_11_out);
  buf buffer_14 (buffer_14_out, buffer_17_out);
  buf buffer_15 (buffer_15_out, buffer_4_out);
  buf buffer_16 (buffer_16_out, buffer_15_out);
  buf buffer_17 (buffer_17_out, buffer_16_out);
  not not_19 (not_19_out, nRAMen__nCE);
  or or_7 (or_7_out, and_13_out, buffer_7_out);
  not not_20 (not_20_out, and_14_out);
  uprgraded_buffer uprgraded_buffer_3 (.In(or_8_out), .Out(uprgraded_buffer_3_out));
  or or_8 (or_8_out, buffer_18_out, buffer_21_out, buffer_24_out);
  buf buffer_18 (buffer_18_out, buffer_19_out);
  buf buffer_19 (buffer_19_out, buffer_20_out);
  buf buffer_20 (buffer_20_out, buffer_13_out);
  buf buffer_21 (buffer_21_out, buffer_22_out);
  buf buffer_22 (buffer_22_out, buffer_23_out);
  buf buffer_23 (buffer_23_out, buffer_14_out);
  buf buffer_24 (buffer_24_out, buffer_25_out);
  buf buffer_25 (buffer_25_out, not_19_out);
  and and_15 (and_15_out, or_7_out, not_20_out);
  uprgraded_buffer uprgraded_buffer_4 (.In(buffer_26_out), .Out(uprgraded_buffer_4_out));
  buf buffer_26 (buffer_26_out, and_15_out);
  _16bit_74193 u_16bit_74193_3 (
    .I0(Bus_0), .I1(Bus_1), .I2(Bus_2), .I3(Bus_3), .I4(Bus_4), .I5(Bus_5), .I6(Bus_6), .I7(Bus_7),
    .I8(Bus_8), .I9(Bus_9), .I10(Bus_10), .I11(Bus_11), .I12(Bus_12), .I13(Bus_13), .I14(Bus_14),
    .I15(Bus_15), .CLR(Reset), .DOWN(1'b1), .UP(uprgraded_buffer_6_out), .nLOAD(uprgraded_buffer_5_out),
    .enAout(enPC), .OA0(n16bit_74193_3_oa0), .OA1(n16bit_74193_3_oa1), .OA2(n16bit_74193_3_oa2),
    .OA3(n16bit_74193_3_oa3), .OA4(n16bit_74193_3_oa4), .OA5(n16bit_74193_3_oa5), .OA6(n16bit_74193_3_oa6),
    .OA7(n16bit_74193_3_oa7), .OA8(n16bit_74193_3_oa8), .OA9(n16bit_74193_3_oa9), .OA10(n16bit_74193_3_oa10),
    .OA11(n16bit_74193_3_oa11), .OA12(n16bit_74193_3_oa12), .OA13(n16bit_74193_3_oa13),
    .OA14(n16bit_74193_3_oa14), .OA15(n16bit_74193_3_oa15));  // open: spOVF
  uprgraded_buffer uprgraded_buffer_5 (.In(nPCload), .Out(uprgraded_buffer_5_out));
  PC_adder pc_adder_1 (
    .A15(n16bit_74193_3_oa15), .A14(n16bit_74193_3_oa14), .A13(n16bit_74193_3_oa13),
    .A12(n16bit_74193_3_oa12), .A11(n16bit_74193_3_oa11), .A10(n16bit_74193_3_oa10), .A9(n16bit_74193_3_oa9),
    .A8(n16bit_74193_3_oa8), .A7(n16bit_74193_3_oa7), .A6(n16bit_74193_3_oa6), .A5(n16bit_74193_3_oa5),
    .A4(n16bit_74193_3_oa4), .A3(n16bit_74193_3_oa3), .A2(n16bit_74193_3_oa2), .A1(n16bit_74193_3_oa1),
    .A0(n16bit_74193_3_oa0), .O15(pc_adder_1_o15), .O14(pc_adder_1_o14), .O13(pc_adder_1_o13),
    .O12(pc_adder_1_o12), .O11(pc_adder_1_o11), .O10(pc_adder_1_o10), .O9(pc_adder_1_o9), .O8(pc_adder_1_o8),
    .O7(pc_adder_1_o7), .O6(pc_adder_1_o6), .O5(pc_adder_1_o5), .O4(pc_adder_1_o4), .O3(pc_adder_1_o3),
    .O2(pc_adder_1_o2), .O1(pc_adder_1_o1), .O0(pc_adder_1_o0), .B0(jpr_1_o15), .B1(jpr_1_o14),
    .B2(jpr_1_o13), .B3(jpr_1_o12), .B4(jpr_1_o11), .B5(jpr_1_o10), .B6(jpr_1_o9), .B7(jpr_1_o8),
    .B8(jpr_1_o7), .B9(jpr_1_o6), .B10(jpr_1_o5), .B11(jpr_1_o4), .B12(jpr_1_o3), .B13(jpr_1_o2),
    .B14(jpr_1_o1), .B15(jpr_1_o0));
  REG reg_2 (
    .I15(pc_adder_1_o15), .I14(pc_adder_1_o14), .I13(pc_adder_1_o13), .I12(pc_adder_1_o12),
    .I11(pc_adder_1_o11), .I10(pc_adder_1_o10), .I9(pc_adder_1_o9), .I8(pc_adder_1_o8), .I7(pc_adder_1_o7),
    .I6(pc_adder_1_o6), .I5(pc_adder_1_o5), .I4(pc_adder_1_o4), .I3(pc_adder_1_o3), .I2(pc_adder_1_o2),
    .I1(pc_adder_1_o1), .I0(pc_adder_1_o0), .O15(reg_2_o0[15]), .O14(reg_2_o0[14]), .O13(reg_2_o0[13]),
    .O12(reg_2_o0[12]), .O11(reg_2_o0[11]), .O10(reg_2_o0[10]), .O9(reg_2_o0[9]), .O8(reg_2_o0[8]),
    .O7(reg_2_o0[7]), .O6(reg_2_o0[6]), .O5(reg_2_o0[5]), .O4(reg_2_o0[4]), .O3(reg_2_o0[3]),
    .O2(reg_2_o0[2]), .O1(reg_2_o0[1]), .O0(reg_2_o0[0]), .LM(MARload), .CLR(Reset), .CLK(not_21_out),
    .nRegEn(1'b0));
  not not_21 (not_21_out, huge_delay_2_out);
  HUGE_Delay huge_delay_2 (.In(CLK), .Out(huge_delay_2_out));
  RAM #(.addrWidth(16), .dataWidth(16), .bus("asynch")) ram_1 (
    .addr({Adr_15, Adr_14, Adr_13, Adr_12, Adr_11, Adr_10, Adr_9, Adr_8, Adr_7, Adr_6, Adr_5, Adr_4, Adr_3, Adr_2, Adr_1, Adr_0}),
    .data({Bus_15, Bus_14, Bus_13, Bus_12, Bus_11, Bus_10, Bus_9, Bus_8, Bus_7, Bus_6, Bus_5, Bus_4, Bus_3, Bus_2, Bus_1, Bus_0}),
    .sel(uprgraded_buffer_3_out), .ld(uprgraded_buffer_4_out));  // open: clr
  and and_16 (and_16_out, incPC, not_26_out);
  uprgraded_buffer uprgraded_buffer_6 (.In(and_16_out), .Out(uprgraded_buffer_6_out));
  not not_22 (not_22_out, MANIAC_OUTPUT0___data_recived);
  not not_23 (not_23_out, MANIAC_OUTPUT1___data_recived);
  not not_24 (not_24_out, MANIAC_OUTPUT2___data_recived);
  not not_25 (not_25_out, MANIAC_OUTPUT3___data_recived);
  not not_26 (not_26_out, CLK);
  JPR jpr_1 (
    .I15(Bus_0), .I14(Bus_1), .I13(Bus_2), .I12(Bus_3), .I11(Bus_4), .I10(Bus_5), .I9(Bus_6), .I8(Bus_7),
    .I7(Bus_8), .I6(Bus_9), .I5(Bus_10), .I4(Bus_11), .I3(Bus_12), .I2(Bus_13), .I1(Bus_14), .I0(Bus_15),
    .O15(jpr_1_o15), .O14(jpr_1_o14), .O13(jpr_1_o13), .O12(jpr_1_o12), .O11(jpr_1_o11), .O10(jpr_1_o10),
    .O9(jpr_1_o9), .O8(jpr_1_o8), .O7(jpr_1_o7), .O6(jpr_1_o6), .O5(jpr_1_o5), .O4(jpr_1_o4), .O3(jpr_1_o3),
    .O2(jpr_1_o2), .O1(jpr_1_o1), .O0(jpr_1_o0), .LM(JPRload), .nCLR(nclrJPR), .CLK(CLK), .nRegEn(1'b0));
  REG reg_3 (
    .I15(Bus_0), .I14(Bus_1), .I13(Bus_2), .I12(Bus_3), .I11(Bus_4), .I10(Bus_5), .I9(Bus_6), .I8(Bus_7),
    .I7(Bus_8), .I6(Bus_9), .I5(Bus_10), .I4(Bus_11), .I3(Bus_12), .I2(Bus_13), .I1(Bus_14), .I0(Bus_15),
    .O15(MANIAC_OUT_0), .O14(MANIAC_OUT_1), .O13(MANIAC_OUT_2), .O12(MANIAC_OUT_3), .O11(MANIAC_OUT_4),
    .O10(MANIAC_OUT_5), .O9(MANIAC_OUT_6), .O8(MANIAC_OUT_7), .O7(MANIAC_OUT_8), .O6(MANIAC_OUT_9),
    .O5(MANIAC_OUT_10), .O4(MANIAC_OUT_11), .O3(MANIAC_OUT_12), .O2(MANIAC_OUT_13), .O1(MANIAC_OUT_14),
    .O0(MANIAC_OUT_15), .LM(OUTPUTregLoad0), .CLK(CLK), .nRegEn(1'b0));  // open: CLR
  Interrupt_Pin interrupt_pin_1 (.nsetINT(OUTR0_STF), .Out(OUTR0), .nclrINT(not_22_out));
  REG reg_4 (
    .I15(Bus_0), .I14(Bus_1), .I13(Bus_2), .I12(Bus_3), .I11(Bus_4), .I10(Bus_5), .I9(Bus_6), .I8(Bus_7),
    .I7(Bus_8), .I6(Bus_9), .I5(Bus_10), .I4(Bus_11), .I3(Bus_12), .I2(Bus_13), .I1(Bus_14), .I0(Bus_15),
    .O15(MANIAC_OUT_0_2), .O14(MANIAC_OUT_1_2), .O13(MANIAC_OUT_2_2), .O12(MANIAC_OUT_3_2),
    .O11(MANIAC_OUT_4_2), .O10(MANIAC_OUT_5_2), .O9(MANIAC_OUT_6_2), .O8(MANIAC_OUT_7_2),
    .O7(MANIAC_OUT_8_2), .O6(MANIAC_OUT_9_2), .O5(MANIAC_OUT_10_2), .O4(MANIAC_OUT_11_2),
    .O3(MANIAC_OUT_12_2), .O2(MANIAC_OUT_13_2), .O1(MANIAC_OUT_14_2), .O0(MANIAC_OUT_15_2),
    .LM(OUTPUTregLoad1), .CLK(CLK), .nRegEn(1'b0));  // open: CLR
  Interrupt_Pin interrupt_pin_2 (.nsetINT(OUTR1_STF), .Out(OUTR1), .nclrINT(not_23_out));
  REG reg_5 (
    .I15(Bus_0), .I14(Bus_1), .I13(Bus_2), .I12(Bus_3), .I11(Bus_4), .I10(Bus_5), .I9(Bus_6), .I8(Bus_7),
    .I7(Bus_8), .I6(Bus_9), .I5(Bus_10), .I4(Bus_11), .I3(Bus_12), .I2(Bus_13), .I1(Bus_14), .I0(Bus_15),
    .O15(MANIAC_OUT_0_3), .O14(MANIAC_OUT_1_3), .O13(MANIAC_OUT_2_3), .O12(MANIAC_OUT_3_3),
    .O11(MANIAC_OUT_4_3), .O10(MANIAC_OUT_5_3), .O9(MANIAC_OUT_6_3), .O8(MANIAC_OUT_7_3),
    .O7(MANIAC_OUT_8_3), .O6(MANIAC_OUT_9_3), .O5(MANIAC_OUT_10_3), .O4(MANIAC_OUT_11_3),
    .O3(MANIAC_OUT_12_3), .O2(MANIAC_OUT_13_3), .O1(MANIAC_OUT_14_3), .O0(MANIAC_OUT_15_3),
    .LM(OUTPUTregLoad2), .CLK(CLK), .nRegEn(1'b0));  // open: CLR
  Interrupt_Pin interrupt_pin_3 (.nsetINT(OUTR2_STF), .Out(OUTR2), .nclrINT(not_24_out));
  REG reg_6 (
    .I15(Bus_0), .I14(Bus_1), .I13(Bus_2), .I12(Bus_3), .I11(Bus_4), .I10(Bus_5), .I9(Bus_6), .I8(Bus_7),
    .I7(Bus_8), .I6(Bus_9), .I5(Bus_10), .I4(Bus_11), .I3(Bus_12), .I2(Bus_13), .I1(Bus_14), .I0(Bus_15),
    .O15(MANIAC_OUT_0_4), .O14(MANIAC_OUT_1_4), .O13(MANIAC_OUT_2_4), .O12(MANIAC_OUT_3_4),
    .O11(MANIAC_OUT_4_4), .O10(MANIAC_OUT_5_4), .O9(MANIAC_OUT_6_4), .O8(MANIAC_OUT_7_4),
    .O7(MANIAC_OUT_8_4), .O6(MANIAC_OUT_9_4), .O5(MANIAC_OUT_10_4), .O4(MANIAC_OUT_11_4),
    .O3(MANIAC_OUT_12_4), .O2(MANIAC_OUT_13_4), .O1(MANIAC_OUT_14_4), .O0(MANIAC_OUT_15_4),
    .LM(OUTPUTregLoad3), .CLK(CLK), .nRegEn(1'b0));  // open: CLR
  Interrupt_Pin interrupt_pin_4 (.nsetINT(OUTR3_STF), .Out(OUTR3), .nclrINT(not_25_out));
  Row_of_transistors row_of_transistors_2 (
    .I(n16bit_74193_3_oa0), .I_2(n16bit_74193_3_oa1), .I_3(n16bit_74193_3_oa2), .I_4(n16bit_74193_3_oa3),
    .I_5(n16bit_74193_3_oa4), .I_6(n16bit_74193_3_oa5), .I_7(n16bit_74193_3_oa6), .I_8(n16bit_74193_3_oa7),
    .I_9(n16bit_74193_3_oa8), .I_10(n16bit_74193_3_oa9), .I_11(n16bit_74193_3_oa10),
    .I_12(n16bit_74193_3_oa11), .I_13(n16bit_74193_3_oa12), .I_14(n16bit_74193_3_oa13),
    .I_15(n16bit_74193_3_oa14), .I_16(n16bit_74193_3_oa15), .nEnOut(nPC____Main_bus), .O(Bus_0), .O_2(Bus_1),
    .O_3(Bus_2), .O_4(Bus_3), .O_5(Bus_4), .O_6(Bus_5), .O_7(Bus_6), .O_8(Bus_7), .O_9(Bus_8), .O_10(Bus_9),
    .O_11(Bus_10), .O_12(Bus_11), .O_13(Bus_12), .O_14(Bus_13), .O_15(Bus_14), .O_16(Bus_15));
  Row_of_transistors row_of_transistors_3 (
    .I(Bus_15), .I_2(Bus_14), .I_3(Bus_13), .I_4(Bus_12), .I_5(Bus_11), .I_6(Bus_10), .I_7(Bus_9),
    .I_8(Bus_8), .I_9(Bus_7), .I_10(Bus_6), .I_11(Bus_5), .I_12(Bus_4), .I_13(Bus_3), .I_14(Bus_2),
    .I_15(Bus_1), .I_16(Bus_0), .nEnOut(nmain_bus____MAR), .O(pc_adder_1_o15), .O_2(pc_adder_1_o14),
    .O_3(pc_adder_1_o13), .O_4(pc_adder_1_o12), .O_5(pc_adder_1_o11), .O_6(pc_adder_1_o10),
    .O_7(pc_adder_1_o9), .O_8(pc_adder_1_o8), .O_9(pc_adder_1_o7), .O_10(pc_adder_1_o6),
    .O_11(pc_adder_1_o5), .O_12(pc_adder_1_o4), .O_13(pc_adder_1_o3), .O_14(pc_adder_1_o2),
    .O_15(pc_adder_1_o1), .O_16(pc_adder_1_o0));
  Row_of_transistors row_of_transistors_4 (
    .I(reg_2_o0[0]), .I_2(reg_2_o0[1]), .I_3(reg_2_o0[2]), .I_4(reg_2_o0[3]), .I_5(reg_2_o0[4]),
    .I_6(reg_2_o0[5]), .I_7(reg_2_o0[6]), .I_8(reg_2_o0[7]), .I_9(reg_2_o0[8]), .I_10(reg_2_o0[9]),
    .I_11(reg_2_o0[10]), .I_12(reg_2_o0[11]), .I_13(reg_2_o0[12]), .I_14(reg_2_o0[13]), .I_15(reg_2_o0[14]),
    .I_16(reg_2_o0[15]), .nEnOut(nMAR____main_bus), .O(Bus_0), .O_2(Bus_1), .O_3(Bus_2), .O_4(Bus_3),
    .O_5(Bus_4), .O_6(Bus_5), .O_7(Bus_6), .O_8(Bus_7), .O_9(Bus_8), .O_10(Bus_9), .O_11(Bus_10),
    .O_12(Bus_11), .O_13(Bus_12), .O_14(Bus_13), .O_15(Bus_14), .O_16(Bus_15));
  Row_of_transistors row_of_transistors_5 (
    .I(MANIAC_IN_15), .I_2(MANIAC_IN_14), .I_3(MANIAC_IN_13), .I_4(MANIAC_IN_12), .I_5(MANIAC_IN_11),
    .I_6(MANIAC_IN_10), .I_7(MANIAC_IN_9), .I_8(MANIAC_IN_8), .I_9(MANIAC_IN_7), .I_10(MANIAC_IN_6),
    .I_11(MANIAC_IN_5), .I_12(MANIAC_IN_4), .I_13(MANIAC_IN_3), .I_14(MANIAC_IN_2), .I_15(MANIAC_IN_1),
    .I_16(MANIAC_IN_0), .nEnOut(nenINPUT0), .O(Bus_15), .O_2(Bus_14), .O_3(Bus_13), .O_4(Bus_12),
    .O_5(Bus_11), .O_6(Bus_10), .O_7(Bus_9), .O_8(Bus_8), .O_9(Bus_7), .O_10(Bus_6), .O_11(Bus_5),
    .O_12(Bus_4), .O_13(Bus_3), .O_14(Bus_2), .O_15(Bus_1), .O_16(Bus_0));
  Row_of_transistors row_of_transistors_6 (
    .I(MANIAC_IN_15_2), .I_2(MANIAC_IN_14_2), .I_3(MANIAC_IN_13_2), .I_4(MANIAC_IN_12_2),
    .I_5(MANIAC_IN_11_2), .I_6(MANIAC_IN_10_2), .I_7(MANIAC_IN_9_2), .I_8(MANIAC_IN_8_2),
    .I_9(MANIAC_IN_7_2), .I_10(MANIAC_IN_6_2), .I_11(MANIAC_IN_5_2), .I_12(MANIAC_IN_4_2),
    .I_13(MANIAC_IN_3_2), .I_14(MANIAC_IN_2_2), .I_15(MANIAC_IN_1_2), .I_16(MANIAC_IN_0_2),
    .nEnOut(nenINPUT1), .O(Bus_15), .O_2(Bus_14), .O_3(Bus_13), .O_4(Bus_12), .O_5(Bus_11), .O_6(Bus_10),
    .O_7(Bus_9), .O_8(Bus_8), .O_9(Bus_7), .O_10(Bus_6), .O_11(Bus_5), .O_12(Bus_4), .O_13(Bus_3),
    .O_14(Bus_2), .O_15(Bus_1), .O_16(Bus_0));
  Row_of_transistors row_of_transistors_7 (
    .I(MANIAC_IN_15_3), .I_2(MANIAC_IN_14_3), .I_3(MANIAC_IN_13_3), .I_4(MANIAC_IN_12_3),
    .I_5(MANIAC_IN_11_3), .I_6(MANIAC_IN_10_3), .I_7(MANIAC_IN_9_3), .I_8(MANIAC_IN_8_3),
    .I_9(MANIAC_IN_7_3), .I_10(MANIAC_IN_6_3), .I_11(MANIAC_IN_5_3), .I_12(MANIAC_IN_4_3),
    .I_13(MANIAC_IN_3_3), .I_14(MANIAC_IN_2_3), .I_15(MANIAC_IN_1_3), .I_16(MANIAC_IN_0_3),
    .nEnOut(nenINPUT2), .O(Bus_15), .O_2(Bus_14), .O_3(Bus_13), .O_4(Bus_12), .O_5(Bus_11), .O_6(Bus_10),
    .O_7(Bus_9), .O_8(Bus_8), .O_9(Bus_7), .O_10(Bus_6), .O_11(Bus_5), .O_12(Bus_4), .O_13(Bus_3),
    .O_14(Bus_2), .O_15(Bus_1), .O_16(Bus_0));
  Row_of_transistors row_of_transistors_8 (
    .I(MANIAC_IN_15_4), .I_2(MANIAC_IN_14_4), .I_3(MANIAC_IN_13_4), .I_4(MANIAC_IN_12_4),
    .I_5(MANIAC_IN_11_4), .I_6(MANIAC_IN_10_4), .I_7(MANIAC_IN_9_4), .I_8(MANIAC_IN_8_4),
    .I_9(MANIAC_IN_7_4), .I_10(MANIAC_IN_6_4), .I_11(MANIAC_IN_5_4), .I_12(MANIAC_IN_4_4),
    .I_13(MANIAC_IN_3_4), .I_14(MANIAC_IN_2_4), .I_15(MANIAC_IN_1_4), .I_16(MANIAC_IN_0_4),
    .nEnOut(nenINPUT3), .O(Bus_15), .O_2(Bus_14), .O_3(Bus_13), .O_4(Bus_12), .O_5(Bus_11), .O_6(Bus_10),
    .O_7(Bus_9), .O_8(Bus_8), .O_9(Bus_7), .O_10(Bus_6), .O_11(Bus_5), .O_12(Bus_4), .O_13(Bus_3),
    .O_14(Bus_2), .O_15(Bus_1), .O_16(Bus_0));
  Buff_short_one_protection buff_short_one_protection_2 (.I(A0load), .O(buff_short_one_protection_2_o));
  reg_experimental u_A0 (
    .I15(Bus_15), .I14(Bus_14), .I13(Bus_13), .I12(Bus_12), .I11(Bus_11), .I10(Bus_10), .I9(Bus_9),
    .I8(Bus_8), .I7(Bus_7), .I6(Bus_6), .I5(Bus_5), .I4(Bus_4), .I3(Bus_3), .I2(Bus_2), .I1(Bus_1),
    .I0(Bus_0), .LM(buff_short_one_protection_2_o), .CLK(CLK), .nenOut(buff_short_zero_protection_1_out),
    .OB15(A0_ob15), .OB14(A0_ob14), .OB13(A0_ob13), .OB12(A0_ob12), .OB11(A0_ob11), .OB10(A0_ob10),
    .OB9(A0_ob9), .OB8(A0_ob8), .OB7(A0_ob7), .OB6(A0_ob6), .OB5(A0_ob5), .OB4(A0_ob4), .OB3(A0_ob3),
    .OB2(A0_ob2), .OB1(A0_ob1), .OB0(A0_ob0));
  Buff_short_zero_protection buff_short_zero_protection_1 (.In(nenA0out), .Out(buff_short_zero_protection_1_out));
  Buff_short_one_protection buff_short_one_protection_3 (.I(A1load), .O(buff_short_one_protection_3_o));
  reg_experimental u_A1 (
    .I15(Bus_15), .I14(Bus_14), .I13(Bus_13), .I12(Bus_12), .I11(Bus_11), .I10(Bus_10), .I9(Bus_9),
    .I8(Bus_8), .I7(Bus_7), .I6(Bus_6), .I5(Bus_5), .I4(Bus_4), .I3(Bus_3), .I2(Bus_2), .I1(Bus_1),
    .I0(Bus_0), .LM(buff_short_one_protection_3_o), .CLK(CLK), .nenOut(buff_short_zero_protection_2_out),
    .OB15(A0_ob15), .OB14(A0_ob14), .OB13(A0_ob13), .OB12(A0_ob12), .OB11(A0_ob11), .OB10(A0_ob10),
    .OB9(A0_ob9), .OB8(A0_ob8), .OB7(A0_ob7), .OB6(A0_ob6), .OB5(A0_ob5), .OB4(A0_ob4), .OB3(A0_ob3),
    .OB2(A0_ob2), .OB1(A0_ob1), .OB0(A0_ob0));
  Buff_short_zero_protection buff_short_zero_protection_2 (.In(nenA1out), .Out(buff_short_zero_protection_2_out));
  Buff_short_one_protection buff_short_one_protection_4 (.I(A2load), .O(buff_short_one_protection_4_o));
  reg_experimental u_A2 (
    .I15(Bus_15), .I14(Bus_14), .I13(Bus_13), .I12(Bus_12), .I11(Bus_11), .I10(Bus_10), .I9(Bus_9),
    .I8(Bus_8), .I7(Bus_7), .I6(Bus_6), .I5(Bus_5), .I4(Bus_4), .I3(Bus_3), .I2(Bus_2), .I1(Bus_1),
    .I0(Bus_0), .LM(buff_short_one_protection_4_o), .CLK(CLK), .nenOut(buff_short_zero_protection_3_out),
    .OB15(A0_ob15), .OB14(A0_ob14), .OB13(A0_ob13), .OB12(A0_ob12), .OB11(A0_ob11), .OB10(A0_ob10),
    .OB9(A0_ob9), .OB8(A0_ob8), .OB7(A0_ob7), .OB6(A0_ob6), .OB5(A0_ob5), .OB4(A0_ob4), .OB3(A0_ob3),
    .OB2(A0_ob2), .OB1(A0_ob1), .OB0(A0_ob0));
  Buff_short_zero_protection buff_short_zero_protection_3 (.In(nenA2out), .Out(buff_short_zero_protection_3_out));
  Buff_short_one_protection buff_short_one_protection_5 (.I(A3load), .O(buff_short_one_protection_5_o));
  reg_experimental u_A3 (
    .I15(Bus_15), .I14(Bus_14), .I13(Bus_13), .I12(Bus_12), .I11(Bus_11), .I10(Bus_10), .I9(Bus_9),
    .I8(Bus_8), .I7(Bus_7), .I6(Bus_6), .I5(Bus_5), .I4(Bus_4), .I3(Bus_3), .I2(Bus_2), .I1(Bus_1),
    .I0(Bus_0), .LM(buff_short_one_protection_5_o), .CLK(CLK), .nenOut(buff_short_zero_protection_4_out),
    .OB15(A0_ob15), .OB14(A0_ob14), .OB13(A0_ob13), .OB12(A0_ob12), .OB11(A0_ob11), .OB10(A0_ob10),
    .OB9(A0_ob9), .OB8(A0_ob8), .OB7(A0_ob7), .OB6(A0_ob6), .OB5(A0_ob5), .OB4(A0_ob4), .OB3(A0_ob3),
    .OB2(A0_ob2), .OB1(A0_ob1), .OB0(A0_ob0));
  Buff_short_zero_protection buff_short_zero_protection_4 (.In(nenA3out), .Out(buff_short_zero_protection_4_out));
  Row_of_transistors row_of_transistors_9 (
    .I(A0_ob0), .I_2(A0_ob1), .I_3(A0_ob2), .I_4(A0_ob3), .I_5(A0_ob4), .I_6(A0_ob5), .I_7(A0_ob6),
    .I_8(A0_ob7), .I_9(A0_ob8), .I_10(A0_ob9), .I_11(A0_ob10), .I_12(A0_ob11), .I_13(A0_ob12),
    .I_14(A0_ob13), .I_15(A0_ob14), .I_16(A0_ob15), .nEnOut(nA_bus____Main_bus), .O(Bus_0), .O_2(Bus_1),
    .O_3(Bus_2), .O_4(Bus_3), .O_5(Bus_4), .O_6(Bus_5), .O_7(Bus_6), .O_8(Bus_7), .O_9(Bus_8), .O_10(Bus_9),
    .O_11(Bus_10), .O_12(Bus_11), .O_13(Bus_12), .O_14(Bus_13), .O_15(Bus_14), .O_16(Bus_15));
  Row_of_transistors row_of_transistors_10 (
    .I(B0_ob0), .I_2(B0_ob1), .I_3(B0_ob2), .I_4(B0_ob3), .I_5(B0_ob4), .I_6(B0_ob5), .I_7(B0_ob6),
    .I_8(B0_ob7), .I_9(B0_ob8), .I_10(B0_ob9), .I_11(B0_ob10), .I_12(B0_ob11), .I_13(B0_ob12),
    .I_14(B0_ob13), .I_15(B0_ob14), .I_16(B0_ob15), .nEnOut(nB_bus____Main_bus), .O(Bus_0), .O_2(Bus_1),
    .O_3(Bus_2), .O_4(Bus_3), .O_5(Bus_4), .O_6(Bus_5), .O_7(Bus_6), .O_8(Bus_7), .O_9(Bus_8), .O_10(Bus_9),
    .O_11(Bus_10), .O_12(Bus_11), .O_13(Bus_12), .O_14(Bus_13), .O_15(Bus_14), .O_16(Bus_15));
  Buff_short_one_protection buff_short_one_protection_6 (.I(B0load), .O(buff_short_one_protection_6_o));
  Buff_short_zero_protection buff_short_zero_protection_5 (.In(nenB0out), .Out(buff_short_zero_protection_5_out));
  reg_experimental B0 (
    .I15(Bus_15), .I14(Bus_14), .I13(Bus_13), .I12(Bus_12), .I11(Bus_11), .I10(Bus_10), .I9(Bus_9),
    .I8(Bus_8), .I7(Bus_7), .I6(Bus_6), .I5(Bus_5), .I4(Bus_4), .I3(Bus_3), .I2(Bus_2), .I1(Bus_1),
    .I0(Bus_0), .LM(buff_short_one_protection_6_o), .CLK(CLK), .nenOut(buff_short_zero_protection_5_out),
    .OB15(B0_ob15), .OB14(B0_ob14), .OB13(B0_ob13), .OB12(B0_ob12), .OB11(B0_ob11), .OB10(B0_ob10),
    .OB9(B0_ob9), .OB8(B0_ob8), .OB7(B0_ob7), .OB6(B0_ob6), .OB5(B0_ob5), .OB4(B0_ob4), .OB3(B0_ob3),
    .OB2(B0_ob2), .OB1(B0_ob1), .OB0(B0_ob0));
  Buff_short_one_protection buff_short_one_protection_7 (.I(B1load), .O(buff_short_one_protection_7_o));
  Buff_short_zero_protection buff_short_zero_protection_6 (.In(nenB1out), .Out(buff_short_zero_protection_6_out));
  reg_experimental B1 (
    .I15(Bus_15), .I14(Bus_14), .I13(Bus_13), .I12(Bus_12), .I11(Bus_11), .I10(Bus_10), .I9(Bus_9),
    .I8(Bus_8), .I7(Bus_7), .I6(Bus_6), .I5(Bus_5), .I4(Bus_4), .I3(Bus_3), .I2(Bus_2), .I1(Bus_1),
    .I0(Bus_0), .LM(buff_short_one_protection_7_o), .CLK(CLK), .nenOut(buff_short_zero_protection_6_out),
    .OB15(B0_ob15), .OB14(B0_ob14), .OB13(B0_ob13), .OB12(B0_ob12), .OB11(B0_ob11), .OB10(B0_ob10),
    .OB9(B0_ob9), .OB8(B0_ob8), .OB7(B0_ob7), .OB6(B0_ob6), .OB5(B0_ob5), .OB4(B0_ob4), .OB3(B0_ob3),
    .OB2(B0_ob2), .OB1(B0_ob1), .OB0(B0_ob0));
  Buff_short_one_protection buff_short_one_protection_8 (.I(B2load), .O(buff_short_one_protection_8_o));
  Buff_short_zero_protection buff_short_zero_protection_7 (.In(nenB2out), .Out(buff_short_zero_protection_7_out));
  reg_experimental B2 (
    .I15(Bus_15), .I14(Bus_14), .I13(Bus_13), .I12(Bus_12), .I11(Bus_11), .I10(Bus_10), .I9(Bus_9),
    .I8(Bus_8), .I7(Bus_7), .I6(Bus_6), .I5(Bus_5), .I4(Bus_4), .I3(Bus_3), .I2(Bus_2), .I1(Bus_1),
    .I0(Bus_0), .LM(buff_short_one_protection_8_o), .CLK(CLK), .nenOut(buff_short_zero_protection_7_out),
    .OB15(B0_ob15), .OB14(B0_ob14), .OB13(B0_ob13), .OB12(B0_ob12), .OB11(B0_ob11), .OB10(B0_ob10),
    .OB9(B0_ob9), .OB8(B0_ob8), .OB7(B0_ob7), .OB6(B0_ob6), .OB5(B0_ob5), .OB4(B0_ob4), .OB3(B0_ob3),
    .OB2(B0_ob2), .OB1(B0_ob1), .OB0(B0_ob0));
  Buff_short_one_protection buff_short_one_protection_9 (.I(B3load), .O(buff_short_one_protection_9_o));
  reg_experimental B3 (
    .I15(Bus_15), .I14(Bus_14), .I13(Bus_13), .I12(Bus_12), .I11(Bus_11), .I10(Bus_10), .I9(Bus_9),
    .I8(Bus_8), .I7(Bus_7), .I6(Bus_6), .I5(Bus_5), .I4(Bus_4), .I3(Bus_3), .I2(Bus_2), .I1(Bus_1),
    .I0(Bus_0), .LM(buff_short_one_protection_9_o), .CLK(CLK), .nenOut(buff_short_zero_protection_8_out),
    .OB15(B0_ob15), .OB14(B0_ob14), .OB13(B0_ob13), .OB12(B0_ob12), .OB11(B0_ob11), .OB10(B0_ob10),
    .OB9(B0_ob9), .OB8(B0_ob8), .OB7(B0_ob7), .OB6(B0_ob6), .OB5(B0_ob5), .OB4(B0_ob4), .OB3(B0_ob3),
    .OB2(B0_ob2), .OB1(B0_ob1), .OB0(B0_ob0));
  Buff_short_zero_protection buff_short_zero_protection_8 (.In(nenB3out), .Out(buff_short_zero_protection_8_out));
  Buff_short_one_protection buff_short_one_protection_10 (.I(G0load), .O(buff_short_one_protection_10_o));
  Buff_short_zero_protection buff_short_zero_protection_9 (.In(nenG0out), .Out(buff_short_zero_protection_9_out));
  reg_experimental G0 (
    .I15(Bus_15), .I14(Bus_14), .I13(Bus_13), .I12(Bus_12), .I11(Bus_11), .I10(Bus_10), .I9(Bus_9),
    .I8(Bus_8), .I7(Bus_7), .I6(Bus_6), .I5(Bus_5), .I4(Bus_4), .I3(Bus_3), .I2(Bus_2), .I1(Bus_1),
    .I0(Bus_0), .LM(buff_short_one_protection_10_o), .CLK(CLK), .nenOut(buff_short_zero_protection_9_out),
    .OB15(Bus_15), .OB14(Bus_14), .OB13(Bus_13), .OB12(Bus_12), .OB11(Bus_11), .OB10(Bus_10), .OB9(Bus_9),
    .OB8(Bus_8), .OB7(Bus_7), .OB6(Bus_6), .OB5(Bus_5), .OB4(Bus_4), .OB3(Bus_3), .OB2(Bus_2), .OB1(Bus_1),
    .OB0(Bus_0));
  Buff_short_one_protection buff_short_one_protection_11 (.I(G1load), .O(buff_short_one_protection_11_o));
  reg_experimental G1 (
    .I15(Bus_15), .I14(Bus_14), .I13(Bus_13), .I12(Bus_12), .I11(Bus_11), .I10(Bus_10), .I9(Bus_9),
    .I8(Bus_8), .I7(Bus_7), .I6(Bus_6), .I5(Bus_5), .I4(Bus_4), .I3(Bus_3), .I2(Bus_2), .I1(Bus_1),
    .I0(Bus_0), .LM(buff_short_one_protection_11_o), .CLK(CLK), .nenOut(buff_short_zero_protection_10_out),
    .OB15(Bus_15), .OB14(Bus_14), .OB13(Bus_13), .OB12(Bus_12), .OB11(Bus_11), .OB10(Bus_10), .OB9(Bus_9),
    .OB8(Bus_8), .OB7(Bus_7), .OB6(Bus_6), .OB5(Bus_5), .OB4(Bus_4), .OB3(Bus_3), .OB2(Bus_2), .OB1(Bus_1),
    .OB0(Bus_0));
  Buff_short_zero_protection buff_short_zero_protection_10 (.In(nenG1out), .Out(buff_short_zero_protection_10_out));
  _16bit_74193 u_16bit_74193_4 (
    .I0(Bus_0), .I1(Bus_1), .I2(Bus_2), .I3(Bus_3), .I4(Bus_4), .I5(Bus_5), .I6(Bus_6), .I7(Bus_7),
    .I8(Bus_8), .I9(Bus_9), .I10(Bus_10), .I11(Bus_11), .I12(Bus_12), .I13(Bus_13), .I14(Bus_14),
    .I15(Bus_15), .CLR(Reset), .DOWN(buff_short_one_protection_12_o), .UP(buff_short_one_protection_13_o),
    .nLOAD(buff_short_zero_protection_11_out), .enAout(buff_short_one_protection_14_o), .spOVF(spOVF),
    .OA0(Bus_0), .OA1(Bus_1), .OA2(Bus_2), .OA3(Bus_3), .OA4(Bus_4), .OA5(Bus_5), .OA6(Bus_6), .OA7(Bus_7),
    .OA8(Bus_8), .OA9(Bus_9), .OA10(Bus_10), .OA11(Bus_11), .OA12(Bus_12), .OA13(Bus_13), .OA14(Bus_14),
    .OA15(Bus_15));
  not not_27 (not_27_out, Reset);
  not not_28 (not_28_out, Reset);
  not not_29 (not_29_out, Reset);
  not not_30 (not_30_out, Reset);
  and and_17 (and_17_out, INR0_CLF, not_27_out);
  not not_31 (not_31_out, MANIAC_INPUT0___data_ready);
  Interrupt_Pin interrupt_pin_5 (.nsetINT(not_31_out), .Out(INPUT_0_ready_INDICATOR), .nclrINT(and_17_out));
  and and_18 (and_18_out, INR1_CLF, not_28_out);
  not not_32 (not_32_out, MANIAC_INPUT1___data_ready);
  Interrupt_Pin interrupt_pin_6 (.nsetINT(not_32_out), .Out(INPUT_1_ready_INDICATOR), .nclrINT(and_18_out));
  and and_19 (and_19_out, INR2_CLF, not_29_out);
  not not_33 (not_33_out, MANIAC_INPUT2___data_ready);
  Interrupt_Pin interrupt_pin_7 (.nsetINT(not_33_out), .Out(INPUT_2_ready_INDICATOR), .nclrINT(and_19_out));
  and and_20 (and_20_out, INR3_CLF, not_30_out);
  Interrupt_Pin interrupt_pin_8 (.nsetINT(not_34_out), .Out(INPUT_3_ready_INDICATOR), .nclrINT(and_20_out));
  not not_34 (not_34_out, MANIAC_INPUT3___data_ready);
  Buff_short_one_protection buff_short_one_protection_12 (.I(SPdown), .O(buff_short_one_protection_12_o));
  Buff_short_one_protection buff_short_one_protection_13 (.I(SPup), .O(buff_short_one_protection_13_o));
  Buff_short_zero_protection buff_short_zero_protection_11 (.In(nloadSP), .Out(buff_short_zero_protection_11_out));
  Buff_short_one_protection buff_short_one_protection_14 (.I(enSPout), .O(buff_short_one_protection_14_o));
  ALU alu_1 (
    .O0(Bus_0), .O1(Bus_1), .O2(Bus_2), .O3(Bus_3), .O4(Bus_4), .O5(Bus_5), .O6(Bus_6), .O7(Bus_7),
    .O8(Bus_8), .O9(Bus_9), .O10(Bus_10), .O11(Bus_11), .O12(Bus_12), .O13(Bus_13), .O14(Bus_14),
    .O15(Bus_15), .A15(A0_ob15), .A14(A0_ob14), .A13(A0_ob13), .A12(A0_ob12), .A11(A0_ob11), .A10(A0_ob10),
    .A9(A0_ob9), .A8(A0_ob8), .A7(A0_ob7), .A6(A0_ob6), .A5(A0_ob5), .A4(A0_ob4), .A3(A0_ob3), .A2(A0_ob2),
    .A1(A0_ob1), .A0(A0_ob0), .R15(B0_ob15), .R14(B0_ob14), .R13(B0_ob13), .R12(B0_ob12), .R11(B0_ob11),
    .R1O(B0_ob10), .R9(B0_ob9), .R8(B0_ob8), .R7(B0_ob7), .R6(B0_ob6), .R5(B0_ob5), .R4(B0_ob4), .R3(B0_ob3),
    .R2(B0_ob2), .R1(B0_ob1), .RO(B0_ob0), .NOT(NOT), .CRFI(flag_reg_1_cr_2), .CRFO(alu_1_crfo),
    .PRFO(alu_1_prfo), .OVF(alu_1_ovf), .MFO(alu_1_mfo), .ZRF(alu_1_zrf), .Address_0(ALUadr0),
    .Address_1(ALUadr1), .Address_2(ALUadr2), .Address_3(ALUadr3), .enOut(enALUout));
  Zero_Reg zero_reg_1 (
    .out_2(Bus_0), .out_3(Bus_1), .out_4(Bus_2), .out_5(Bus_3), .out_6(Bus_4), .out_7(Bus_5), .out_8(Bus_6),
    .out_9(Bus_7), .out_10(Bus_8), .out_11(Bus_9), .out_12(Bus_10), .out_13(Bus_11), .out_14(Bus_12),
    .out_15(Bus_13), .out_16(Bus_14), .out_17(Bus_15), .nZerRegEn(nenR0));
  Row_of_transistors row_of_transistors_11 (
    .I(flag_reg_1_zrout), .I_2(flag_reg_1_mout), .I_3(flag_reg_1_ovfout), .I_4(flag_reg_1_prout),
    .I_5(flag_reg_1_crout), .I_6(flag_reg_1_nuout), .I_7(flag_reg_1_nuout_2), .I_8(flag_reg_1_nuout_3),
    .I_9(OUTR0), .I_10(OUTR1), .I_11(OUTR2), .I_12(OUTR3), .I_13(INPUT_0_ready_INDICATOR),
    .I_14(INPUT_1_ready_INDICATOR), .I_15(INPUT_2_ready_INDICATOR), .I_16(INPUT_3_ready_INDICATOR),
    .nEnOut(nenFlagREG), .O(A0_ob0), .O_2(A0_ob1), .O_3(A0_ob2), .O_4(A0_ob3), .O_5(A0_ob4), .O_6(A0_ob5),
    .O_7(A0_ob6), .O_8(A0_ob7), .O_9(A0_ob8), .O_10(A0_ob9), .O_11(A0_ob10), .O_12(A0_ob11), .O_13(A0_ob12),
    .O_14(A0_ob13), .O_15(A0_ob14), .O_16(A0_ob15));
  FLAG_Reg flag_reg_1 (
    .CLF(CLF), .STF(STF), .ID0(FLadr0), .ID1(FLadr1), .ID2(FLadr2), .ID3(FLadr3), .ZR(alu_1_zrf),
    .M(alu_1_mfo), .OVF(alu_1_ovf), .PR(alu_1_prfo), .CR(alu_1_crfo), .NU(1'b0), .NU_2(1'b0), .NU_3(1'b0),
    .ZRout(flag_reg_1_zrout), .Mout(flag_reg_1_mout), .OVFout(flag_reg_1_ovfout), .PRout(flag_reg_1_prout),
    .CRout(flag_reg_1_crout), .NUout(flag_reg_1_nuout), .NUout_2(flag_reg_1_nuout_2),
    .NUout_3(flag_reg_1_nuout_3), .ldFR(ldALUflagREG), .CR_2(flag_reg_1_cr_2), .CLR(Reset), .CLK(CLK),
    .OUTR0(OUTR0_STF), .OUTR1(OUTR1_STF), .OUTR2(OUTR2_STF), .OUTR3(OUTR3_STF), .INR0(INR0_CLF),
    .INR1(INR1_CLF), .INR2(INR2_CLF), .INR3(INR3_CLF));
  Multiplexer #(.select(4)) multiplexer_5 (
    .in0(flag_reg_1_zrout), .in1(flag_reg_1_mout), .in2(flag_reg_1_ovfout), .in3(flag_reg_1_prout),
    .in4(flag_reg_1_crout), .in5(flag_reg_1_nuout), .in6(flag_reg_1_nuout_2), .in7(flag_reg_1_nuout_3),
    .in8(OUTR0), .in9(OUTR1), .in10(OUTR2), .in11(OUTR3), .in12(INPUT_0_ready_INDICATOR),
    .in13(INPUT_1_ready_INDICATOR), .in14(INPUT_2_ready_INDICATOR), .in15(INPUT_3_ready_INDICATOR),
    .out(Flag_state), .sel({FLadr0, FLadr1, FLadr2, FLadr3}));  // open: en

  assign out_114 = INPUT_0_ready_INDICATOR;
  assign out_115 = INPUT_1_ready_INDICATOR;
  assign out_116 = INPUT_2_ready_INDICATOR;
  assign out_117 = INPUT_3_ready_INDICATOR;

  // Other names for the same wires on the sheet: INR0 = INPUT_0_ready_INDICATOR; INR1 = INPUT_1_ready_INDICATOR;
  //   INR2 = INPUT_2_ready_INDICATOR; INR3 = INPUT_3_ready_INDICATOR

  // Notes on the sheet:
  //   Q
  //   T
  //   contents of rom_1 (hex, n*v repeats v):
  //   1024*0 7 a d 10 13 16 19 1c 1f 22 25 28 4*886 2b 2e 31 34 37 3a 3d 40 43 46 49 4c 4*886 4f 52 55 58
  //   5b 5e 61 64 67 6a 6d 70 4*886 73 76 79 7c 7f 82 85 88 8b 8e 91 94 4*886 97 9a 9d a0 a3 a6 a9 ac af
  //   b2 b5 b8 4*886 bb be c1 c4 c7 ca cd d0 d3 d6 d9 dc 4*886 df e2 e5 e8 eb ee f1 f4 f7 fa fd 100 4*886
  //   103 106 109 10c 10f 112 115 118 11b 11e 121 124 4*886 127 12a 12d 130 133 136 139 13c 13f 142 145
  //   148 4*886 14b 14e 151 154 157 15a 15d 160 163 166 169 16c 4*886 16f 172 175 178 17b 17e 181 184 187
  //   18a 18d 190 4*886 193 196 199 19c 19f 1a2 1a5 1a8 1ab 1ae 1b1 1b4 4*886 1b7 1ba 1bd 1c0 1c3 1c6 1c9
  //   1cc 1cf 1d2 1d5 1d8 4*886 1db 1de 1e1 1e4 1e7 1ea 1ed 1f0 1f3 1f6 1f9 1fc 4*886 1ff 202 205 208 20b
  //   20e 211 214 217 21a 21d 220 4*886 223 226 229 22c 22f 232 235 238 23b 23e 241 244 4*886 7 a d 10 13
  //   16 19 1c 1f 22 25 28 4*886 2b 2e 31 34 37 3a 3d 40 43 46 49 4c 4*886 4f 52 55 58 5b 5e 61 64 67 6a
  //   6d 70 4*886 73 76 79 7c 7f 82 85 88 8b 8e 91 94 4*886 97 9a 9d a0 a3 a6 a9 ac af b2 b5 b8 4*886 bb
  //   be c1 c4 c7 ca cd d0 d3 d6 d9 dc 4*886 df e2 e5 e8 eb ee f1 f4 f7 fa fd 100 4*886 103 106 109 10c
  //   10f 112 115 118 11b 11e 121 124 4*886 127 12a 12d 130 133 136 139 13c 13f 142 145 148 4*886 14b 14e
  //   151 154 157 15a 15d 160 163 166 169 16c 4*886 16f 172 175 178 17b 17e 181 184 187 18a 18d 190 4*886
  //   193 196 199 19c 19f 1a2 1a5 1a8 1ab 1ae 1b1 1b4 4*886 1b7 1ba 1bd 1c0 1c3 1c6 1c9 1cc 1cf 1d2 1d5
  //   1d8 4*886 1db 1de 1e1 1e4 1e7 1ea 1ed 1f0 1f3 1f6 1f9 1fc 4*886 1ff 202 205 208 20b 20e 211 214 217
  //   21a 21d 220 4*886 223 226 229 22c 22f 232 235 238 23b 23e 241 244 4*886 7 a d 10 13 16 19 1c 1f 22
  //   25 28 4*886 2b 2e 31 34 37 3a 3d 40 43 46 49 4c 4*886 4f 52 55 58 5b 5e 61 64 67 6a 6d 70 4*886 73
  //   76 79 7c 7f 82 85 88 8b 8e 91 94 4*886 97 9a 9d a0 a3 a6 a9 ac af b2 b5 b8 4*886 bb be c1 c4 c7 ca
  //   cd d0 d3 d6 d9 dc 4*886 df e2 e5 e8 eb ee f1 f4 f7 fa fd 100 4*886 103 106 109 10c 10f 112 115 118
  //   11b 11e 121 124 4*886 127 12a 12d 130 133 136 139 13c 13f 142 145 148 4*886 14b 14e 151 154 157 15a
  //   15d 160 163 166 169 16c 4*886 16f 172 175 178 17b 17e 181 184 187 18a 18d 190 4*886 193 196 199 19c
  //   19f 1a2 1a5 1a8 1ab 1ae 1b1 1b4 4*886 1b7 1ba 1bd 1c0 1c3 1c6 1c9 1cc 1cf 1d2 1d5 1d8 4*886 1db 1de
  //   1e1 1e4 1e7 1ea 1ed 1f0 1f3 1f6 1f9 1fc 4*886 1ff 202 205 208 20b 20e 211 214 217 21a 21d 220 4*886
  //   223 226 229 22c 22f 232 235 238 23b 23e 241 244 4*886 7 a d 10 13 16 19 1c 1f 22 25 28 4*886 2b 2e
  //   31 34 37 3a 3d 40 43 46 49 4c 4*886 4f 52 55 58 5b 5e 61 64 67 6a 6d 70 4*886 73 76 79 7c 7f 82 85
  //   88 8b 8e 91 94 4*886 97 9a 9d a0 a3 a6 a9 ac af b2 b5 b8 4*886 bb be c1 c4 c7 ca cd d0 d3 d6 d9 dc
  //   4*886 df e2 e5 e8 eb ee f1 f4 f7 fa fd 100 4*886 103 106 109 10c 10f 112 115 118 11b 11e 121 124
  //   4*886 127 12a 12d 130 133 136 139 13c 13f 142 145 148 4*886 14b 14e 151 154 157 15a 15d 160 163 166
  //   169 16c 4*886 16f 172 175 178 17b 17e 181 184 187 18a 18d 190 4*886 193 196 199 19c 19f 1a2 1a5 1a8
  //   1ab 1ae 1b1 1b4 4*886 1b7 1ba 1bd 1c0 1c3 1c6 1c9 1cc 1cf 1d2 1d5 1d8 4*886 1db 1de 1e1 1e4 1e7 1ea
  //   1ed 1f0 1f3 1f6 1f9 1fc 4*886 1ff 202 205 208 20b 20e 211 214 217 21a 21d 220 4*886 223 226 229 22c
  //   22f 232 235 238 23b 23e 241 244 4*886 7 a d 10 13 16 19 1c 1f 22 25 28 4*886 2b 2e 31 34 37 3a 3d 40
  //   43 46 49 4c 4*886 4f 52 55 58 5b 5e 61 64 67 6a 6d 70 4*886 73 76 79 7c 7f 82 85 88 8b 8e 91 94
  //   4*886 97 9a 9d a0 a3 a6 a9 ac af b2 b5 b8 4*886 bb be c1 c4 c7 ca cd d0 d3 d6 d9 dc 4*886 df e2 e5
  //   e8 eb ee f1 f4 f7 fa fd 100 4*886 103 106 109 10c 10f 112 115 118 11b 11e 121 124 4*886 127 12a 12d
  //   130 133 136 139 13c 13f 142 145 148 4*886 14b 14e 151 154 157 15a 15d 160 163 166 169 16c 4*886 16f
  //   172 175 178 17b 17e 181 184 187 18a 18d 190 4*886 193 196 199 19c 19f 1a2 1a5 1a8 1ab 1ae 1b1 1b4
  //   4*886 1b7 1ba 1bd 1c0 1c3 1c6 1c9 1cc 1cf 1d2 1d5 1d8 4*886 1db 1de 1e1 1e4 1e7 1ea 1ed 1f0 1f3 1f6
  //   1f9 1fc 4*886 1ff 202 205 208 20b 20e 211 214 217 21a 21d 220 4*886 223 226 229 22c 22f 232 235 238
  //   23b 23e 241 244 4*886 7 a d 10 13 16 19 1c 1f 22 25 28 4*886 2b 2e 31 34 37 3a 3d 40 43 46 49 4c
  //   4*886 4f 52 55 58 5b 5e 61 6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
  //   RISING
  //   dodać bufor
  //   contents of rom_2 (hex, n*v repeats v):
  //   aaaa5fc8 aaaa5fc6 aaaa58c7 aaaa5fc6 aaaa1ac0 aaaa5af2 aaaa5f82 a8a8dfc2 aaaa5af2 aaaa5f82 a8a9dfc2
  //   aaaa5af2 aaaa5f82 a8acdfc2 aaaa5af2 aaaa5f82 a8b8dfc2 aaaa5af2 aaaa5f82 a8e8dfc2 aaaa5af2 aaaa5f82
  //   a9a8dfc2 aaaa5af2 aaaa5f82 aca8dfc2 aaaa5af2 aaaa5f82 b8a8dfc2 aaaa5af2 aaaa5f82 e8a8dfc2 aaaa5af2
  //   aaaa5f82 a8a8dfc2 aaaa5af2 aaaa5f82 a8a8dfc2 aaaa5af2 aaaa5f82 a8a8dfc2 aaaa5af2 aaaa5f82 a2a8dfc2
  //   aaaa5af2 aaaa5f82 a2a9dfc2 aaaa5af2 aaaa5f82 a2acdfc2 aaaa5af2 aaaa5f82 a2b8dfc2 aaaa5af2 aaaa5f82
  //   a2e8dfc2 aaaa5af2 aaaa5f82 a3a8dfc2 aaaa5af2 aaaa5f82 a6a8dfc2 aaaa5af2 aaaa5f82 b2a8dfc2 aaaa5af2
  //   aaaa5f82 e2a8dfc2 aaaa5af2 aaaa5f82 a2a8dfc2 aaaa5af2 aaaa5f82 a2a8dfc2 aaaa5af2 aaaa5f82 a2a8dfc2
  //   aaaa5af2 aaaa5f82 8aa8dfc2 aaaa5af2 aaaa5f82 8aa9dfc2 aaaa5af2 aaaa5f82 8aacdfc2 aaaa5af2 aaaa5f82
  //   8ab8dfc2 aaaa5af2 aaaa5f82 8ae8dfc2 aaaa5af2 aaaa5f82 8ba8dfc2 aaaa5af2 aaaa5f82 8ea8dfc2 aaaa5af2
  //   aaaa5f82 9aa8dfc2 aaaa5af2 aaaa5f82 caa8dfc2 aaaa5af2 aaaa5f82 8aa8dfc2 aaaa5af2 aaaa5f82 8aa8dfc2
  //   aaaa5af2 aaaa5f82 8aa8dfc2 aaaa5af2 aaaa5f82 2aa8dfc2 aaaa5af2 aaaa5f82 2aa9dfc2 aaaa5af2 aaaa5f82
  //   2aacdfc2 aaaa5af2 aaaa5f82 2ab8dfc2 aaaa5af2 aaaa5f82 2ae8dfc2 aaaa5af2 aaaa5f82 2ba8dfc2 aaaa5af2
  //   aaaa5f82 2ea8dfc2 aaaa5af2 aaaa5f82 3aa8dfc2 aaaa5af2 aaaa5f82 6aa8dfc2 aaaa5af2 aaaa5f82 2aa8dfc2
  //   aaaa5af2 aaaa5f82 2aa8dfc2 aaaa5af2 aaaa5f82 2aa8dfc2 aaaa5af2 aaaa5f82 a8a2dfc2 aaaa5af2 aaaa5f82
  //   a8a3dfc2 aaaa5af2 aaaa5f82 a8a6dfc2 aaaa5af2 aaaa5f82 a8b2dfc2 aaaa5af2 aaaa5f82 a8e2dfc2 aaaa5af2
  //   aaaa5f82 a9a2dfc2 aaaa5af2 aaaa5f82 aca2dfc2 aaaa5af2 aaaa5f82 b8a2dfc2 aaaa5af2 aaaa5f82 e8a2dfc2
  //   aaaa5af2 aaaa5f82 a8a2dfc2 aaaa5af2 aaaa5f82 a8a2dfc2 aaaa5af2 aaaa5f82 a8a2dfc2 aaaa5af2 aaaa5f82
  //   a2a2dfc2 aaaa5af2 aaaa5f82 a2a3dfc2 aaaa5af2 aaaa5f82 a2a6dfc2 aaaa5af2 aaaa5f82 a2b2dfc2 aaaa5af2
  //   aaaa5f82 a2e2dfc2 aaaa5af2 aaaa5f82 a3a2dfc2 aaaa5af2 aaaa5f82 a6a2dfc2 aaaa5af2 aaaa5f82 b2a2dfc2
  //   aaaa5af2 aaaa5f82 e2a2dfc2 aaaa5af2 aaaa5f82 a2a2dfc2 aaaa5af2 aaaa5f82 a2a2dfc2 aaaa5af2 aaaa5f82
  //   a2a2dfc2 aaaa5af2 aaaa5f82 8aa2dfc2 aaaa5af2 aaaa5f82 8aa3dfc2 aaaa5af2 aaaa5f82 8aa6dfc2 aaaa5af2
  //   aaaa5f82 8ab2dfc2 aaaa5af2 aaaa5f82 8ae2dfc2 aaaa5af2 aaaa5f82 8ba2dfc2 aaaa5af2 aaaa5f82 8ea2dfc2
  //   aaaa5af2 aaaa5f82 9aa2dfc2 aaaa5af2 aaaa5f82 caa2dfc2 aaaa5af2 aaaa5f82 8aa2dfc2 aaaa5af2 aaaa5f82
  //   8aa2dfc2 aaaa5af2 aaaa5f82 8aa2dfc2 aaaa5af2 aaaa5f82 2aa2dfc2 aaaa5af2 aaaa5f82 2aa3dfc2 aaaa5af2
  //   aaaa5f82 2aa6dfc2 aaaa5af2 aaaa5f82 2ab2dfc2 aaaa5af2 aaaa5f82 2ae2dfc2 aaaa5af2 aaaa5f82 2ba2dfc2
  //   aaaa5af2 aaaa5f82 2ea2dfc2 aaaa5af2 aaaa5f82 3aa2dfc2 aaaa5af2 aaaa5f82 6aa2dfc2 aaaa5af2 aaaa5f82
  //   2aa2dfc2 aaaa5af2 aaaa5f82 2aa2dfc2 aaaa5af2 aaaa5f82 2aa2dfc2 aaaa5af2 aaaa5f82 a88adfc2 aaaa5af2
  //   aaaa5f82 a88bdfc2 aaaa5af2 aaaa5f82 a88edfc2 aaaa5af2 aaaa5f82 a89adfc2 aaaa5af2 aaaa5f82 a8cadfc2
  //   aaaa5af2 aaaa5f82 a98adfc2 aaaa5af2 aaaa5f82 ac8adfc2 aaaa5af2 aaaa5f82 b88adfc2 aaaa5af2 aaaa5f82
  //   e88adfc2 aaaa5af2 aaaa5f82 a88adfc2 aaaa5af2 aaaa5f82 a88adfc2 aaaa5af2 aaaa5f82 a88adfc2 aaaa5af2
  //   aaaa5f82 a28adfc2 aaaa5af2 aaaa5f82 a28bdfc2 aaaa5af2 aaaa5f82 a28edfc2 aaaa5af2 aaaa5f82 a29adfc2
  //   aaaa5af2 aaaa5f82 a2cadfc2 aaaa5af2 aaaa5f82 a38adfc2 aaaa5af2 aaaa5f82 a68adfc2 aaaa5af2 aaaa5f82
  //   b28adfc2 aaaa5af2 aaaa5f82 e28adfc2 aaaa5af2 aaaa5f82 a28adfc2 aaaa5af2 aaaa5f82 a28adfc2 aaaa5af2
  //   aaaa5f82 a28adfc2 aaaa5af2 aaaa5f82 8a8adfc2 aaaa5af2 aaaa5f82 8a8bdfc2 aaaa5af2 aaaa5f82 8a8edfc2
  //   aaaa5af2 aaaa5f82 8a9adfc2 aaaa5af2 aaaa5f82 8acadfc2 aaaa5af2 aaaa5f82 8b8adfc2 aaaa5af2 aaaa5f82
  //   8e8adfc2 aaaa5af2 aaaa5f82 9a8adfc2 aaaa5af2 aaaa5f82 ca8adfc2 aaaa5af2 aaaa5f82 8a8adfc2 aaaa5af2
  //   aaaa5f82 8a8adfc2 aaaa5af2 aaaa5f82 8a8adfc2 aaaa5af2 aaaa5f82 2a8adfc2 aaaa5af2 aaaa5f82 2a8bdfc2
  //   aaaa5af2 aaaa5f82 2a8edfc2 aaaa5af2 aaaa5f82 2a9adfc2 aaaa5af2 aaaa5f82 2acadfc2 aaaa5af2 aaaa5f82
  //   2b8adfc2 aaaa5af2 aaaa5f82 2e8adfc2 aaaa5af2 aaaa5f82 3a8adfc2 aaaa5af2 aaaa5f82 6a8adfc2 aaaa5af2
  //   aaaa5f82 2a8adfc2 aaaa5af2 aaaa5f82 2a8adfc2 aaaa5af2 aaaa5f82 2a8adfc2 aaaa5af2 aaaa5f82 a82adfc2
  //   aaaa5af2 aaaa5f82 a82bdfc2 aaaa5af2 aaaa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
  //   contents of rom_3 (hex, n*v repeats v):
  //   7*fc000d3a fc082d3a fc000d3a fc000d3a fc082d3a fc000d3a fc000d3a fc082d3a fc000d3a fc000d3a fc082d3a
  //   fc000d3a fc000d3a fc082d3a fc000d3a fc000d3a fc082d3a fc000d3a fc000d3a fc082d3a fc000d3a fc000d3a
  //   fc082d3a fc000d3a fc000d3a fc082d3a fc000d3a fc000d3a fc082d3b fc000d3a fc000d3a fc082d3e fc000d3a
  //   fc000d3a fc082c3a fc000d3a fc000d3a fc082d3a fc000d3a fc000d3a fc082d3a fc000d3a fc000d3a fc082d3a
  //   fc000d3a fc000d3a fc082d3a fc000d3a fc000d3a fc082d3a fc000d3a fc000d3a fc082d3a fc000d3a fc000d3a
  //   fc082d3a fc000d3a fc000d3a fc082d3a fc000d3a fc000d3a fc082d3a fc000d3a fc000d3a fc082d3b fc000d3a
  //   fc000d3a fc082d3e fc000d3a fc000d3a fc082c3a fc000d3a fc000d3a fc082d3a fc000d3a fc000d3a fc082d3a
  //   fc000d3a fc000d3a fc082d3a fc000d3a fc000d3a fc082d3a fc000d3a fc000d3a fc082d3a fc000d3a fc000d3a
  //   fc082d3a fc000d3a fc000d3a fc082d3a fc000d3a fc000d3a fc082d3a fc000d3a fc000d3a fc082d3a fc000d3a
  //   fc000d3a fc082d3b fc000d3a fc000d3a fc082d3e fc000d3a fc000d3a fc082c3a fc000d3a fc000d3a fc082d3a
  //   fc000d3a fc000d3a fc082d3a fc000d3a fc000d3a fc082d3a fc000d3a fc000d3a fc082d3a fc000d3a fc000d3a
  //   fc082d3a fc000d3a fc000d3a fc082d3a fc000d3a fc000d3a fc082d3a fc000d3a fc000d3a fc082d3a fc000d3a
  //   fc000d3a fc082d3a fc000d3a fc000d3a fc082d3b fc000d3a fc000d3a fc082d3e fc000d3a fc000d3a fc082c3a
  //   fc000d3a fc000d3a fc082d3a fc000d3a fc000d3a fc082d3a fc000d3a fc000d3a fc082d3a fc000d3a fc000d3a
  //   fc082d3a fc000d3a fc000d3a fc082d3a fc000d3a fc000d3a fc082d3a fc000d3a fc000d3a fc082d3a fc000d3a
  //   fc000d3a fc082d3a fc000d3a fc000d3a fc082d3a fc000d3a fc000d3a fc082d3b fc000d3a fc000d3a fc082d3e
  //   fc000d3a fc000d3a fc082c3a fc000d3a fc000d3a fc082d3a fc000d3a fc000d3a fc082d3a fc000d3a fc000d3a
  //   fc082d3a fc000d3a fc000d3a fc082d3a fc000d3a fc000d3a fc082d3a fc000d3a fc000d3a fc082d3a fc000d3a
  //   fc000d3a fc082d3a fc000d3a fc000d3a fc082d3a fc000d3a fc000d3a fc082d3a fc000d3a fc000d3a fc082d3b
  //   fc000d3a fc000d3a fc082d3e fc000d3a fc000d3a fc082c3a fc000d3a fc000d3a fc082d3a fc000d3a fc000d3a
  //   fc082d3a fc000d3a fc000d3a fc082d3a fc000d3a fc000d3a fc082d3a fc000d3a fc000d3a fc082d3a fc000d3a
  //   fc000d3a fc082d3a fc000d3a fc000d3a fc082d3a fc000d3a fc000d3a fc082d3a fc000d3a fc000d3a fc082d3a
  //   fc000d3a fc000d3a fc082d3b fc000d3a fc000d3a fc082d3e fc000d3a fc000d3a fc082c3a fc000d3a fc000d3a
  //   fc082d3a fc000d3a fc000d3a fc082d3a fc000d3a fc000d3a fc082d3a fc000d3a fc000d3a fc082d3a fc000d3a
  //   fc000d3a fc082d3a fc000d3a fc000d3a fc082d3a fc000d3a fc000d3a fc082d3a fc000d3a fc000d3a fc082d3a
  //   fc000d3a fc000d3a fc082d3a fc000d3a fc000d3a fc082d3b fc000d3a fc000d3a fc082d3e fc000d3a fc000d3a
  //   fc082c3a fc000d3a fc000d3a fc082d3a fc000d3a fc000d3a fc082d3a fc000d3a fc000d3a fc082d3a fc000d3a
  //   fc000d3a fc082d3a fc000d3a fc000d3a fc082d3a fc000d3a fc000d3a fc082d3a fc000d3a fc000d3a fc082d3a
  //   fc000d3a fc000d3a fc082d3a fc000d3a fc000d3a fc082d3a fc000d3a fc000d3a fc082d3b fc000d3a fc000d3a
  //   fc082d3e fc000d3a fc000d3a fc082c3a fc000d3a fc000d3a fc082d3a fc000d3a fc000d3a fc082d3a fc000d3a
  //   fc000d3a fc082d3a fc000d3a fc000d3a fc082d3a fc000d3a fc000d3a fc082d3a fc000d3a fc000d3a fc082d3a
  //   fc000d3a fc000d3a fc082d3a fc000d3a fc000d3a fc082d3a fc000d3a fc000d3a fc082d3a fc000d3a fc000d3a
  //   fc082d3b fc000d3a fc000d3a fc082d3e fc000d3a fc000d3a fc082c3a fc000d3a fc000d3a fc082d3a fc000d3a
  //   fc000d3a fc082d3a fc000d3a fc000d3a fc082d3a fc000d3a fc000d3a fc082d3a fc000d3a fc000d3a fc082d3a
  //   fc000d3a fc000d3a fc082d3a fc000d3a fc000d3a fc082d3a fc000d3a fc000d3a fc082d3a fc000d3a fc000d3a
  //   fc082d3a fc000d3a fc000d3a fc082d3b fc000d3a fc000d3a fc082d3e fc000d3a fc000d3a fc082c3a fc000d3a
  //   fc000d3a fc082d3a fc000d3a fc000d3a fc082d3a fc000d3a fc000d3a fc082d3a fc000d3a fc000d3a fc082d3a
  //   fc000d3a fc000d3a fc082d3a fc000d3a fc000d3a fc082d3a fc000d3a fc000d3a fc082d3a fc000d3a fc000d3a
  //   fc082d3a fc000d3a fc000d3a fc082d3a fc000d3a fc000d3a fc082d3b fc000d3a fc000d3a fc082d3e fc000d3a
  //   fc000d3a fc082c3a fc000d3a fc000d3a fc082d3a fc000d3a fc000d3a fc082d3a fc000d3a fc000d3a fc082d3a
  //   fc000d3a fc000d3a fc082d3a fc000d3a fc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
  //   RISING
  //   inc => falling edge
endmodule

module ALU (
  input  NOT,
  input  CRFI,
  input  A15,
  input  A14,
  input  A13,
  input  A12,
  input  A11,
  input  A10,
  input  A9,
  input  A8,
  input  A7,
  input  A6,
  input  A5,
  input  A4,
  input  A3,
  input  A2,
  input  A1,
  input  A0,
  input  R15,
  input  R14,
  input  R13,
  input  R12,
  input  R11,
  input  R1O,
  input  R9,
  input  R8,
  input  R7,
  input  R6,
  input  R5,
  input  R4,
  input  R3,
  input  R2,
  input  R1,
  input  RO,
  input  Address_0,
  input  Address_1,
  input  Address_2,
  input  Address_3,
  input  enOut,
  output CRFO,
  output PRFO,
  output OVF,
  output MFO,
  output ZRF,
  output O0,
  output O1,
  output O2,
  output O3,
  output O4,
  output O5,
  output O6,
  output O7,
  output O8,
  output O9,
  output O10,
  output O11,
  output O12,
  output O13,
  output O14,
  output O15
);

  wire ADDO0, ADDO1, ADDO2, ADDO3, ADDO4, ADDO5, ADDO6, ADDO7, ADDO8, ADDO9, ADDO10, ADDO11, ADDO12, ADDO13,
       ADDO14, ADDO15, and_1_out, and_2_out, and_4_out, and_5_out, and_6_out, and_7_out, and_8_out,
       and_9_out, and_10_out, and_11_out, and_12_out, and_13_out, and_14_out, and_15_out, and_16_out,
       and_17_out, and_18_out, and_19_out, and_20_out, and_21_out, and_22_out, and_23_out, and_24_out,
       and_25_out, and_26_out, and_27_out, and_28_out, and_29_out, and_30_out, and_31_out, and_32_out,
       and_33_out, and_34_out, and_35_out, and_36_out, and_37_out, and_38_out, and_39_out, and_40_out,
       and_41_out, and_42_out, and_43_out, and_44_out, and_45_out, and_46_out, and_47_out, and_48_out,
       and_49_out, ANDA0, ANDA1, ANDA2, ANDA3, ANDA4, ANDA5, ANDA6, ANDA7, ANDA8, ANDA9, ANDA10, ANDA11,
       ANDA12, ANDA13, ANDA14, ANDA15, ANDR0, ANDR1, ANDR2, ANDR3, ANDR4, ANDR5, ANDR6, ANDR7, ANDR8, ANDR9,
       ANDR10, ANDR11, ANDR12, ANDR13, ANDR14, ANDR15, demultiplexer_1_out4, demultiplexer_1_out5,
       demultiplexer_2_out4, demultiplexer_2_out5, demultiplexer_3_out4, demultiplexer_3_out5,
       demultiplexer_4_out4, demultiplexer_4_out5, demultiplexer_5_out4, demultiplexer_5_out5,
       demultiplexer_6_out4, demultiplexer_6_out5, demultiplexer_7_out4, demultiplexer_7_out5,
       demultiplexer_8_out4, demultiplexer_8_out5, demultiplexer_9_out4, demultiplexer_9_out5,
       demultiplexer_10_out4, demultiplexer_10_out5, demultiplexer_11_out4, demultiplexer_11_out5,
       demultiplexer_12_out4, demultiplexer_12_out5, demultiplexer_13_out4, demultiplexer_13_out5,
       demultiplexer_14_out4, demultiplexer_14_out5, demultiplexer_15_out4, demultiplexer_15_out5,
       demultiplexer_16_out4, demultiplexer_16_out5, full_adder_1_c_2, full_adder_2_c_2, full_adder_3_c_2,
       full_adder_4_c_2, full_adder_5_c_2, full_adder_6_c_2, full_adder_7_c_2, full_adder_8_c_2,
       full_adder_9_c_2, full_adder_10_c_2, full_adder_11_c_2, full_adder_12_c_2, full_adder_13_c_2,
       full_adder_14_c_2, full_adder_15_c_2, multiplexer_1_out, multiplexer_2_out, multiplexer_3_out,
       multiplexer_4_out, multiplexer_5_out, multiplexer_6_out, multiplexer_7_out, multiplexer_8_out,
       multiplexer_9_out, multiplexer_10_out, multiplexer_11_out, multiplexer_12_out, multiplexer_13_out,
       multiplexer_14_out, multiplexer_15_out, multiplexer_16_out, MXR0, MXR1, MXR2, MXR3, MXR4, MXR5, MXR6,
       MXR7, MXR8, MXR9, MXR10, MXR11, MXR12, MXR13, MXR14, MXR15, nand_1_out, nand_2_out, nand_3_out,
       nand_4_out, not_1_out, not_3_out, not_4_out, not_5_out, not_6_out, not_7_out, not_8_out, not_9_out,
       not_10_out, not_11_out, not_12_out, not_13_out, not_14_out, not_15_out, not_16_out, not_17_out,
       not_18_out, not_19_out, not_20_out, not_21_out, not_22_out, not_23_out, not_24_out, not_25_out,
       not_26_out, not_27_out, not_28_out, not_29_out, not_30_out, not_31_out, not_32_out, not_33_out,
       not_34_out, not_35_out, not_36_out, not_37_out, not_38_out, not_39_out, not_40_out, not_41_out,
       or_2_out, or_4_out, or_6_out, or_7_out, or_8_out, or_9_out, or_10_out, or_11_out, or_12_out,
       or_13_out, or_14_out, or_15_out, or_16_out, or_17_out, or_18_out, or_19_out, or_20_out, or_21_out,
       or_22_out, or_24_out, or_26_out, or_28_out, or_30_out, or_32_out, or_34_out, or_36_out, or_38_out,
       or_40_out, or_42_out, or_44_out, or_46_out, or_48_out, ORA0, ORA1, ORA2, ORA3, ORA4, ORA5, ORA6, ORA7,
       ORA8, ORA9, ORA10, ORA11, ORA12, ORA13, ORA14, ORA15, ORR0, ORR1, ORR2, ORR3, ORR4, ORR5, ORR6, ORR7,
       ORR8, ORR9, ORR10, ORR11, ORR12, ORR13, ORR14, ORR15, ROL0, ROL1, ROL2, ROL3, ROL4, ROL5, ROL6, ROL7,
       ROL8, ROL9, ROL10, ROL11, ROL12, ROL13, ROL14, ROL15, ROR0, ROR1, ROR2, ROR3, ROR4, ROR5, ROR6, ROR7,
       ROR8, ROR9, ROR10, ROR11, ROR12, ROR13, ROR14, ROR15, SLL0, SLL1, SLL2, SLL3, SLL4, SLL5, SLL6, SLL7,
       SLL8, SLL9, SLL10, SLL11, SLL12, SLL13, SLL14, SLL15, SRA0, SRA1, SRA2, SRA3, SRA4, SRA5, SRA6, SRA7,
       SRA8, SRA9, SRA10, SRA11, SRA12, SRA13, SRA14, SRA15, SRL0, SRL1, SRL2, SRL3, SRL4, SRL5, SRL6, SRL7,
       SRL8, SRL9, SRL10, SRL11, SRL12, SRL13, SRL14, SRL15, xor_17_out, xor_18_out, xor_19_out, xor_20_out,
       xor_21_out, xor_22_out, xor_23_out, xor_24_out, xor_25_out, xor_26_out, xor_27_out, xor_28_out,
       xor_29_out, xor_30_out, xor_31_out, xor_32_out, XORA0, XORA1, XORA2, XORA3, XORA4, XORA5, XORA6,
       XORA7, XORA8, XORA9, XORA10, XORA11, XORA12, XORA13, XORA14, XORA15, XORR0, XORR1, XORR2, XORR3,
       XORR4, XORR5, XORR6, XORR7, XORR8, XORR9, XORR10, XORR11, XORR12, XORR13, XORR14, XORR15, ZF0, ZF1,
       ZF2, ZF3, ZF4, ZF5, ZF6, ZF7, ZF8, ZF9, ZF10, ZF11, ZF12, ZF13, ZF14;

  Demultiplexer #(.select(4)) demultiplexer_1 (
    .out1(ANDR15), .out2(ORR15), .out3(XORR15), .out4(demultiplexer_1_out4), .out5(demultiplexer_1_out5),
    .out8(SLL15), .out9(SRL15), .out10(SRA15), .out11(ROL15), .out12(ROR15), .in(R15),
    .sel({Address_3, Address_2, Address_1, Address_0}));  // open: out0, out6, out7, out13, out14, out15, en
  not not_1 (not_1_out, enOut);
  Transistor transistor_1 (.in(ZF0), .out(O0), .gate(not_1_out));
  not not_2 (PRFO, ZF0);
  Transistor transistor_2 (.in(ZF1), .out(O1), .gate(not_1_out));
  Transistor transistor_3 (.in(ZF2), .out(O2), .gate(not_1_out));
  Transistor transistor_4 (.in(ZF3), .out(O3), .gate(not_1_out));
  Transistor transistor_5 (.in(ZF4), .out(O4), .gate(not_1_out));
  Transistor transistor_6 (.in(ZF5), .out(O5), .gate(not_1_out));
  Transistor transistor_7 (.in(ZF6), .out(O6), .gate(not_1_out));
  Transistor transistor_8 (.in(ZF7), .out(O7), .gate(not_1_out));
  Transistor transistor_9 (.in(ZF8), .out(O8), .gate(not_1_out));
  Transistor transistor_10 (.in(ZF9), .out(O9), .gate(not_1_out));
  Transistor transistor_11 (.in(ZF10), .out(O10), .gate(not_1_out));
  Transistor transistor_12 (.in(ZF11), .out(O11), .gate(not_1_out));
  Transistor transistor_13 (.in(ZF12), .out(O12), .gate(not_1_out));
  Transistor transistor_14 (.in(ZF13), .out(O13), .gate(not_1_out));
  Transistor transistor_15 (.in(ZF14), .out(O14), .gate(not_1_out));
  Transistor transistor_16 (.in(MFO), .out(O15), .gate(not_1_out));
  not not_3 (not_3_out, ZF0);
  not not_4 (not_4_out, ZF1);
  not not_5 (not_5_out, ZF2);
  not not_6 (not_6_out, ZF3);
  not not_7 (not_7_out, ZF4);
  not not_8 (not_8_out, ZF5);
  not not_9 (not_9_out, ZF6);
  not not_10 (not_10_out, ZF7);
  not not_11 (not_11_out, ZF8);
  not not_12 (not_12_out, ZF9);
  not not_13 (not_13_out, ZF10);
  not not_14 (not_14_out, ZF11);
  not not_15 (not_15_out, ZF12);
  not not_16 (not_16_out, ZF13);
  not not_17 (not_17_out, ZF14);
  not not_18 (not_18_out, MFO);
  xor xor_1 (ZF0, NOT, multiplexer_1_out);
  xor xor_2 (ZF1, NOT, multiplexer_2_out);
  xor xor_3 (ZF2, NOT, multiplexer_3_out);
  xor xor_4 (ZF3, NOT, multiplexer_4_out);
  xor xor_5 (ZF4, NOT, multiplexer_5_out);
  xor xor_6 (ZF5, NOT, multiplexer_6_out);
  xor xor_7 (ZF6, NOT, multiplexer_7_out);
  xor xor_8 (ZF7, NOT, multiplexer_8_out);
  xor xor_9 (ZF8, NOT, multiplexer_9_out);
  xor xor_10 (ZF9, NOT, multiplexer_10_out);
  xor xor_11 (ZF10, NOT, multiplexer_11_out);
  xor xor_12 (ZF11, NOT, multiplexer_12_out);
  xor xor_13 (ZF12, NOT, multiplexer_13_out);
  xor xor_14 (ZF13, NOT, multiplexer_14_out);
  xor xor_15 (ZF14, NOT, multiplexer_15_out);
  xor xor_16 (MFO, NOT, multiplexer_16_out);
  or or_1 (CRFO, SLL15, SRL0, SRA0);
  not not_19 (not_19_out, demultiplexer_1_out5);
  and and_1 (and_1_out, not_19_out, not_38_out);
  or or_2 (or_2_out, demultiplexer_1_out4, and_1_out);
  and and_2 (and_2_out, or_2_out, nand_2_out);
  or or_3 (MXR15, and_2_out, not_34_out);
  and and_3 (ZRF, not_3_out, not_4_out, not_5_out, not_6_out, not_7_out, not_8_out, not_9_out, not_10_out, not_11_out, not_12_out, not_13_out, not_14_out, not_15_out, not_16_out, not_17_out, not_18_out);
  Multiplexer #(.select(4)) multiplexer_1 (
    .in0(A0), .in1(and_6_out), .in2(or_6_out), .in3(xor_17_out), .in4(ADDO0), .in5(ADDO0), .in6(ADDO0),
    .in7(ADDO0), .in8(CRFI), .in9(SRL1), .in10(SRA1), .in11(ROL15), .in12(ROR1), .in13(1'b0), .in14(1'b0),
    .in15(1'b0), .out(multiplexer_1_out), .sel({Address_3, Address_2, Address_1, Address_0}));  // open: en
  Multiplexer #(.select(4)) multiplexer_2 (
    .in0(A1), .in1(and_7_out), .in2(or_7_out), .in3(xor_18_out), .in4(ADDO1), .in5(ADDO1), .in6(ADDO1),
    .in7(ADDO1), .in8(SLL0), .in9(SRL2), .in10(SRA2), .in11(ROL0), .in12(ROR2), .in13(1'b0), .in14(1'b0),
    .in15(1'b0), .out(multiplexer_2_out), .sel({Address_3, Address_2, Address_1, Address_0}));  // open: en
  Multiplexer #(.select(4)) multiplexer_3 (
    .in0(A2), .in1(and_8_out), .in2(or_8_out), .in3(xor_19_out), .in4(ADDO2), .in5(ADDO2), .in6(ADDO2),
    .in7(ADDO2), .in8(SLL1), .in9(SRL3), .in10(SRA3), .in11(ROL1), .in12(ROR3), .in13(1'b0), .in14(1'b0),
    .in15(1'b0), .out(multiplexer_3_out), .sel({Address_3, Address_2, Address_1, Address_0}));  // open: en
  Multiplexer #(.select(4)) multiplexer_4 (
    .in0(A3), .in1(and_9_out), .in2(or_9_out), .in3(xor_20_out), .in4(ADDO3), .in5(ADDO3), .in6(ADDO3),
    .in7(ADDO3), .in8(SLL2), .in9(SRL4), .in10(SRA4), .in11(ROL2), .in12(ROR4), .in13(1'b0), .in14(1'b0),
    .in15(1'b0), .out(multiplexer_4_out), .sel({Address_3, Address_2, Address_1, Address_0}));  // open: en
  Multiplexer #(.select(4)) multiplexer_5 (
    .in0(A4), .in1(and_10_out), .in2(or_10_out), .in3(xor_21_out), .in4(ADDO4), .in5(ADDO4), .in6(ADDO4),
    .in7(ADDO4), .in8(SLL3), .in9(SRL5), .in10(SRA5), .in11(ROL3), .in12(ROR5), .in13(1'b0), .in14(1'b0),
    .in15(1'b0), .out(multiplexer_5_out), .sel({Address_3, Address_2, Address_1, Address_0}));  // open: en
  Multiplexer #(.select(4)) multiplexer_6 (
    .in0(A5), .in1(and_11_out), .in2(or_11_out), .in3(xor_22_out), .in4(ADDO5), .in5(ADDO5), .in6(ADDO5),
    .in7(ADDO5), .in8(SLL4), .in9(SRL6), .in10(SRA6), .in11(ROL4), .in12(ROR6), .in13(1'b0), .in14(1'b0),
    .in15(1'b0), .out(multiplexer_6_out), .sel({Address_3, Address_2, Address_1, Address_0}));  // open: en
  Multiplexer #(.select(4)) multiplexer_7 (
    .in0(A6), .in1(and_12_out), .in2(or_12_out), .in3(xor_23_out), .in4(ADDO6), .in5(ADDO6), .in6(ADDO6),
    .in7(ADDO6), .in8(SLL5), .in9(SRL7), .in10(SRA7), .in11(ROL5), .in12(ROR7), .in13(1'b0), .in14(1'b0),
    .in15(1'b0), .out(multiplexer_7_out), .sel({Address_3, Address_2, Address_1, Address_0}));  // open: en
  Multiplexer #(.select(4)) multiplexer_8 (
    .in0(A7), .in1(and_13_out), .in2(or_13_out), .in3(xor_24_out), .in4(ADDO7), .in5(ADDO7), .in6(ADDO7),
    .in7(ADDO7), .in8(SLL6), .in9(SRL8), .in10(SRA8), .in11(ROL6), .in12(ROR8), .in13(1'b0), .in14(1'b0),
    .in15(1'b0), .out(multiplexer_8_out), .sel({Address_3, Address_2, Address_1, Address_0}));  // open: en
  Multiplexer #(.select(4)) multiplexer_9 (
    .in0(A8), .in1(and_14_out), .in2(or_14_out), .in3(xor_25_out), .in4(ADDO8), .in5(ADDO8), .in6(ADDO8),
    .in7(ADDO8), .in8(SLL7), .in9(SRL9), .in10(SRA9), .in11(ROL7), .in12(ROR9), .in13(1'b0), .in14(1'b0),
    .in15(1'b0), .out(multiplexer_9_out), .sel({Address_3, Address_2, Address_1, Address_0}));  // open: en
  Multiplexer #(.select(4)) multiplexer_10 (
    .in0(A9), .in1(and_15_out), .in2(or_15_out), .in3(xor_26_out), .in4(ADDO9), .in5(ADDO9), .in6(ADDO9),
    .in7(ADDO9), .in8(SLL8), .in9(SRL10), .in10(SRA10), .in11(ROL8), .in12(ROR10), .in13(1'b0), .in14(1'b0),
    .in15(1'b0), .out(multiplexer_10_out), .sel({Address_3, Address_2, Address_1, Address_0}));  // open: en
  Multiplexer #(.select(4)) multiplexer_11 (
    .in0(A10), .in1(and_16_out), .in2(or_16_out), .in3(xor_27_out), .in4(ADDO10), .in5(ADDO10), .in6(ADDO10),
    .in7(ADDO10), .in8(SLL9), .in9(SRL11), .in10(SRA11), .in11(ROL9), .in12(ROR11), .in13(1'b0), .in14(1'b0),
    .in15(1'b0), .out(multiplexer_11_out), .sel({Address_3, Address_2, Address_1, Address_0}));  // open: en
  Multiplexer #(.select(4)) multiplexer_12 (
    .in0(A11), .in1(and_17_out), .in2(or_17_out), .in3(xor_28_out), .in4(ADDO11), .in5(ADDO11), .in6(ADDO11),
    .in7(ADDO11), .in8(SLL10), .in9(SRL12), .in10(SRA12), .in11(ROL10), .in12(ROR12), .in13(1'b0),
    .in14(1'b0), .in15(1'b0), .out(multiplexer_12_out), .sel({Address_3, Address_2, Address_1, Address_0}));  // open: en
  Multiplexer #(.select(4)) multiplexer_13 (
    .in0(A12), .in1(and_18_out), .in2(or_18_out), .in3(xor_29_out), .in4(ADDO12), .in5(ADDO12), .in6(ADDO12),
    .in7(ADDO12), .in8(SLL11), .in9(SRL13), .in10(SRA13), .in11(ROL11), .in12(ROR13), .in13(1'b0),
    .in14(1'b0), .in15(1'b0), .out(multiplexer_13_out), .sel({Address_3, Address_2, Address_1, Address_0}));  // open: en
  Multiplexer #(.select(4)) multiplexer_14 (
    .in0(A13), .in1(and_19_out), .in2(or_19_out), .in3(xor_30_out), .in4(ADDO13), .in5(ADDO13), .in6(ADDO13),
    .in7(ADDO13), .in8(SLL12), .in9(SRL14), .in10(SRA14), .in11(ROL12), .in12(ROR14), .in13(1'b0),
    .in14(1'b0), .in15(1'b0), .out(multiplexer_14_out), .sel({Address_3, Address_2, Address_1, Address_0}));  // open: en
  Multiplexer #(.select(4)) multiplexer_15 (
    .in0(A14), .in1(and_20_out), .in2(or_20_out), .in3(xor_31_out), .in4(ADDO14), .in5(ADDO14), .in6(ADDO14),
    .in7(ADDO14), .in8(SLL13), .in9(SRL15), .in10(SRA15), .in11(ROL13), .in12(ROR15), .in13(1'b0),
    .in14(1'b0), .in15(1'b0), .out(multiplexer_15_out), .sel({Address_3, Address_2, Address_1, Address_0}));  // open: en
  Multiplexer #(.select(4)) multiplexer_16 (
    .in0(A15), .in1(and_21_out), .in2(or_21_out), .in3(xor_32_out), .in4(ADDO15), .in5(ADDO15), .in6(ADDO15),
    .in7(ADDO15), .in8(SLL14), .in9(CRFI), .in10(SRA15), .in11(ROL14), .in12(ROR0), .in13(1'b0), .in14(1'b0),
    .in15(1'b0), .out(multiplexer_16_out), .sel({Address_3, Address_2, Address_1, Address_0}));  // open: en
  Demultiplexer #(.select(4)) demultiplexer_2 (
    .out1(ANDR14), .out2(ORR14), .out3(XORR14), .out4(demultiplexer_2_out4), .out5(demultiplexer_2_out5),
    .out8(SLL14), .out9(SRL14), .out10(SRA14), .out11(ROL14), .out12(ROR14), .in(R14),
    .sel({Address_3, Address_2, Address_1, Address_0}));  // open: out0, out6, out7, out13, out14, out15, en
  not not_20 (not_20_out, demultiplexer_2_out5);
  and and_4 (and_4_out, not_20_out, not_38_out);
  or or_4 (or_4_out, demultiplexer_2_out4, and_4_out);
  and and_5 (and_5_out, or_4_out, nand_2_out);
  or or_5 (MXR14, and_5_out, not_34_out);
  and and_6 (and_6_out, ANDA0, ANDR0);
  or or_6 (or_6_out, ORA0, ORR0);
  xor xor_17 (xor_17_out, XORA0, XORR0);
  and and_7 (and_7_out, ANDA1, ANDR1);
  or or_7 (or_7_out, ORA1, ORR1);
  xor xor_18 (xor_18_out, XORA1, XORR1);
  and and_8 (and_8_out, ANDA2, ANDR2);
  or or_8 (or_8_out, ORA2, ORR2);
  xor xor_19 (xor_19_out, XORA2, XORR2);
  and and_9 (and_9_out, ANDA3, ANDR3);
  or or_9 (or_9_out, ORA3, ORR3);
  xor xor_20 (xor_20_out, XORA3, XORR3);
  and and_10 (and_10_out, ANDA4, ANDR4);
  or or_10 (or_10_out, ORA4, ORR4);
  xor xor_21 (xor_21_out, XORA4, XORR4);
  and and_11 (and_11_out, ANDA5, ANDR5);
  or or_11 (or_11_out, ORA5, ORR5);
  xor xor_22 (xor_22_out, XORA5, XORR5);
  and and_12 (and_12_out, ANDA6, ANDR6);
  or or_12 (or_12_out, ORA6, ORR6);
  xor xor_23 (xor_23_out, XORA6, XORR6);
  and and_13 (and_13_out, ANDA7, ANDR7);
  or or_13 (or_13_out, ORA7, ORR7);
  xor xor_24 (xor_24_out, XORA7, XORR7);
  and and_14 (and_14_out, ANDA8, ANDR8);
  or or_14 (or_14_out, ORA8, ORR8);
  xor xor_25 (xor_25_out, XORA8, XORR8);
  and and_15 (and_15_out, ANDA9, ANDR9);
  or or_15 (or_15_out, ORA9, ORR9);
  xor xor_26 (xor_26_out, XORA9, XORR9);
  and and_16 (and_16_out, ANDA10, ANDR10);
  or or_16 (or_16_out, ORA10, ORR10);
  xor xor_27 (xor_27_out, XORA10, XORR10);
  and and_17 (and_17_out, ANDA11, ANDR11);
  or or_17 (or_17_out, ORA11, ORR11);
  xor xor_28 (xor_28_out, XORA11, XORR11);
  and and_18 (and_18_out, ANDA12, ANDR12);
  or or_18 (or_18_out, ORA12, ORR12);
  xor xor_29 (xor_29_out, XORA12, XORR12);
  and and_19 (and_19_out, ANDA13, ANDR13);
  or or_19 (or_19_out, ORA13, ORR13);
  xor xor_30 (xor_30_out, XORA13, XORR13);
  and and_20 (and_20_out, ANDA14, ANDR14);
  or or_20 (or_20_out, ORA14, ORR14);
  xor xor_31 (xor_31_out, XORA14, XORR14);
  and and_21 (and_21_out, ANDA15, ANDR15);
  or or_21 (or_21_out, ORA15, ORR15);
  xor xor_32 (xor_32_out, XORA15, XORR15);
  Demultiplexer #(.select(4)) demultiplexer_3 (
    .out1(ANDR13), .out2(ORR13), .out3(XORR13), .out4(demultiplexer_3_out4), .out5(demultiplexer_3_out5),
    .out8(SLL13), .out9(SRL13), .out10(SRA13), .out11(ROL13), .out12(ROR13), .in(R13),
    .sel({Address_3, Address_2, Address_1, Address_0}));  // open: out0, out6, out7, out13, out14, out15, en
  not not_21 (not_21_out, demultiplexer_3_out5);
  or or_22 (or_22_out, demultiplexer_3_out4, and_22_out);
  and and_22 (and_22_out, not_21_out, not_38_out);
  and and_23 (and_23_out, or_22_out, nand_2_out);
  or or_23 (MXR13, and_23_out, not_34_out);
  Demultiplexer #(.select(4)) demultiplexer_4 (
    .out1(ANDR12), .out2(ORR12), .out3(XORR12), .out4(demultiplexer_4_out4), .out5(demultiplexer_4_out5),
    .out8(SLL12), .out9(SRL12), .out10(SRA12), .out11(ROL12), .out12(ROR12), .in(R12),
    .sel({Address_3, Address_2, Address_1, Address_0}));  // open: out0, out6, out7, out13, out14, out15, en
  not not_22 (not_22_out, demultiplexer_4_out5);
  or or_24 (or_24_out, demultiplexer_4_out4, and_24_out);
  and and_24 (and_24_out, not_22_out, not_38_out);
  and and_25 (and_25_out, or_24_out, nand_2_out);
  or or_25 (MXR12, and_25_out, not_34_out);
  Demultiplexer #(.select(4)) demultiplexer_5 (
    .out1(ANDR11), .out2(ORR11), .out3(XORR11), .out4(demultiplexer_5_out4), .out5(demultiplexer_5_out5),
    .out8(SLL11), .out9(SRL11), .out10(SRA11), .out11(ROL11), .out12(ROR11), .in(R11),
    .sel({Address_3, Address_2, Address_1, Address_0}));  // open: out0, out6, out7, out13, out14, out15, en
  not not_23 (not_23_out, demultiplexer_5_out5);
  or or_26 (or_26_out, demultiplexer_5_out4, and_26_out);
  and and_26 (and_26_out, not_23_out, not_38_out);
  and and_27 (and_27_out, or_26_out, nand_2_out);
  or or_27 (MXR11, and_27_out, not_34_out);
  Demultiplexer #(.select(4)) demultiplexer_6 (
    .out1(ANDR10), .out2(ORR10), .out3(XORR10), .out4(demultiplexer_6_out4), .out5(demultiplexer_6_out5),
    .out8(SLL10), .out9(SRL10), .out10(SRA10), .out11(ROL10), .out12(ROR10), .in(R1O),
    .sel({Address_3, Address_2, Address_1, Address_0}));  // open: out0, out6, out7, out13, out14, out15, en
  not not_24 (not_24_out, demultiplexer_6_out5);
  and and_28 (and_28_out, not_24_out, not_38_out);
  or or_28 (or_28_out, demultiplexer_6_out4, and_28_out);
  and and_29 (and_29_out, or_28_out, nand_2_out);
  or or_29 (MXR10, and_29_out, not_34_out);
  Demultiplexer #(.select(4)) demultiplexer_7 (
    .out1(ANDR9), .out2(ORR9), .out3(XORR9), .out4(demultiplexer_7_out4), .out5(demultiplexer_7_out5),
    .out8(SLL9), .out9(SRL9), .out10(SRA9), .out11(ROL9), .out12(ROR9), .in(R9),
    .sel({Address_3, Address_2, Address_1, Address_0}));  // open: out0, out6, out7, out13, out14, out15, en
  not not_25 (not_25_out, demultiplexer_7_out5);
  and and_30 (and_30_out, not_25_out, not_38_out);
  or or_30 (or_30_out, demultiplexer_7_out4, and_30_out);
  and and_31 (and_31_out, or_30_out, nand_2_out);
  or or_31 (MXR9, and_31_out, not_34_out);
  Demultiplexer #(.select(4)) demultiplexer_8 (
    .out1(ANDR8), .out2(ORR8), .out3(XORR8), .out4(demultiplexer_8_out4), .out5(demultiplexer_8_out5),
    .out8(SLL8), .out9(SRL8), .out10(SRA8), .out11(ROL8), .out12(ROR8), .in(R8),
    .sel({Address_3, Address_2, Address_1, Address_0}));  // open: out0, out6, out7, out13, out14, out15, en
  not not_26 (not_26_out, demultiplexer_8_out5);
  and and_32 (and_32_out, not_26_out, not_38_out);
  or or_32 (or_32_out, demultiplexer_8_out4, and_32_out);
  and and_33 (and_33_out, or_32_out, nand_2_out);
  or or_33 (MXR8, and_33_out, not_34_out);
  Demultiplexer #(.select(4)) demultiplexer_9 (
    .out1(ANDR7), .out2(ORR7), .out3(XORR7), .out4(demultiplexer_9_out4), .out5(demultiplexer_9_out5),
    .out8(SLL7), .out9(SRL7), .out10(SRA7), .out11(ROL7), .out12(ROR7), .in(R7),
    .sel({Address_3, Address_2, Address_1, Address_0}));  // open: out0, out6, out7, out13, out14, out15, en
  not not_27 (not_27_out, demultiplexer_9_out5);
  and and_34 (and_34_out, not_27_out, not_38_out);
  or or_34 (or_34_out, demultiplexer_9_out4, and_34_out);
  and and_35 (and_35_out, or_34_out, nand_2_out);
  or or_35 (MXR7, and_35_out, not_34_out);
  Demultiplexer #(.select(4)) demultiplexer_10 (
    .out1(ANDR6), .out2(ORR6), .out3(XORR6), .out4(demultiplexer_10_out4), .out5(demultiplexer_10_out5),
    .out8(SLL6), .out9(SRL6), .out10(SRA6), .out11(ROL6), .out12(ROR6), .in(R6),
    .sel({Address_3, Address_2, Address_1, Address_0}));  // open: out0, out6, out7, out13, out14, out15, en
  not not_28 (not_28_out, demultiplexer_10_out5);
  and and_36 (and_36_out, not_28_out, not_38_out);
  or or_36 (or_36_out, demultiplexer_10_out4, and_36_out);
  and and_37 (and_37_out, or_36_out, nand_2_out);
  or or_37 (MXR6, and_37_out, not_34_out);
  Demultiplexer #(.select(4)) demultiplexer_11 (
    .out1(ANDR5), .out2(ORR5), .out3(XORR5), .out4(demultiplexer_11_out4), .out5(demultiplexer_11_out5),
    .out8(SLL5), .out9(SRL5), .out10(SRA5), .out11(ROL5), .out12(ROR5), .in(R5),
    .sel({Address_3, Address_2, Address_1, Address_0}));  // open: out0, out6, out7, out13, out14, out15, en
  not not_29 (not_29_out, demultiplexer_11_out5);
  and and_38 (and_38_out, not_29_out, not_38_out);
  or or_38 (or_38_out, demultiplexer_11_out4, and_38_out);
  and and_39 (and_39_out, or_38_out, nand_2_out);
  or or_39 (MXR5, and_39_out, not_34_out);
  Demultiplexer #(.select(4)) demultiplexer_12 (
    .out1(ANDR4), .out2(ORR4), .out3(XORR4), .out4(demultiplexer_12_out4), .out5(demultiplexer_12_out5),
    .out8(SLL4), .out9(SRL4), .out10(SRA4), .out11(ROL4), .out12(ROR4), .in(R4),
    .sel({Address_3, Address_2, Address_1, Address_0}));  // open: out0, out6, out7, out13, out14, out15, en
  not not_30 (not_30_out, demultiplexer_12_out5);
  or or_40 (or_40_out, demultiplexer_12_out4, and_40_out);
  and and_40 (and_40_out, not_30_out, not_38_out);
  and and_41 (and_41_out, or_40_out, nand_2_out);
  or or_41 (MXR4, and_41_out, not_34_out);
  Demultiplexer #(.select(4)) demultiplexer_13 (
    .out1(ANDR3), .out2(ORR3), .out3(XORR3), .out4(demultiplexer_13_out4), .out5(demultiplexer_13_out5),
    .out8(SLL3), .out9(SRL3), .out10(SRA3), .out11(ROL3), .out12(ROR3), .in(R3),
    .sel({Address_3, Address_2, Address_1, Address_0}));  // open: out0, out6, out7, out13, out14, out15, en
  not not_31 (not_31_out, demultiplexer_13_out5);
  or or_42 (or_42_out, demultiplexer_13_out4, and_42_out);
  and and_42 (and_42_out, not_31_out, not_38_out);
  and and_43 (and_43_out, or_42_out, nand_2_out);
  or or_43 (MXR3, and_43_out, not_34_out);
  Demultiplexer #(.select(4)) demultiplexer_14 (
    .out1(ANDR2), .out2(ORR2), .out3(XORR2), .out4(demultiplexer_14_out4), .out5(demultiplexer_14_out5),
    .out8(SLL2), .out9(SRL2), .out10(SRA2), .out11(ROL2), .out12(ROR2), .in(R2),
    .sel({Address_3, Address_2, Address_1, Address_0}));  // open: out0, out6, out7, out13, out14, out15, en
  not not_32 (not_32_out, demultiplexer_14_out5);
  and and_44 (and_44_out, not_32_out, not_38_out);
  or or_44 (or_44_out, demultiplexer_14_out4, and_44_out);
  and and_45 (and_45_out, or_44_out, nand_2_out);
  or or_45 (MXR2, and_45_out, not_34_out);
  Demultiplexer #(.select(4)) demultiplexer_15 (
    .out1(ANDR1), .out2(ORR1), .out3(XORR1), .out4(demultiplexer_15_out4), .out5(demultiplexer_15_out5),
    .out8(SLL1), .out9(SRL1), .out10(SRA1), .out11(ROL1), .out12(ROR1), .in(R1),
    .sel({Address_3, Address_2, Address_1, Address_0}));  // open: out0, out6, out7, out13, out14, out15, en
  not not_33 (not_33_out, demultiplexer_15_out5);
  and and_46 (and_46_out, not_33_out, not_38_out);
  or or_46 (or_46_out, demultiplexer_15_out4, and_46_out);
  and and_47 (and_47_out, or_46_out, nand_2_out);
  or or_47 (MXR1, and_47_out, not_34_out);
  Demultiplexer #(.select(4)) demultiplexer_16 (
    .out1(ANDR0), .out2(ORR0), .out3(XORR0), .out4(demultiplexer_16_out4), .out5(demultiplexer_16_out5),
    .out8(SLL0), .out9(SRL0), .out10(SRA0), .out11(ROL0), .out12(ROR0), .in(RO),
    .sel({Address_3, Address_2, Address_1, Address_0}));  // open: out0, out6, out7, out13, out14, out15, en
  not not_34 (not_34_out, nand_4_out);
  not not_35 (not_35_out, demultiplexer_16_out5);
  and and_48 (and_48_out, not_35_out, not_38_out);
  or or_48 (or_48_out, demultiplexer_16_out4, and_48_out);
  and and_49 (and_49_out, or_48_out, nand_2_out);
  not not_36 (not_36_out, Address_3);
  not not_37 (not_37_out, Address_1);
  nand nand_1 (nand_1_out, not_36_out, Address_2, not_37_out, Address_0);
  not not_38 (not_38_out, nand_1_out);
  and and_50 (MXR0, and_49_out, nand_4_out);
  not not_39 (not_39_out, Address_0);
  not not_40 (not_40_out, Address_3);
  nand nand_2 (nand_2_out, not_40_out, Address_2, Address_1, not_39_out);
  nand nand_3 (nand_3_out, nand_1_out, nand_2_out, nand_4_out);
  not not_41 (not_41_out, Address_3);
  nand nand_4 (nand_4_out, not_41_out, Address_2, Address_1, Address_0);
  Full_Adder full_adder_1 (.A(A0), .B(nand_3_out), .C(MXR0), .O(ADDO0), .C_2(full_adder_1_c_2));
  Full_Adder full_adder_2 (.A(A1), .B(full_adder_1_c_2), .C(MXR1), .O(ADDO1), .C_2(full_adder_2_c_2));
  Full_Adder full_adder_3 (.A(A2), .B(full_adder_2_c_2), .C(MXR2), .O(ADDO2), .C_2(full_adder_3_c_2));
  Full_Adder full_adder_4 (.A(A3), .B(full_adder_3_c_2), .C(MXR3), .O(ADDO3), .C_2(full_adder_4_c_2));
  Full_Adder full_adder_5 (.A(A4), .B(full_adder_4_c_2), .C(MXR4), .O(ADDO4), .C_2(full_adder_5_c_2));
  Full_Adder full_adder_6 (.A(A5), .B(full_adder_5_c_2), .C(MXR5), .O(ADDO5), .C_2(full_adder_6_c_2));
  Full_Adder full_adder_7 (.A(A6), .B(full_adder_6_c_2), .C(MXR6), .O(ADDO6), .C_2(full_adder_7_c_2));
  Full_Adder full_adder_8 (.A(A7), .B(full_adder_7_c_2), .C(MXR7), .O(ADDO7), .C_2(full_adder_8_c_2));
  Full_Adder full_adder_9 (.A(A8), .B(full_adder_8_c_2), .C(MXR8), .O(ADDO8), .C_2(full_adder_9_c_2));
  Demultiplexer #(.select(4)) demultiplexer_17 (
    .out1(ANDA15), .out2(ORA15), .out3(XORA15), .in(A15), .sel({Address_3, Address_2, Address_1, Address_0}));  // open: out0, out4, out5, out6, out7, out8, out9, out10, out11, out12, out13, out14, out15, en
  Full_Adder full_adder_10 (.A(A9), .B(full_adder_9_c_2), .C(MXR9), .O(ADDO9), .C_2(full_adder_10_c_2));
  Full_Adder full_adder_11 (.A(A10), .B(full_adder_10_c_2), .C(MXR10), .O(ADDO10), .C_2(full_adder_11_c_2));
  Full_Adder full_adder_12 (.A(A11), .B(full_adder_11_c_2), .C(MXR11), .O(ADDO11), .C_2(full_adder_12_c_2));
  Full_Adder full_adder_13 (.A(A12), .B(full_adder_12_c_2), .C(MXR12), .O(ADDO12), .C_2(full_adder_13_c_2));
  Demultiplexer #(.select(4)) demultiplexer_18 (
    .out1(ANDA14), .out2(ORA14), .out3(XORA14), .in(A14), .sel({Address_3, Address_2, Address_1, Address_0}));  // open: out0, out4, out5, out6, out7, out8, out9, out10, out11, out12, out13, out14, out15, en
  Full_Adder full_adder_14 (.A(A13), .B(full_adder_13_c_2), .C(MXR13), .O(ADDO13), .C_2(full_adder_14_c_2));
  Full_Adder full_adder_15 (.A(A14), .B(full_adder_14_c_2), .C(MXR14), .O(ADDO14), .C_2(full_adder_15_c_2));
  Full_Adder full_adder_16 (.A(A15), .B(full_adder_15_c_2), .C(MXR15), .O(ADDO15), .C_2(OVF));
  Demultiplexer #(.select(4)) demultiplexer_19 (
    .out1(ANDA13), .out2(ORA13), .out3(XORA13), .in(A13), .sel({Address_3, Address_2, Address_1, Address_0}));  // open: out0, out4, out5, out6, out7, out8, out9, out10, out11, out12, out13, out14, out15, en
  Demultiplexer #(.select(4)) demultiplexer_20 (
    .out1(ANDA12), .out2(ORA12), .out3(XORA12), .in(A12), .sel({Address_3, Address_2, Address_1, Address_0}));  // open: out0, out4, out5, out6, out7, out8, out9, out10, out11, out12, out13, out14, out15, en
  Demultiplexer #(.select(4)) demultiplexer_21 (
    .out1(ANDA11), .out2(ORA11), .out3(XORA11), .in(A11), .sel({Address_3, Address_2, Address_1, Address_0}));  // open: out0, out4, out5, out6, out7, out8, out9, out10, out11, out12, out13, out14, out15, en
  Demultiplexer #(.select(4)) demultiplexer_22 (
    .out1(ANDA10), .out2(ORA10), .out3(XORA10), .in(A10), .sel({Address_3, Address_2, Address_1, Address_0}));  // open: out0, out4, out5, out6, out7, out8, out9, out10, out11, out12, out13, out14, out15, en
  Demultiplexer #(.select(4)) demultiplexer_23 (
    .out1(ANDA9), .out2(ORA9), .out3(XORA9), .in(A9), .sel({Address_3, Address_2, Address_1, Address_0}));  // open: out0, out4, out5, out6, out7, out8, out9, out10, out11, out12, out13, out14, out15, en
  Demultiplexer #(.select(4)) demultiplexer_24 (
    .out1(ANDA8), .out2(ORA8), .out3(XORA8), .in(A8), .sel({Address_3, Address_2, Address_1, Address_0}));  // open: out0, out4, out5, out6, out7, out8, out9, out10, out11, out12, out13, out14, out15, en
  Demultiplexer #(.select(4)) demultiplexer_25 (
    .out1(ANDA7), .out2(ORA7), .out3(XORA7), .in(A7), .sel({Address_3, Address_2, Address_1, Address_0}));  // open: out0, out4, out5, out6, out7, out8, out9, out10, out11, out12, out13, out14, out15, en
  Demultiplexer #(.select(4)) demultiplexer_26 (
    .out1(ANDA6), .out2(ORA6), .out3(XORA6), .in(A6), .sel({Address_3, Address_2, Address_1, Address_0}));  // open: out0, out4, out5, out6, out7, out8, out9, out10, out11, out12, out13, out14, out15, en
  Demultiplexer #(.select(4)) demultiplexer_27 (
    .out1(ANDA5), .out2(ORA5), .out3(XORA5), .in(A5), .sel({Address_3, Address_2, Address_1, Address_0}));  // open: out0, out4, out5, out6, out7, out8, out9, out10, out11, out12, out13, out14, out15, en
  Demultiplexer #(.select(4)) demultiplexer_28 (
    .out1(ANDA4), .out2(ORA4), .out3(XORA4), .in(A4), .sel({Address_3, Address_2, Address_1, Address_0}));  // open: out0, out4, out5, out6, out7, out8, out9, out10, out11, out12, out13, out14, out15, en
  Demultiplexer #(.select(4)) demultiplexer_29 (
    .out1(ANDA3), .out2(ORA3), .out3(XORA3), .in(A3), .sel({Address_3, Address_2, Address_1, Address_0}));  // open: out0, out4, out5, out6, out7, out8, out9, out10, out11, out12, out13, out14, out15, en
  Demultiplexer #(.select(4)) demultiplexer_30 (
    .out1(ANDA2), .out2(ORA2), .out3(XORA2), .in(A2), .sel({Address_3, Address_2, Address_1, Address_0}));  // open: out0, out4, out5, out6, out7, out8, out9, out10, out11, out12, out13, out14, out15, en
  Demultiplexer #(.select(4)) demultiplexer_31 (
    .out1(ANDA1), .out2(ORA1), .out3(XORA1), .in(A1), .sel({Address_3, Address_2, Address_1, Address_0}));  // open: out0, out4, out5, out6, out7, out8, out9, out10, out11, out12, out13, out14, out15, en
  Demultiplexer #(.select(4)) demultiplexer_32 (
    .out1(ANDA0), .out2(ORA0), .out3(XORA0), .in(A0), .sel({Address_3, Address_2, Address_1, Address_0}));  // open: out0, out4, out5, out6, out7, out8, out9, out10, out11, out12, out13, out14, out15, en

  // Other names for the same wires on the sheet: PRF = PRFO; R0 = RO; R10 = R1O; ZF15 = MFO
endmodule
module ALU_testing (
  input  A15,
  input  in_2,
  input  in_3,
  input  in_4,
  input  in_5,
  input  in_6,
  input  in_7,
  input  in_8,
  input  in_9,
  input  in_10,
  input  in_11,
  input  in_12,
  input  in_13,
  input  in_14,
  input  in_15,
  input  A0,
  input  NOT,
  input  CRFI,
  input  Adr4,
  input  in_20,
  input  in_21,
  input  Adr0,
  input  EnA,
  input  R15,
  input  in_25,
  input  in_26,
  input  in_27,
  input  in_28,
  input  in_29,
  input  in_30,
  input  in_31,
  input  in_32,
  input  in_33,
  input  in_34,
  input  in_35,
  input  in_36,
  input  in_37,
  input  in_38,
  input  R0
);

  wire alu_1_mfo, alu_1_o0, alu_1_o1, alu_1_o2, alu_1_o3, alu_1_o4, alu_1_o5, alu_1_o6, alu_1_o7, alu_1_o8,
       alu_1_o9, alu_1_o10, alu_1_o11, alu_1_o12, alu_1_o13, alu_1_o14, alu_1_o15, alu_1_ovf, alu_1_prfo;

  ALU alu_1 (
    .O0(alu_1_o0), .O1(alu_1_o1), .O2(alu_1_o2), .O3(alu_1_o3), .O4(alu_1_o4), .O5(alu_1_o5), .O6(alu_1_o6),
    .O7(alu_1_o7), .O8(alu_1_o8), .O9(alu_1_o9), .O10(alu_1_o10), .O11(alu_1_o11), .O12(alu_1_o12),
    .O13(alu_1_o13), .O14(alu_1_o14), .O15(alu_1_o15), .A15(A15), .A14(in_2), .A13(in_3), .A12(in_4),
    .A11(in_5), .A10(in_6), .A9(in_7), .A8(in_8), .A7(in_9), .A6(in_10), .A5(in_11), .A4(in_12), .A3(in_13),
    .A2(in_14), .A1(in_15), .A0(A0), .R15(R15), .R14(in_25), .R13(in_26), .R12(in_27), .R11(in_28),
    .R1O(in_29), .R9(in_30), .R8(in_31), .R7(in_32), .R6(in_33), .R5(in_34), .R4(in_35), .R3(in_36),
    .R2(in_37), .R1(in_38), .RO(R0), .NOT(NOT), .CRFI(CRFI), .PRFO(alu_1_prfo), .OVF(alu_1_ovf),
    .MFO(alu_1_mfo), .Address_0(Adr0), .Address_1(in_21), .Address_2(in_20), .Address_3(Adr4), .enOut(EnA));  // open: CRFO, ZRF
endmodule

module _74193_experimental (
  input  CLR,
  input  UP,
  input  DOWN,
  input  nLOAD,
  input  A,
  input  B,
  input  C,
  input  D,
  output QA,
  output QB,
  output QC,
  output QD,
  output CO,
  output BO
);

  wire and_1_out, and_2_out, and_3_out, and_4_out, and_5_out, and_6_out, and_7_out, and_8_out, and_9_out,
       and_10_out, and_11_out, and_12_out, and_13_out, and_14_out, and_15_out, and_16_out, j_k_ff_1_qn,
       j_k_ff_2_qn, j_k_ff_3_qn, j_k_ff_4_qn, not_1_out, not_2_out, not_3_out, not_4_out, not_5_out,
       not_6_out, not_7_out, or_1_out, or_2_out, or_3_out, or_4_out, or_5_out, or_6_out, or_7_out, or_8_out;

  not not_1 (not_1_out, nLOAD);
  not not_2 (not_2_out, UP);
  not not_3 (not_3_out, DOWN);
  not not_4 (not_4_out, A);
  not not_5 (not_5_out, B);
  not not_6 (not_6_out, C);
  not not_7 (not_7_out, D);
  and and_1 (and_1_out, A, not_1_out);
  and and_2 (and_2_out, not_4_out, not_1_out);
  and and_3 (and_3_out, B, not_1_out);
  and and_4 (and_4_out, not_5_out, not_1_out);
  and and_5 (and_5_out, C, not_1_out);
  and and_6 (and_6_out, not_6_out, not_1_out);
  and and_7 (and_7_out, D, not_1_out);
  and and_8 (and_8_out, not_7_out, not_1_out);
  and and_9 (and_9_out, not_2_out, QA);
  and and_10 (and_10_out, not_3_out, j_k_ff_1_qn);
  and and_11 (and_11_out, not_2_out, QA, QB);
  and and_12 (and_12_out, not_3_out, j_k_ff_1_qn, j_k_ff_2_qn);
  and and_13 (and_13_out, not_2_out, QA, QB, QC);
  and and_14 (and_14_out, not_3_out, j_k_ff_1_qn, j_k_ff_2_qn, j_k_ff_3_qn);
  or or_1 (or_1_out, not_2_out, not_3_out);
  or or_2 (or_2_out, and_9_out, and_10_out);
  or or_3 (or_3_out, and_11_out, and_12_out);
  or or_4 (or_4_out, and_13_out, and_14_out);
  J_K_Flip_Flop #(.trigger("falling")) j_k_ff_1 (
    .J(1'b1), .clk(or_1_out), .K(1'b1), .Q(QA), .Qn(j_k_ff_1_qn), .preset(and_1_out), .reset(or_5_out));  // open: en
  or or_5 (or_5_out, CLR, and_2_out);
  J_K_Flip_Flop #(.trigger("falling")) j_k_ff_2 (
    .J(1'b1), .clk(or_2_out), .K(1'b1), .Q(QB), .Qn(j_k_ff_2_qn), .preset(and_3_out), .reset(or_6_out));  // open: en
  or or_6 (or_6_out, CLR, and_4_out);
  J_K_Flip_Flop #(.trigger("falling")) j_k_ff_3 (
    .J(1'b1), .clk(or_3_out), .K(1'b1), .Q(QC), .Qn(j_k_ff_3_qn), .preset(and_5_out), .reset(or_7_out));  // open: en
  or or_7 (or_7_out, CLR, and_6_out);
  J_K_Flip_Flop #(.trigger("falling")) j_k_ff_4 (
    .J(1'b1), .clk(or_4_out), .K(1'b1), .Q(QD), .Qn(j_k_ff_4_qn), .preset(and_7_out), .reset(or_8_out));  // open: en
  or or_8 (or_8_out, CLR, and_8_out);
  and and_15 (and_15_out, QD, not_2_out, QA, QB, QC);
  and and_16 (and_16_out, j_k_ff_4_qn, not_3_out, j_k_ff_1_qn, j_k_ff_2_qn, j_k_ff_3_qn);
  not not_8 (CO, and_15_out);
  not not_9 (BO, and_16_out);
endmodule

module _16bit_74193 (
  input  CLR,
  input  DOWN,
  input  UP,
  input  nLOAD,
  input  enAout,
  input  I0,
  input  I1,
  input  I2,
  input  I3,
  input  I4,
  input  I5,
  input  I6,
  input  I7,
  input  I8,
  input  I9,
  input  I10,
  input  I11,
  input  I12,
  input  I13,
  input  I14,
  input  I15,
  output OA0,
  output OA1,
  output OA2,
  output OA3,
  output OA4,
  output OA5,
  output OA6,
  output OA7,
  output OA8,
  output OA9,
  output OA10,
  output OA11,
  output OA12,
  output OA13,
  output OA14,
  output OA15,
  output spOVF
);

  wire n74193_experimental_1_bo, n74193_experimental_1_co, n74193_experimental_1_qa,
       n74193_experimental_1_qb, n74193_experimental_1_qc, n74193_experimental_1_qd,
       n74193_experimental_2_bo, n74193_experimental_2_co, n74193_experimental_2_qa,
       n74193_experimental_2_qb, n74193_experimental_2_qc, n74193_experimental_2_qd,
       n74193_experimental_3_bo, n74193_experimental_3_co, n74193_experimental_3_qa,
       n74193_experimental_3_qb, n74193_experimental_3_qc, n74193_experimental_3_qd,
       n74193_experimental_4_bo, n74193_experimental_4_co, n74193_experimental_4_qa,
       n74193_experimental_4_qb, n74193_experimental_4_qc, n74193_experimental_4_qd, not_1_out;

  not not_1 (not_1_out, enAout);
  _74193_experimental u_74193_experimental_1 (
    .CLR(CLR), .UP(UP), .DOWN(DOWN), .nLOAD(nLOAD), .A(I0), .B(I1), .C(I2), .D(I3),
    .QA(n74193_experimental_1_qa), .QB(n74193_experimental_1_qb), .QC(n74193_experimental_1_qc),
    .QD(n74193_experimental_1_qd), .CO(n74193_experimental_1_co), .BO(n74193_experimental_1_bo));
  _74193_experimental u_74193_experimental_2 (
    .CLR(CLR), .UP(n74193_experimental_1_co), .DOWN(n74193_experimental_1_bo), .nLOAD(nLOAD), .A(I4), .B(I5),
    .C(I6), .D(I7), .QA(n74193_experimental_2_qa), .QB(n74193_experimental_2_qb),
    .QC(n74193_experimental_2_qc), .QD(n74193_experimental_2_qd), .CO(n74193_experimental_2_co),
    .BO(n74193_experimental_2_bo));
  _74193_experimental u_74193_experimental_3 (
    .CLR(CLR), .UP(n74193_experimental_2_co), .DOWN(n74193_experimental_2_bo), .nLOAD(nLOAD), .A(I8), .B(I9),
    .C(I10), .D(I11), .QA(n74193_experimental_3_qa), .QB(n74193_experimental_3_qb),
    .QC(n74193_experimental_3_qc), .QD(n74193_experimental_3_qd), .CO(n74193_experimental_3_co),
    .BO(n74193_experimental_3_bo));
  _74193_experimental u_74193_experimental_4 (
    .CLR(CLR), .UP(n74193_experimental_3_co), .DOWN(n74193_experimental_3_bo), .nLOAD(nLOAD), .A(I12),
    .B(I13), .C(I14), .D(I15), .QA(n74193_experimental_4_qa), .QB(n74193_experimental_4_qb),
    .QC(n74193_experimental_4_qc), .QD(n74193_experimental_4_qd), .CO(n74193_experimental_4_co),
    .BO(n74193_experimental_4_bo));
  or or_1 (spOVF, n74193_experimental_4_bo, n74193_experimental_4_co);
  Transistor transistor_1 (.in(n74193_experimental_1_qa), .out(OA0), .gate(not_1_out));
  Transistor transistor_2 (.in(n74193_experimental_1_qb), .out(OA1), .gate(not_1_out));
  Transistor transistor_3 (.in(n74193_experimental_1_qc), .out(OA2), .gate(not_1_out));
  Transistor transistor_4 (.in(n74193_experimental_1_qd), .out(OA3), .gate(not_1_out));
  Transistor transistor_5 (.in(n74193_experimental_2_qa), .out(OA4), .gate(not_1_out));
  Transistor transistor_6 (.in(n74193_experimental_2_qb), .out(OA5), .gate(not_1_out));
  Transistor transistor_7 (.in(n74193_experimental_2_qc), .out(OA6), .gate(not_1_out));
  Transistor transistor_8 (.in(n74193_experimental_2_qd), .out(OA7), .gate(not_1_out));
  Transistor transistor_9 (.in(n74193_experimental_3_qa), .out(OA8), .gate(not_1_out));
  Transistor transistor_10 (.in(n74193_experimental_3_qb), .out(OA9), .gate(not_1_out));
  Transistor transistor_11 (.in(n74193_experimental_3_qc), .out(OA10), .gate(not_1_out));
  Transistor transistor_12 (.in(n74193_experimental_3_qd), .out(OA11), .gate(not_1_out));
  Transistor transistor_13 (.in(n74193_experimental_4_qa), .out(OA12), .gate(not_1_out));
  Transistor transistor_14 (.in(n74193_experimental_4_qb), .out(OA13), .gate(not_1_out));
  Transistor transistor_15 (.in(n74193_experimental_4_qc), .out(OA14), .gate(not_1_out));
  Transistor transistor_16 (.in(n74193_experimental_4_qd), .out(OA15), .gate(not_1_out));
endmodule

// REG
module reg_experimental (
  input  I15,
  input  I14,
  input  I13,
  input  I12,
  input  I11,
  input  I10,
  input  I9,
  input  I8,
  input  I7,
  input  I6,
  input  I5,
  input  I4,
  input  I3,
  input  I2,
  input  I1,
  input  I0,
  input  LM,
  input  CLK,
  input  nenOut,
  output OB15,
  output OB14,
  output OB13,
  output OB12,
  output OB11,
  output OB10,
  output OB9,
  output OB8,
  output OB7,
  output OB6,
  output OB5,
  output OB4,
  output OB3,
  output OB2,
  output OB1,
  output OB0
);

  wire and_1_out, and_2_out, and_3_out, and_4_out, and_5_out, and_6_out, and_7_out, and_8_out, and_9_out,
       and_10_out, and_11_out, and_12_out, and_13_out, and_14_out, and_15_out, and_16_out, and_17_out,
       and_18_out, and_19_out, and_20_out, and_21_out, and_22_out, and_23_out, and_24_out, and_25_out,
       and_26_out, and_27_out, and_28_out, and_29_out, and_30_out, and_31_out, and_32_out, d_ff_1_q,
       d_ff_2_q, d_ff_3_q, d_ff_4_q, d_ff_5_q, d_ff_6_q, d_ff_7_q, d_ff_8_q, d_ff_9_q, d_ff_10_q, d_ff_11_q,
       d_ff_12_q, d_ff_13_q, d_ff_14_q, d_ff_15_q, d_ff_16_q, not_1_out, or_1_out, or_2_out, or_3_out,
       or_4_out, or_5_out, or_6_out, or_7_out, or_8_out, or_9_out, or_10_out, or_11_out, or_12_out,
       or_13_out, or_14_out, or_15_out, or_16_out;

  and and_1 (and_1_out, I15, LM);
  or or_1 (or_1_out, and_1_out, and_2_out);
  and and_2 (and_2_out, not_1_out, d_ff_1_q);
  D_Flip_Flop #(.trigger("falling")) d_ff_1 (.clk(CLK), .D(or_1_out), .Q(d_ff_1_q));  // open: Qn, preset, en, reset
  and and_3 (and_3_out, I14, LM);
  or or_2 (or_2_out, and_3_out, and_4_out);
  and and_4 (and_4_out, not_1_out, d_ff_2_q);
  D_Flip_Flop #(.trigger("falling")) d_ff_2 (.clk(CLK), .D(or_2_out), .Q(d_ff_2_q));  // open: Qn, preset, en, reset
  and and_5 (and_5_out, I13, LM);
  or or_3 (or_3_out, and_5_out, and_6_out);
  and and_6 (and_6_out, not_1_out, d_ff_3_q);
  D_Flip_Flop #(.trigger("falling")) d_ff_3 (.clk(CLK), .D(or_3_out), .Q(d_ff_3_q));  // open: Qn, preset, en, reset
  and and_7 (and_7_out, I12, LM);
  or or_4 (or_4_out, and_7_out, and_8_out);
  and and_8 (and_8_out, not_1_out, d_ff_4_q);
  D_Flip_Flop #(.trigger("falling")) d_ff_4 (.clk(CLK), .D(or_4_out), .Q(d_ff_4_q));  // open: Qn, preset, en, reset
  and and_9 (and_9_out, I11, LM);
  or or_5 (or_5_out, and_9_out, and_10_out);
  and and_10 (and_10_out, not_1_out, d_ff_5_q);
  D_Flip_Flop #(.trigger("falling")) d_ff_5 (.clk(CLK), .D(or_5_out), .Q(d_ff_5_q));  // open: Qn, preset, en, reset
  and and_11 (and_11_out, I10, LM);
  and and_12 (and_12_out, not_1_out, d_ff_6_q);
  or or_6 (or_6_out, and_11_out, and_12_out);
  D_Flip_Flop #(.trigger("falling")) d_ff_6 (.clk(CLK), .D(or_6_out), .Q(d_ff_6_q));  // open: Qn, preset, en, reset
  and and_13 (and_13_out, I9, LM);
  or or_7 (or_7_out, and_13_out, and_14_out);
  and and_14 (and_14_out, not_1_out, d_ff_7_q);
  D_Flip_Flop #(.trigger("falling")) d_ff_7 (.clk(CLK), .D(or_7_out), .Q(d_ff_7_q));  // open: Qn, preset, en, reset
  and and_15 (and_15_out, I8, LM);
  and and_16 (and_16_out, not_1_out, d_ff_8_q);
  or or_8 (or_8_out, and_15_out, and_16_out);
  D_Flip_Flop #(.trigger("falling")) d_ff_8 (.clk(CLK), .D(or_8_out), .Q(d_ff_8_q));  // open: Qn, preset, en, reset
  and and_17 (and_17_out, I7, LM);
  and and_18 (and_18_out, not_1_out, d_ff_9_q);
  or or_9 (or_9_out, and_17_out, and_18_out);
  D_Flip_Flop #(.trigger("falling")) d_ff_9 (.clk(CLK), .D(or_9_out), .Q(d_ff_9_q));  // open: Qn, preset, en, reset
  and and_19 (and_19_out, I6, LM);
  and and_20 (and_20_out, not_1_out, d_ff_10_q);
  or or_10 (or_10_out, and_19_out, and_20_out);
  D_Flip_Flop #(.trigger("falling")) d_ff_10 (.clk(CLK), .D(or_10_out), .Q(d_ff_10_q));  // open: Qn, preset, en, reset
  and and_21 (and_21_out, I5, LM);
  and and_22 (and_22_out, not_1_out, d_ff_11_q);
  or or_11 (or_11_out, and_21_out, and_22_out);
  D_Flip_Flop #(.trigger("falling")) d_ff_11 (.clk(CLK), .D(or_11_out), .Q(d_ff_11_q));  // open: Qn, preset, en, reset
  and and_23 (and_23_out, I4, LM);
  and and_24 (and_24_out, not_1_out, d_ff_12_q);
  or or_12 (or_12_out, and_23_out, and_24_out);
  D_Flip_Flop #(.trigger("falling")) d_ff_12 (.clk(CLK), .D(or_12_out), .Q(d_ff_12_q));  // open: Qn, preset, en, reset
  and and_25 (and_25_out, I3, LM);
  or or_13 (or_13_out, and_25_out, and_26_out);
  and and_26 (and_26_out, not_1_out, d_ff_13_q);
  D_Flip_Flop #(.trigger("falling")) d_ff_13 (.clk(CLK), .D(or_13_out), .Q(d_ff_13_q));  // open: Qn, preset, en, reset
  and and_27 (and_27_out, I2, LM);
  or or_14 (or_14_out, and_27_out, and_28_out);
  and and_28 (and_28_out, not_1_out, d_ff_14_q);
  D_Flip_Flop #(.trigger("falling")) d_ff_14 (.clk(CLK), .D(or_14_out), .Q(d_ff_14_q));  // open: Qn, preset, en, reset
  and and_29 (and_29_out, I1, LM);
  or or_15 (or_15_out, and_29_out, and_30_out);
  and and_30 (and_30_out, not_1_out, d_ff_15_q);
  D_Flip_Flop #(.trigger("falling")) d_ff_15 (.clk(CLK), .D(or_15_out), .Q(d_ff_15_q));  // open: Qn, preset, en, reset
  and and_31 (and_31_out, I0, LM);
  or or_16 (or_16_out, and_31_out, and_32_out);
  not not_1 (not_1_out, LM);
  and and_32 (and_32_out, not_1_out, d_ff_16_q);
  D_Flip_Flop #(.trigger("falling")) d_ff_16 (.clk(CLK), .D(or_16_out), .Q(d_ff_16_q));  // open: Qn, preset, en, reset
  Transistor transistor_1 (.in(d_ff_1_q), .out(OB15), .gate(nenOut));
  Transistor transistor_2 (.in(d_ff_2_q), .out(OB14), .gate(nenOut));
  Transistor transistor_3 (.in(d_ff_3_q), .out(OB13), .gate(nenOut));
  Transistor transistor_4 (.in(d_ff_4_q), .out(OB12), .gate(nenOut));
  Transistor transistor_5 (.in(d_ff_5_q), .out(OB11), .gate(nenOut));
  Transistor transistor_6 (.in(d_ff_6_q), .out(OB10), .gate(nenOut));
  Transistor transistor_7 (.in(d_ff_7_q), .out(OB9), .gate(nenOut));
  Transistor transistor_8 (.in(d_ff_8_q), .out(OB8), .gate(nenOut));
  Transistor transistor_9 (.in(d_ff_9_q), .out(OB7), .gate(nenOut));
  Transistor transistor_10 (.in(d_ff_10_q), .out(OB6), .gate(nenOut));
  Transistor transistor_11 (.in(d_ff_11_q), .out(OB5), .gate(nenOut));
  Transistor transistor_12 (.in(d_ff_12_q), .out(OB4), .gate(nenOut));
  Transistor transistor_13 (.in(d_ff_13_q), .out(OB3), .gate(nenOut));
  Transistor transistor_14 (.in(d_ff_14_q), .out(OB2), .gate(nenOut));
  Transistor transistor_15 (.in(d_ff_15_q), .out(OB1), .gate(nenOut));
  Transistor transistor_16 (.in(d_ff_16_q), .out(OB0), .gate(nenOut));
endmodule

module Row_of_transistors (
  input  nEnOut,
  input  I,
  input  I_2,
  input  I_3,
  input  I_4,
  input  I_5,
  input  I_6,
  input  I_7,
  input  I_8,
  input  I_9,
  input  I_10,
  input  I_11,
  input  I_12,
  input  I_13,
  input  I_14,
  input  I_15,
  input  I_16,
  output O,
  output O_2,
  output O_3,
  output O_4,
  output O_5,
  output O_6,
  output O_7,
  output O_8,
  output O_9,
  output O_10,
  output O_11,
  output O_12,
  output O_13,
  output O_14,
  output O_15,
  output O_16
);

  Transistor transistor_1 (.in(I), .out(O), .gate(nEnOut));
  Transistor transistor_2 (.in(I_2), .out(O_2), .gate(nEnOut));
  Transistor transistor_3 (.in(I_3), .out(O_3), .gate(nEnOut));
  Transistor transistor_4 (.in(I_4), .out(O_4), .gate(nEnOut));
  Transistor transistor_5 (.in(I_5), .out(O_5), .gate(nEnOut));
  Transistor transistor_6 (.in(I_6), .out(O_6), .gate(nEnOut));
  Transistor transistor_7 (.in(I_7), .out(O_7), .gate(nEnOut));
  Transistor transistor_8 (.in(I_8), .out(O_8), .gate(nEnOut));
  Transistor transistor_9 (.in(I_9), .out(O_9), .gate(nEnOut));
  Transistor transistor_10 (.in(I_10), .out(O_10), .gate(nEnOut));
  Transistor transistor_11 (.in(I_11), .out(O_11), .gate(nEnOut));
  Transistor transistor_12 (.in(I_12), .out(O_12), .gate(nEnOut));
  Transistor transistor_13 (.in(I_13), .out(O_13), .gate(nEnOut));
  Transistor transistor_14 (.in(I_14), .out(O_14), .gate(nEnOut));
  Transistor transistor_15 (.in(I_15), .out(O_15), .gate(nEnOut));
  Transistor transistor_16 (.in(I_16), .out(O_16), .gate(nEnOut));
endmodule

// Flag Reg
module FLAG_Reg (
  input  ZR,
  input  M,
  input  OVF,
  input  PR,
  input  CR,
  input  NU,
  input  NU_2,
  input  NU_3,
  input  ldFR,
  input  CLR,
  input  CLK,
  input  CLF,
  input  STF,
  input  ID0,
  input  ID1,
  input  ID2,
  input  ID3,
  output CR_2,
  output OUTR0,
  output OUTR1,
  output OUTR2,
  output OUTR3,
  output INR0,
  output INR1,
  output INR2,
  output INR3,
  output ZRout,
  output Mout,
  output OVFout,
  output PRout,
  output CRout,
  output NUout,
  output NUout_2,
  output NUout_3
);

  wire and_1_out, and_2_out, and_3_out, and_4_out, and_5_out, and_6_out, and_7_out, and_8_out, and_9_out,
       and_10_out, and_11_out, and_12_out, and_13_out, and_14_out, and_15_out, and_16_out, CL_2_out,
       CL_3_out, CL_4_out, CL_5_out, CL_6_out, CL_7_out, CL_8_out, CL_out, demultiplexer_1_out0,
       demultiplexer_1_out1, demultiplexer_1_out2, demultiplexer_1_out3, demultiplexer_1_out4,
       demultiplexer_1_out5, demultiplexer_1_out6, demultiplexer_1_out7, demultiplexer_1_out8,
       demultiplexer_1_out9, demultiplexer_1_out10, demultiplexer_1_out11, demultiplexer_1_out12,
       demultiplexer_1_out13, demultiplexer_1_out14, demultiplexer_1_out15, not_1_out, or_1_out, or_2_out,
       or_3_out, or_4_out, or_5_out, or_6_out, or_7_out, or_8_out, or_9_out, or_10_out, or_11_out, or_12_out,
       or_13_out, or_14_out, or_15_out, or_16_out, or_17_out, ST_2_out, ST_3_out, ST_4_out, ST_5_out,
       ST_6_out, ST_7_out, ST_8_out, ST_out;

  or or_1 (or_1_out, CLF, STF);
  Demultiplexer #(.select(4)) demultiplexer_1 (
    .out0(demultiplexer_1_out0), .out1(demultiplexer_1_out1), .out2(demultiplexer_1_out2),
    .out3(demultiplexer_1_out3), .out4(demultiplexer_1_out4), .out5(demultiplexer_1_out5),
    .out6(demultiplexer_1_out6), .out7(demultiplexer_1_out7), .out8(demultiplexer_1_out8),
    .out9(demultiplexer_1_out9), .out10(demultiplexer_1_out10), .out11(demultiplexer_1_out11),
    .out12(demultiplexer_1_out12), .out13(demultiplexer_1_out13), .out14(demultiplexer_1_out14),
    .out15(demultiplexer_1_out15), .in(or_1_out), .sel({ID3, ID2, ID1, ID0}));  // open: en
  and and_1 (and_1_out, ZR, ldFR);
  or or_2 (or_2_out, and_1_out, and_2_out);
  and and_2 (and_2_out, not_1_out, ZRout);
  D_Flip_Flop d_ff_1 (.clk(CLK), .D(or_2_out), .Q(ZRout), .preset(CL_out), .reset(or_3_out));  // open: Qn, en
  or or_3 (or_3_out, CLR, ST_out);
  and ST (ST_out, demultiplexer_1_out0, CLF);
  and CL (CL_out, demultiplexer_1_out0, STF);
  and and_3 (and_3_out, M, ldFR);
  or or_4 (or_4_out, and_3_out, and_4_out);
  and and_4 (and_4_out, not_1_out, Mout);
  D_Flip_Flop d_ff_2 (.clk(CLK), .D(or_4_out), .Q(Mout), .preset(CL_2_out), .reset(or_5_out));  // open: Qn, en
  or or_5 (or_5_out, CLR, ST_2_out);
  and CL_2 (CL_2_out, demultiplexer_1_out1, STF);
  and ST_2 (ST_2_out, demultiplexer_1_out1, CLF);
  and and_5 (and_5_out, OVF, ldFR);
  or or_6 (or_6_out, and_5_out, and_6_out);
  and CL_3 (CL_3_out, demultiplexer_1_out2, STF);
  and and_6 (and_6_out, not_1_out, OVFout);
  D_Flip_Flop d_ff_3 (.clk(CLK), .D(or_6_out), .Q(OVFout), .preset(CL_3_out), .reset(or_7_out));  // open: Qn, en
  or or_7 (or_7_out, CLR, ST_3_out);
  and ST_3 (ST_3_out, demultiplexer_1_out2, CLF);
  and and_7 (and_7_out, PR, ldFR);
  or or_8 (or_8_out, and_7_out, and_8_out);
  and CL_4 (CL_4_out, demultiplexer_1_out3, STF);
  and and_8 (and_8_out, not_1_out, PRout);
  D_Flip_Flop d_ff_4 (.clk(CLK), .D(or_8_out), .Q(PRout), .preset(CL_4_out), .reset(or_9_out));  // open: Qn, en
  or or_9 (or_9_out, CLR, ST_4_out);
  and ST_4 (ST_4_out, demultiplexer_1_out3, CLF);
  and and_9 (and_9_out, CR, ldFR);
  or or_10 (or_10_out, and_9_out, and_10_out);
  and CL_5 (CL_5_out, demultiplexer_1_out4, STF);
  and and_10 (and_10_out, not_1_out, CR_2);
  D_Flip_Flop d_ff_5 (.clk(CLK), .D(or_10_out), .Q(CR_2), .preset(CL_5_out), .reset(or_11_out));  // open: Qn, en
  or or_11 (or_11_out, CLR, ST_5_out);
  and ST_5 (ST_5_out, demultiplexer_1_out4, CLF);
  and and_11 (and_11_out, NU, ldFR);
  or or_12 (or_12_out, and_11_out, and_12_out);
  and and_12 (and_12_out, not_1_out, NUout);
  D_Flip_Flop d_ff_6 (.clk(CLK), .D(or_12_out), .Q(NUout), .preset(CL_6_out), .reset(or_13_out));  // open: Qn, en
  or or_13 (or_13_out, CLR, ST_6_out);
  and ST_6 (ST_6_out, demultiplexer_1_out5, CLF);
  and CL_6 (CL_6_out, demultiplexer_1_out5, STF);
  and and_13 (and_13_out, NU_2, ldFR);
  and and_14 (and_14_out, not_1_out, NUout_2);
  or or_14 (or_14_out, and_13_out, and_14_out);
  or or_15 (or_15_out, CLR, ST_7_out);
  and CL_7 (CL_7_out, demultiplexer_1_out6, STF);
  D_Flip_Flop d_ff_7 (.clk(CLK), .D(or_14_out), .Q(NUout_2), .preset(CL_7_out), .reset(or_15_out));  // open: Qn, en
  and ST_7 (ST_7_out, demultiplexer_1_out6, CLF);
  and and_15 (and_15_out, NU_3, ldFR);
  or or_16 (or_16_out, and_15_out, and_16_out);
  and CL_8 (CL_8_out, demultiplexer_1_out7, STF);
  not not_1 (not_1_out, ldFR);
  and and_16 (and_16_out, not_1_out, NUout_3);
  D_Flip_Flop d_ff_8 (.clk(CLK), .D(or_16_out), .Q(NUout_3), .preset(CL_8_out), .reset(or_17_out));  // open: Qn, en
  or or_17 (or_17_out, CLR, ST_8_out);
  and ST_8 (ST_8_out, demultiplexer_1_out7, CLF);
  not not_2 (OUTR0, demultiplexer_1_out8);
  not not_3 (OUTR1, demultiplexer_1_out9);
  not not_4 (OUTR2, demultiplexer_1_out10);
  not not_5 (OUTR3, demultiplexer_1_out11);
  not not_6 (INR0, demultiplexer_1_out12);
  not not_7 (INR1, demultiplexer_1_out13);
  not not_8 (INR2, demultiplexer_1_out14);
  not not_9 (INR3, demultiplexer_1_out15);

  assign CRout = CR_2;
endmodule

module Zero_Reg (
  input  nZerRegEn,
  output out_2,
  output out_3,
  output out_4,
  output out_5,
  output out_6,
  output out_7,
  output out_8,
  output out_9,
  output out_10,
  output out_11,
  output out_12,
  output out_13,
  output out_14,
  output out_15,
  output out_16,
  output out_17
);

  Transistor transistor_1 (.in(1'b0), .out(out_2), .gate(nZerRegEn));
  Transistor transistor_2 (.in(1'b0), .out(out_3), .gate(nZerRegEn));
  Transistor transistor_3 (.in(1'b0), .out(out_4), .gate(nZerRegEn));
  Transistor transistor_4 (.in(1'b0), .out(out_5), .gate(nZerRegEn));
  Transistor transistor_5 (.in(1'b0), .out(out_6), .gate(nZerRegEn));
  Transistor transistor_6 (.in(1'b0), .out(out_7), .gate(nZerRegEn));
  Transistor transistor_7 (.in(1'b0), .out(out_8), .gate(nZerRegEn));
  Transistor transistor_8 (.in(1'b0), .out(out_9), .gate(nZerRegEn));
  Transistor transistor_9 (.in(1'b0), .out(out_10), .gate(nZerRegEn));
  Transistor transistor_10 (.in(1'b0), .out(out_11), .gate(nZerRegEn));
  Transistor transistor_11 (.in(1'b0), .out(out_12), .gate(nZerRegEn));
  Transistor transistor_12 (.in(1'b0), .out(out_13), .gate(nZerRegEn));
  Transistor transistor_13 (.in(1'b0), .out(out_14), .gate(nZerRegEn));
  Transistor transistor_14 (.in(1'b0), .out(out_15), .gate(nZerRegEn));
  Transistor transistor_15 (.in(1'b0), .out(out_16), .gate(nZerRegEn));
  Transistor transistor_16 (.in(1'b0), .out(out_17), .gate(nZerRegEn));
endmodule

module MANIAC_testing (
  input  in_1,
  input  in_2,
  input  in_3,
  input  in_4,
  input  in_5
);

  wire and_1_out, and_2_out, not_1_out;

  MANIAC maniac_1 ();  // open: Examine, Examine_Next, Deposit, Deposit_Next, Edit, Single_Step, Run___Stop, CLR_HLT, HLT, out_114, out_115, out_116, out_117, A0, A1, A2, A3, A4, A5, A6, A7, A8, A9, A10, A11, A12, A13, A14, A15, D0, D1, D2, D3, D4, D5, D6, D7, D8, D9, D10, D11, D12, D13, D14, D15, Bus_0, Bus_1, Bus_2, Bus_3, Bus_4, Bus_5, Bus_6, Bus_7, Bus_8, Bus_9, Bus_10, Bus_11, Bus_12, Bus_13, Bus_14, Bus_15, Adr_0, Adr_1, Adr_2, Adr_3, Adr_4, Adr_5, Adr_6, Adr_7, Adr_8, Adr_9, Adr_10, Adr_11, Adr_12, Adr_13, Adr_14, Adr_15, MANIAC_OUT_0, MANIAC_OUT_1, MANIAC_OUT_2, MANIAC_OUT_3, MANIAC_OUT_4, MANIAC_OUT_5, MANIAC_OUT_6, MANIAC_OUT_7, MANIAC_OUT_8, MANIAC_OUT_9, MANIAC_OUT_10, MANIAC_OUT_11, MANIAC_OUT_12, MANIAC_OUT_13, MANIAC_OUT_14, MANIAC_OUT_15, MANIAC_OUTPUT0___data_recived, MANIAC_OUT_0_2, MANIAC_OUT_1_2, MANIAC_OUT_2_2, MANIAC_OUT_3_2, MANIAC_OUT_4_2, MANIAC_OUT_5_2, MANIAC_OUT_6_2, MANIAC_OUT_7_2, MANIAC_OUT_8_2, MANIAC_OUT_9_2, MANIAC_OUT_10_2, MANIAC_OUT_11_2, MANIAC_OUT_12_2, MANIAC_OUT_13_2, MANIAC_OUT_14_2, MANIAC_OUT_15_2, MANIAC_OUTPUT1___data_recived, MANIAC_OUT_0_3, MANIAC_OUT_1_3, MANIAC_OUT_2_3, MANIAC_OUT_3_3, MANIAC_OUT_4_3, MANIAC_OUT_5_3, MANIAC_OUT_6_3, MANIAC_OUT_7_3, MANIAC_OUT_8_3, MANIAC_OUT_9_3, MANIAC_OUT_10_3, MANIAC_OUT_11_3, MANIAC_OUT_12_3, MANIAC_OUT_13_3, MANIAC_OUT_14_3, MANIAC_OUT_15_3, MANIAC_OUTPUT2___data_recived, MANIAC_OUT_0_4, MANIAC_OUT_1_4, MANIAC_OUT_2_4, MANIAC_OUT_3_4, MANIAC_OUT_4_4, MANIAC_OUT_5_4, MANIAC_OUT_6_4, MANIAC_OUT_7_4, MANIAC_OUT_8_4, MANIAC_OUT_9_4, MANIAC_OUT_10_4, MANIAC_OUT_11_4, MANIAC_OUT_12_4, MANIAC_OUT_13_4, MANIAC_OUT_14_4, MANIAC_OUT_15_4, MANIAC_OUTPUT3___data_recived, MANIAC_IN_0, MANIAC_IN_1, MANIAC_IN_2, MANIAC_IN_3, MANIAC_IN_4, MANIAC_IN_5, MANIAC_IN_6, MANIAC_IN_7, MANIAC_IN_8, MANIAC_IN_9, MANIAC_IN_10, MANIAC_IN_11, MANIAC_IN_12, MANIAC_IN_13, MANIAC_IN_14, MANIAC_IN_15, MANIAC_INPUT0___data_ready, INPUT_0_ready_INDICATOR, MANIAC_IN_0_2, MANIAC_IN_1_2, MANIAC_IN_2_2, MANIAC_IN_3_2, MANIAC_IN_4_2, MANIAC_IN_5_2, MANIAC_IN_6_2, MANIAC_IN_7_2, MANIAC_IN_8_2, MANIAC_IN_9_2, MANIAC_IN_10_2, MANIAC_IN_11_2, MANIAC_IN_12_2, MANIAC_IN_13_2, MANIAC_IN_14_2, MANIAC_IN_15_2, MANIAC_INPUT1___data_ready, INPUT_1_ready_INDICATOR, MANIAC_IN_0_3, MANIAC_IN_1_3, MANIAC_IN_2_3, MANIAC_IN_3_3, MANIAC_IN_4_3, MANIAC_IN_5_3, MANIAC_IN_6_3, MANIAC_IN_7_3, MANIAC_IN_8_3, MANIAC_IN_9_3, MANIAC_IN_10_3, MANIAC_IN_11_3, MANIAC_IN_12_3, MANIAC_IN_13_3, MANIAC_IN_14_3, MANIAC_IN_15_3, MANIAC_INPUT2___data_ready, INPUT_2_ready_INDICATOR, MANIAC_IN_0_4, MANIAC_IN_1_4, MANIAC_IN_2_4, MANIAC_IN_3_4, MANIAC_IN_4_4, MANIAC_IN_5_4, MANIAC_IN_6_4, MANIAC_IN_7_4, MANIAC_IN_8_4, MANIAC_IN_9_4, MANIAC_IN_10_4, MANIAC_IN_11_4, MANIAC_IN_12_4, MANIAC_IN_13_4, MANIAC_IN_14_4, MANIAC_IN_15_4, MANIAC_INPUT3___data_ready, INPUT_3_ready_INDICATOR
  not not_1 (not_1_out, in_2);
  and and_1 (and_1_out, in_1, in_2);
  and and_2 (and_2_out, in_1, not_1_out);
  Demultiplexer #(.select(3)) demultiplexer_1 (
    .in(and_1_out), .sel({in_3, in_4, in_5}));  // open: out0, out1, out2, out3, out4, out5, out6, out7, en
  Demultiplexer #(.select(3)) demultiplexer_2 (
    .in(and_2_out), .sel({in_3, in_4, in_5}));  // open: out0, out1, out2, out3, out4, out5, out6, out7, en
endmodule

module Interrupt_Pin (
  input  nsetINT,
  input  nclrINT,
  output Out
);

  wire not_1_out, not_2_out;

  D_Flip_Flop d_ff_1 (.Q(Out), .preset(not_1_out), .reset(not_2_out));  // open: clk, D, Qn, en
  not not_1 (not_1_out, nsetINT);
  not not_2 (not_2_out, nclrINT);
endmodule

// Adder
module PC_adder (
  input  A15,
  input  A14,
  input  A13,
  input  A12,
  input  A11,
  input  A10,
  input  A9,
  input  A8,
  input  A7,
  input  A6,
  input  A5,
  input  A4,
  input  A3,
  input  A2,
  input  A1,
  input  A0,
  input  B0,
  input  B1,
  input  B2,
  input  B3,
  input  B4,
  input  B5,
  input  B6,
  input  B7,
  input  B8,
  input  B9,
  input  B10,
  input  B11,
  input  B12,
  input  B13,
  input  B14,
  input  B15,
  output O15,
  output O14,
  output O13,
  output O12,
  output O11,
  output O10,
  output O9,
  output O8,
  output O7,
  output O6,
  output O5,
  output O4,
  output O3,
  output O2,
  output O1,
  output O0
);

  wire full_adder_1_c_2, full_adder_2_c_2, full_adder_4_c_2, full_adder_5_c_2, full_adder_6_c_2,
       full_adder_7_c_2, full_adder_8_c_2, full_adder_9_c_2, full_adder_10_c_2, full_adder_11_c_2,
       full_adder_12_c_2, full_adder_13_c_2, full_adder_14_c_2, full_adder_15_c_2, full_adder_16_c_2;

  Full_Adder full_adder_1 (.A(full_adder_11_c_2), .B(B13), .C(A13), .O(O13), .C_2(full_adder_1_c_2));
  Full_Adder full_adder_2 (.A(full_adder_1_c_2), .B(B14), .C(A14), .O(O14), .C_2(full_adder_2_c_2));
  Full_Adder full_adder_3 (.A(full_adder_2_c_2), .B(B15), .C(A15), .O(O15));  // open: C_2
  Full_Adder full_adder_4 (.A(full_adder_16_c_2), .B(B5), .C(A5), .O(O5), .C_2(full_adder_4_c_2));
  Full_Adder full_adder_5 (.A(full_adder_4_c_2), .B(B6), .C(A6), .O(O6), .C_2(full_adder_5_c_2));
  Full_Adder full_adder_6 (.A(full_adder_5_c_2), .B(B7), .C(A7), .O(O7), .C_2(full_adder_6_c_2));
  Full_Adder full_adder_7 (.A(full_adder_6_c_2), .B(B8), .C(A8), .O(O8), .C_2(full_adder_7_c_2));
  Full_Adder full_adder_8 (.A(full_adder_7_c_2), .B(B9), .C(A9), .O(O9), .C_2(full_adder_8_c_2));
  Full_Adder full_adder_9 (.A(full_adder_8_c_2), .B(B10), .C(A10), .O(O10), .C_2(full_adder_9_c_2));
  Full_Adder full_adder_10 (.A(full_adder_9_c_2), .B(B11), .C(A11), .O(O11), .C_2(full_adder_10_c_2));
  Full_Adder full_adder_11 (.A(full_adder_10_c_2), .B(B12), .C(A12), .O(O12), .C_2(full_adder_11_c_2));
  Full_Adder full_adder_12 (.A(1'b0), .B(B0), .C(A0), .O(O0), .C_2(full_adder_12_c_2));
  Full_Adder full_adder_13 (.A(full_adder_12_c_2), .B(B1), .C(A1), .O(O1), .C_2(full_adder_13_c_2));
  Full_Adder full_adder_14 (.A(full_adder_13_c_2), .B(B2), .C(A2), .O(O2), .C_2(full_adder_14_c_2));
  Full_Adder full_adder_15 (.A(full_adder_14_c_2), .B(B3), .C(A3), .O(O3), .C_2(full_adder_15_c_2));
  Full_Adder full_adder_16 (.A(full_adder_15_c_2), .B(B4), .C(A4), .O(O4), .C_2(full_adder_16_c_2));
endmodule

module JPR (
  input  I15,
  input  I14,
  input  I13,
  input  I12,
  input  I11,
  input  I10,
  input  I9,
  input  I8,
  input  I7,
  input  I6,
  input  I5,
  input  I4,
  input  I3,
  input  I2,
  input  I1,
  input  I0,
  input  LM,
  input  nCLR,
  input  CLK,
  input  nRegEn,
  output O15,
  output O14,
  output O13,
  output O12,
  output O11,
  output O10,
  output O9,
  output O8,
  output O7,
  output O6,
  output O5,
  output O4,
  output O3,
  output O2,
  output O1,
  output O0
);

  wire and_1_out, and_2_out, and_3_out, and_4_out, and_5_out, and_6_out, and_7_out, and_8_out, and_9_out,
       and_10_out, and_11_out, and_12_out, and_13_out, and_14_out, and_15_out, and_16_out, and_17_out,
       and_18_out, and_19_out, and_20_out, and_21_out, and_22_out, and_23_out, and_24_out, and_25_out,
       and_26_out, and_27_out, and_28_out, and_29_out, and_30_out, and_31_out, and_32_out, d_ff_1_q,
       d_ff_2_q, d_ff_3_q, d_ff_4_q, d_ff_5_q, d_ff_6_q, d_ff_7_q, d_ff_8_q, d_ff_9_q, d_ff_10_q, d_ff_11_q,
       d_ff_12_q, d_ff_13_q, d_ff_14_q, d_ff_15_q, d_ff_16_q, not_1_out, not_2_out, or_1_out, or_2_out,
       or_3_out, or_4_out, or_5_out, or_6_out, or_7_out, or_8_out, or_9_out, or_10_out, or_11_out, or_12_out,
       or_13_out, or_14_out, or_15_out, or_16_out;

  Full_Adder full_adder_1 ();  // open: A, B, C, O, C_2
  and and_1 (and_1_out, I15, LM);
  or or_1 (or_1_out, and_1_out, and_2_out);
  and and_2 (and_2_out, not_1_out, d_ff_1_q);
  D_Flip_Flop d_ff_1 (.clk(CLK), .D(or_1_out), .Q(d_ff_1_q), .reset(not_2_out));  // open: Qn, preset, en
  Transistor transistor_1 (.in(d_ff_1_q), .out(O15), .gate(nRegEn));
  and and_3 (and_3_out, I14, LM);
  or or_2 (or_2_out, and_3_out, and_4_out);
  and and_4 (and_4_out, not_1_out, d_ff_2_q);
  D_Flip_Flop d_ff_2 (.clk(CLK), .D(or_2_out), .Q(d_ff_2_q), .reset(not_2_out));  // open: Qn, preset, en
  Transistor transistor_2 (.in(d_ff_2_q), .out(O14), .gate(nRegEn));
  and and_5 (and_5_out, I13, LM);
  or or_3 (or_3_out, and_5_out, and_6_out);
  and and_6 (and_6_out, not_1_out, d_ff_3_q);
  D_Flip_Flop d_ff_3 (.clk(CLK), .D(or_3_out), .Q(d_ff_3_q), .reset(not_2_out));  // open: Qn, preset, en
  Transistor transistor_3 (.in(d_ff_3_q), .out(O13), .gate(nRegEn));
  and and_7 (and_7_out, I12, LM);
  or or_4 (or_4_out, and_7_out, and_8_out);
  and and_8 (and_8_out, not_1_out, d_ff_4_q);
  D_Flip_Flop d_ff_4 (.clk(CLK), .D(or_4_out), .Q(d_ff_4_q), .reset(not_2_out));  // open: Qn, preset, en
  Transistor transistor_4 (.in(d_ff_4_q), .out(O12), .gate(nRegEn));
  and and_9 (and_9_out, I11, LM);
  or or_5 (or_5_out, and_9_out, and_10_out);
  and and_10 (and_10_out, not_1_out, d_ff_5_q);
  D_Flip_Flop d_ff_5 (.clk(CLK), .D(or_5_out), .Q(d_ff_5_q), .reset(not_2_out));  // open: Qn, preset, en
  and and_11 (and_11_out, I10, LM);
  Transistor transistor_5 (.in(d_ff_5_q), .out(O11), .gate(nRegEn));
  or or_6 (or_6_out, and_11_out, and_12_out);
  and and_12 (and_12_out, not_1_out, d_ff_6_q);
  D_Flip_Flop d_ff_6 (.clk(CLK), .D(or_6_out), .Q(d_ff_6_q), .reset(not_2_out));  // open: Qn, preset, en
  Transistor transistor_6 (.in(d_ff_6_q), .out(O10), .gate(nRegEn));
  and and_13 (and_13_out, I9, LM);
  or or_7 (or_7_out, and_13_out, and_14_out);
  and and_14 (and_14_out, not_1_out, d_ff_7_q);
  D_Flip_Flop d_ff_7 (.clk(CLK), .D(or_7_out), .Q(d_ff_7_q), .reset(not_2_out));  // open: Qn, preset, en
  and and_15 (and_15_out, I8, LM);
  Transistor transistor_7 (.in(d_ff_7_q), .out(O9), .gate(nRegEn));
  or or_8 (or_8_out, and_15_out, and_16_out);
  and and_16 (and_16_out, not_1_out, d_ff_8_q);
  D_Flip_Flop d_ff_8 (.clk(CLK), .D(or_8_out), .Q(d_ff_8_q), .reset(not_2_out));  // open: Qn, preset, en
  and and_17 (and_17_out, I7, LM);
  Transistor transistor_8 (.in(d_ff_8_q), .out(O8), .gate(nRegEn));
  or or_9 (or_9_out, and_17_out, and_18_out);
  and and_18 (and_18_out, not_1_out, d_ff_9_q);
  D_Flip_Flop d_ff_9 (.clk(CLK), .D(or_9_out), .Q(d_ff_9_q), .reset(not_2_out));  // open: Qn, preset, en
  Transistor transistor_9 (.in(d_ff_9_q), .out(O7), .gate(nRegEn));
  and and_19 (and_19_out, I6, LM);
  and and_20 (and_20_out, not_1_out, d_ff_10_q);
  or or_10 (or_10_out, and_19_out, and_20_out);
  D_Flip_Flop d_ff_10 (.clk(CLK), .D(or_10_out), .Q(d_ff_10_q), .reset(not_2_out));  // open: Qn, preset, en
  Transistor transistor_10 (.in(d_ff_10_q), .out(O6), .gate(nRegEn));
  and and_21 (and_21_out, I5, LM);
  or or_11 (or_11_out, and_21_out, and_22_out);
  and and_22 (and_22_out, not_1_out, d_ff_11_q);
  D_Flip_Flop d_ff_11 (.clk(CLK), .D(or_11_out), .Q(d_ff_11_q), .reset(not_2_out));  // open: Qn, preset, en
  Transistor transistor_11 (.in(d_ff_11_q), .out(O5), .gate(nRegEn));
  and and_23 (and_23_out, I4, LM);
  and and_24 (and_24_out, not_1_out, d_ff_12_q);
  or or_12 (or_12_out, and_23_out, and_24_out);
  D_Flip_Flop d_ff_12 (.clk(CLK), .D(or_12_out), .Q(d_ff_12_q), .reset(not_2_out));  // open: Qn, preset, en
  Transistor transistor_12 (.in(d_ff_12_q), .out(O4), .gate(nRegEn));
  and and_25 (and_25_out, I3, LM);
  and and_26 (and_26_out, not_1_out, d_ff_13_q);
  or or_13 (or_13_out, and_25_out, and_26_out);
  D_Flip_Flop d_ff_13 (.clk(CLK), .D(or_13_out), .Q(d_ff_13_q), .reset(not_2_out));  // open: Qn, preset, en
  Transistor transistor_13 (.in(d_ff_13_q), .out(O3), .gate(nRegEn));
  and and_27 (and_27_out, I2, LM);
  and and_28 (and_28_out, not_1_out, d_ff_14_q);
  or or_14 (or_14_out, and_27_out, and_28_out);
  D_Flip_Flop d_ff_14 (.clk(CLK), .D(or_14_out), .Q(d_ff_14_q), .reset(not_2_out));  // open: Qn, preset, en
  Transistor transistor_14 (.in(d_ff_14_q), .out(O2), .gate(nRegEn));
  and and_29 (and_29_out, I1, LM);
  and and_30 (and_30_out, not_1_out, d_ff_15_q);
  or or_15 (or_15_out, and_29_out, and_30_out);
  D_Flip_Flop d_ff_15 (.clk(CLK), .D(or_15_out), .Q(d_ff_15_q), .reset(not_2_out));  // open: Qn, preset, en
  Transistor transistor_15 (.in(d_ff_15_q), .out(O1), .gate(nRegEn));
  and and_31 (and_31_out, I0, LM);
  not not_1 (not_1_out, LM);
  and and_32 (and_32_out, not_1_out, d_ff_16_q);
  or or_16 (or_16_out, and_31_out, and_32_out);
  D_Flip_Flop d_ff_16 (.clk(CLK), .D(or_16_out), .Q(d_ff_16_q), .reset(not_2_out));  // open: Qn, preset, en
  not not_2 (not_2_out, nCLR);
  Transistor transistor_16 (.in(d_ff_16_q), .out(O0), .gate(nRegEn));
endmodule

module Sync_Buffer (
  input  CLK,
  input  IN,
  input  in_3,
  input  in_4,
  input  in_5,
  input  in_6,
  input  in_7,
  input  in_8,
  input  in_9,
  input  in_10,
  input  in_11,
  input  in_12,
  input  in_13,
  input  in_14,
  input  in_15,
  input  in_16,
  input  in_17,
  output OUT,
  output out_19,
  output out_20,
  output out_21,
  output out_22,
  output out_23,
  output out_24,
  output out_25,
  output out_26,
  output out_27,
  output out_28,
  output out_29,
  output out_30,
  output out_31,
  output out_32,
  output out_33
);

  D_Flip_Flop d_ff_1 (.clk(CLK), .D(IN), .Q(OUT));  // open: Qn, preset, en, reset
  D_Flip_Flop d_ff_2 (.clk(CLK), .D(in_3), .Q(out_19));  // open: Qn, preset, en, reset
  D_Flip_Flop d_ff_3 (.clk(CLK), .D(in_4), .Q(out_20));  // open: Qn, preset, en, reset
  D_Flip_Flop d_ff_4 (.clk(CLK), .D(in_5), .Q(out_21));  // open: Qn, preset, en, reset
  D_Flip_Flop d_ff_5 (.clk(CLK), .D(in_6), .Q(out_22));  // open: Qn, preset, en, reset
  D_Flip_Flop d_ff_6 (.clk(CLK), .D(in_7), .Q(out_23));  // open: Qn, preset, en, reset
  D_Flip_Flop d_ff_7 (.clk(CLK), .D(in_8), .Q(out_24));  // open: Qn, preset, en, reset
  D_Flip_Flop d_ff_8 (.clk(CLK), .D(in_9), .Q(out_25));  // open: Qn, preset, en, reset
  D_Flip_Flop d_ff_9 (.clk(CLK), .D(in_10), .Q(out_26));  // open: Qn, preset, en, reset
  D_Flip_Flop d_ff_10 (.clk(CLK), .D(in_11), .Q(out_27));  // open: Qn, preset, en, reset
  D_Flip_Flop d_ff_11 (.clk(CLK), .D(in_12), .Q(out_28));  // open: Qn, preset, en, reset
  D_Flip_Flop d_ff_12 (.clk(CLK), .D(in_13), .Q(out_29));  // open: Qn, preset, en, reset
  D_Flip_Flop d_ff_13 (.clk(CLK), .D(in_14), .Q(out_30));  // open: Qn, preset, en, reset
  D_Flip_Flop d_ff_14 (.clk(CLK), .D(in_15), .Q(out_31));  // open: Qn, preset, en, reset
  D_Flip_Flop d_ff_15 (.clk(CLK), .D(in_16), .Q(out_32));  // open: Qn, preset, en, reset
  D_Flip_Flop d_ff_16 (.clk(CLK), .D(in_17), .Q(out_33));  // open: Qn, preset, en, reset
endmodule

module Buff_short_zero_protection (
  input  In,
  output Out
);

  wire buffer_1_out, buffer_2_out, buffer_3_out;

  buf buffer_1 (buffer_1_out, buffer_3_out);
  buf buffer_2 (buffer_2_out, In);
  buf buffer_3 (buffer_3_out, buffer_2_out);
  or or_1 (Out, In, buffer_1_out);
endmodule

module Buff_short_one_protection (
  input  I,
  output O
);

  wire buffer_1_out, buffer_2_out, buffer_3_out;

  buf buffer_1 (buffer_1_out, buffer_2_out);
  buf buffer_2 (buffer_2_out, I);
  buf buffer_3 (buffer_3_out, buffer_1_out);
  and and_1 (O, buffer_3_out, I);
endmodule

module uprgraded_buffer (
  input  In,
  output Out
);

  wire and_1_out, buffer_1_out, buffer_2_out, buffer_3_out, buffer_4_out, buffer_5_out, buffer_6_out,
       buffer_7_out;

  buf buffer_1 (buffer_1_out, buffer_2_out);
  buf buffer_2 (buffer_2_out, In);
  and and_1 (and_1_out, buffer_1_out, In);
  buf buffer_3 (buffer_3_out, and_1_out);
  buf buffer_4 (buffer_4_out, buffer_3_out);
  buf buffer_5 (buffer_5_out, buffer_6_out);
  buf buffer_6 (buffer_6_out, buffer_7_out);
  buf buffer_7 (buffer_7_out, buffer_4_out);
  or or_1 (Out, and_1_out, buffer_5_out);
endmodule

module HUGE_Delay (
  input  In,
  output Out
);

  wire uprgraded_buffer_1_out, uprgraded_buffer_2_out, uprgraded_buffer_3_out, uprgraded_buffer_4_out,
       uprgraded_buffer_5_out, uprgraded_buffer_6_out, uprgraded_buffer_7_out;

  uprgraded_buffer uprgraded_buffer_1 (.In(uprgraded_buffer_2_out), .Out(uprgraded_buffer_1_out));
  uprgraded_buffer uprgraded_buffer_2 (.In(In), .Out(uprgraded_buffer_2_out));
  uprgraded_buffer uprgraded_buffer_3 (.In(uprgraded_buffer_4_out), .Out(uprgraded_buffer_3_out));
  uprgraded_buffer uprgraded_buffer_4 (.In(uprgraded_buffer_1_out), .Out(uprgraded_buffer_4_out));
  uprgraded_buffer uprgraded_buffer_5 (.In(uprgraded_buffer_3_out), .Out(uprgraded_buffer_5_out));
  uprgraded_buffer uprgraded_buffer_6 (.In(uprgraded_buffer_5_out), .Out(uprgraded_buffer_6_out));
  uprgraded_buffer uprgraded_buffer_7 (.In(uprgraded_buffer_6_out), .Out(uprgraded_buffer_7_out));
  uprgraded_buffer uprgraded_buffer_8 (.In(uprgraded_buffer_7_out), .Out(Out));
endmodule
